// Logisim project int.circ as structural Verilog: 7 circuits, main circuit 单周期单级中断
// 单周期硬布线控制器
module \硬布线控制器  (
  input  [5:0] OP,
  input  [5:0] Func,
  output [3:0] ALU_OP,
  output MemToReg,
  output MemWrite,
  output ALU_SRC,
  output RegWrite,
  output SysCALL,
  output SignedExt,
  output RegDst,
  output Beq,
  output Bne,
  output JR,
  output JMP,
  output JAL,
  output SLLV,
  output LB,
  output BLTZ
);

  \运算控制器  \u_运算控制器_1  (
    .OP0(OP[0]), .OP1(OP[1]), .OP2(OP[2]), .OP3(OP[3]), .OP4(OP[4]), .OP5(OP[5]), .F0(Func[0]), .F1(Func[1]),
    .F2(Func[2]), .F3(Func[3]), .F4(Func[4]), .F5(Func[5]), .S0(ALU_OP[0]), .S1(ALU_OP[1]), .S2(ALU_OP[2]),
    .S3(ALU_OP[3]));
  \控制信号生成  \u_控制信号生成_1  (
    .OP0(OP[0]), .OP1(OP[1]), .OP2(OP[2]), .OP3(OP[3]), .OP4(OP[4]), .OP5(OP[5]), .F0(Func[0]), .F1(Func[1]),
    .F2(Func[2]), .F3(Func[3]), .F4(Func[4]), .F5(Func[5]), .MemToReg(MemToReg), .MemWrite(MemWrite),
    .ALU_SRC(ALU_SRC), .RegWrite(RegWrite), .SysCALL(SysCALL), .SignedExt(SignedExt), .RegDst(RegDst),
    .BEQ(Beq), .BNE(Bne), .JR(JR), .JMP(JMP), .JAL(JAL));
  \_4控制信号生成  \u_4控制信号生成_1  (
    .OP0(OP[0]), .OP1(OP[1]), .OP2(OP[2]), .OP3(OP[3]), .OP4(OP[4]), .OP5(OP[5]), .F0(Func[0]), .F1(Func[1]),
    .F2(Func[2]), .F3(Func[3]), .F4(Func[4]), .F5(Func[5]), .SLLV(SLLV), .LB(LB), .BLTZ(BLTZ));

  // Other names for the same wires on the sheet: OP_CODE[5:0] = OP

  // Notes on the sheet:
  //   运算器控制器，根据指令生成运算器功能选择信号
  //   控制信号生成，产生数据通路需要的其他控制信号
endmodule

// 运算器控制器
module \运算控制器  (
  input  OP0,
  input  OP1,
  input  OP2,
  input  OP3,
  input  OP4,
  input  OP5,
  input  F0,
  input  F1,
  input  F2,
  input  F3,
  input  F4,
  input  F5,
  output S0,
  output S1,
  output S2,
  output S3
);

  wire and_1_out, and_2_out, and_3_out, and_4_out, and_5_out, and_6_out, and_7_out, and_8_out, and_9_out,
       and_10_out, and_11_out, and_12_out, and_13_out, and_14_out, and_15_out, and_16_out, and_17_out,
       and_18_out, and_19_out, and_20_out, and_21_out, and_22_out, and_23_out, and_24_out, and_25_out,
       and_26_out, and_27_out, and_28_out, and_29_out, and_30_out, and_31_out, and_32_out, and_33_out,
       and_34_out, and_35_out, and_36_out, and_37_out, and_38_out, and_39_out, and_40_out, and_41_out,
       not_1_out, not_2_out, not_3_out, not_4_out, not_5_out, not_6_out, not_7_out, not_8_out, not_9_out,
       not_10_out, not_11_out, not_12_out, not_13_out, not_14_out, not_15_out, not_16_out, not_17_out,
       not_18_out, not_19_out, not_20_out, not_21_out, not_22_out, not_23_out, not_24_out, not_25_out,
       not_26_out, not_27_out, not_28_out, not_29_out, not_30_out, not_31_out, not_32_out, not_33_out,
       not_34_out, not_35_out, not_36_out, not_37_out, not_38_out, not_39_out, not_40_out, not_41_out,
       not_42_out, not_43_out, not_44_out, not_45_out, not_46_out, not_47_out, not_48_out, not_49_out,
       not_50_out, not_51_out, not_52_out, not_53_out, not_54_out, not_55_out, not_56_out, not_57_out,
       not_58_out, not_59_out, not_60_out, not_61_out, not_62_out, not_63_out, not_64_out, not_65_out,
       not_66_out, not_67_out, not_68_out, not_69_out, not_70_out, not_71_out, not_72_out, not_73_out,
       not_74_out, not_75_out, not_76_out, not_77_out, not_78_out, not_79_out, not_80_out, not_81_out,
       not_82_out, not_83_out, not_84_out, not_85_out, not_86_out, not_87_out, not_88_out, not_89_out,
       not_90_out, not_91_out, not_92_out, not_93_out, not_94_out, not_95_out, not_96_out, not_97_out,
       not_98_out, not_99_out, not_100_out, not_101_out, not_102_out, not_103_out, not_104_out, not_105_out,
       not_106_out, not_107_out, not_108_out, not_109_out, not_110_out, not_111_out, not_112_out,
       not_113_out, not_114_out, not_115_out, not_116_out, not_117_out, not_118_out, not_119_out,
       not_120_out, not_121_out, not_122_out, not_123_out, not_124_out, not_125_out, not_126_out,
       not_127_out, not_128_out, not_129_out, not_130_out, not_131_out, not_132_out, not_133_out,
       not_134_out, not_135_out, not_136_out, not_137_out, not_138_out, not_139_out, not_140_out,
       not_141_out, not_142_out, not_143_out, not_144_out, not_145_out, not_146_out, not_147_out,
       not_148_out, not_149_out, not_150_out, not_151_out, not_152_out, not_153_out, not_154_out,
       not_155_out, not_156_out, not_157_out, not_158_out, not_159_out, not_160_out, not_161_out,
       not_162_out, not_163_out, not_164_out, not_165_out, not_166_out, not_167_out, not_168_out,
       not_169_out, not_170_out, not_171_out, not_172_out, not_173_out, not_174_out, not_175_out,
       not_176_out, not_177_out, not_178_out, not_179_out, not_180_out, not_181_out, not_182_out,
       not_183_out, not_184_out, not_185_out, not_186_out, not_187_out, not_188_out, not_189_out,
       not_190_out, not_191_out, not_192_out, not_193_out, not_194_out, not_195_out, not_196_out,
       not_197_out, not_198_out, not_199_out, not_200_out, not_201_out, not_202_out, not_203_out,
       not_204_out, not_205_out, not_206_out, not_207_out, not_208_out, not_209_out, not_210_out,
       not_211_out, not_212_out, not_213_out, not_214_out, not_215_out, not_216_out, not_217_out,
       not_218_out, not_219_out, not_220_out, not_221_out, not_222_out, not_223_out, not_224_out,
       not_225_out, not_226_out, not_227_out, not_228_out, not_229_out, not_230_out, not_231_out,
       not_232_out, not_233_out, not_234_out, not_235_out, not_236_out, not_237_out, not_238_out,
       not_239_out, not_240_out, not_241_out, not_242_out, not_243_out, not_244_out, not_245_out,
       not_246_out, not_247_out, not_248_out, not_249_out, not_250_out, not_251_out, not_252_out,
       not_253_out, not_254_out, not_255_out, not_256_out, not_257_out, not_258_out, not_259_out,
       not_260_out, not_261_out, not_262_out, not_263_out, not_264_out, not_265_out, not_266_out,
       not_267_out, not_268_out, not_269_out, not_270_out, not_271_out, not_272_out, not_273_out,
       not_274_out, not_275_out, not_276_out, not_277_out, not_278_out, not_279_out;

  not not_1 (not_1_out, OP5);
  not not_2 (not_2_out, OP4);
  not not_3 (not_3_out, OP3);
  not not_4 (not_4_out, OP2);
  not not_5 (not_5_out, OP1);
  not not_6 (not_6_out, OP0);
  not not_7 (not_7_out, F5);
  not not_8 (not_8_out, F4);
  not not_9 (not_9_out, F3);
  not not_10 (not_10_out, F2);
  not not_11 (not_11_out, OP5);
  not not_12 (not_12_out, OP4);
  not not_13 (not_13_out, OP3);
  not not_14 (not_14_out, OP2);
  not not_15 (not_15_out, OP1);
  not not_16 (not_16_out, OP0);
  not not_17 (not_17_out, F4);
  not not_18 (not_18_out, F3);
  not not_19 (not_19_out, F2);
  not not_20 (not_20_out, F1);
  not not_21 (not_21_out, F0);
  not not_22 (not_22_out, OP5);
  not not_23 (not_23_out, OP4);
  not not_24 (not_24_out, OP3);
  not not_25 (not_25_out, OP2);
  not not_26 (not_26_out, OP1);
  not not_27 (not_27_out, OP0);
  not not_28 (not_28_out, F4);
  not not_29 (not_29_out, F3);
  not not_30 (not_30_out, F2);
  not not_31 (not_31_out, F1);
  not not_32 (not_32_out, OP5);
  not not_33 (not_33_out, OP4);
  not not_34 (not_34_out, OP3);
  not not_35 (not_35_out, OP2);
  not not_36 (not_36_out, OP1);
  not not_37 (not_37_out, OP0);
  not not_38 (not_38_out, F4);
  not not_39 (not_39_out, F3);
  not not_40 (not_40_out, F1);
  not not_41 (not_41_out, F0);
  not not_42 (not_42_out, OP5);
  not not_43 (not_43_out, OP4);
  not not_44 (not_44_out, OP3);
  not not_45 (not_45_out, OP2);
  not not_46 (not_46_out, OP1);
  not not_47 (not_47_out, OP0);
  not not_48 (not_48_out, F4);
  not not_49 (not_49_out, F2);
  not not_50 (not_50_out, F0);
  not not_51 (not_51_out, OP5);
  not not_52 (not_52_out, OP4);
  not not_53 (not_53_out, OP2);
  not not_54 (not_54_out, OP1);
  not not_55 (not_55_out, OP0);
  not not_56 (not_56_out, OP5);
  not not_57 (not_57_out, OP4);
  not not_58 (not_58_out, OP1);
  not not_59 (not_59_out, OP0);
  not not_60 (not_60_out, OP5);
  not not_61 (not_61_out, OP4);
  not not_62 (not_62_out, OP2);
  not not_63 (not_63_out, OP1);
  not not_64 (not_64_out, OP5);
  not not_65 (not_65_out, OP4);
  not not_66 (not_66_out, OP2);
  not not_67 (not_67_out, OP0);
  not not_68 (not_68_out, OP4);
  not not_69 (not_69_out, OP3);
  not not_70 (not_70_out, OP2);
  not not_71 (not_71_out, OP4);
  not not_72 (not_72_out, OP2);
  not not_73 (not_73_out, OP5);
  not not_74 (not_74_out, OP4);
  not not_75 (not_75_out, OP3);
  not not_76 (not_76_out, OP2);
  not not_77 (not_77_out, OP1);
  not not_78 (not_78_out, OP0);
  not not_79 (not_79_out, F4);
  not not_80 (not_80_out, F3);
  not not_81 (not_81_out, F0);
  not not_82 (not_82_out, OP4);
  not not_83 (not_83_out, OP3);
  not not_84 (not_84_out, OP2);
  not not_85 (not_85_out, OP1);
  not not_86 (not_86_out, OP0);
  not not_87 (not_87_out, OP5);
  not not_88 (not_88_out, OP4);
  not not_89 (not_89_out, OP3);
  not not_90 (not_90_out, OP2);
  not not_91 (not_91_out, OP1);
  not not_92 (not_92_out, OP5);
  not not_93 (not_93_out, OP4);
  not not_94 (not_94_out, OP3);
  not not_95 (not_95_out, OP2);
  not not_96 (not_96_out, OP1);
  not not_97 (not_97_out, OP0);
  not not_98 (not_98_out, F5);
  not not_99 (not_99_out, F4);
  not not_100 (not_100_out, F3);
  not not_101 (not_101_out, F2);
  not not_102 (not_102_out, F0);
  not not_103 (not_103_out, OP5);
  not not_104 (not_104_out, OP4);
  not not_105 (not_105_out, OP3);
  not not_106 (not_106_out, OP2);
  not not_107 (not_107_out, OP1);
  not not_108 (not_108_out, OP0);
  not not_109 (not_109_out, F4);
  not not_110 (not_110_out, F3);
  not not_111 (not_111_out, F2);
  not not_112 (not_112_out, F0);
  not not_113 (not_113_out, OP5);
  not not_114 (not_114_out, OP4);
  not not_115 (not_115_out, OP3);
  not not_116 (not_116_out, OP2);
  not not_117 (not_117_out, OP1);
  not not_118 (not_118_out, OP0);
  not not_119 (not_119_out, F4);
  not not_120 (not_120_out, F3);
  not not_121 (not_121_out, F1);
  not not_122 (not_122_out, F0);
  not not_123 (not_123_out, OP5);
  not not_124 (not_124_out, OP4);
  not not_125 (not_125_out, OP3);
  not not_126 (not_126_out, OP2);
  not not_127 (not_127_out, OP1);
  not not_128 (not_128_out, OP0);
  not not_129 (not_129_out, F4);
  not not_130 (not_130_out, F3);
  not not_131 (not_131_out, OP5);
  not not_132 (not_132_out, OP4);
  not not_133 (not_133_out, OP3);
  not not_134 (not_134_out, OP2);
  not not_135 (not_135_out, OP1);
  not not_136 (not_136_out, OP0);
  not not_137 (not_137_out, F4);
  not not_138 (not_138_out, F2);
  not not_139 (not_139_out, F0);
  not not_140 (not_140_out, OP5);
  not not_141 (not_141_out, OP4);
  not not_142 (not_142_out, OP1);
  not not_143 (not_143_out, OP0);
  not not_144 (not_144_out, OP5);
  not not_145 (not_145_out, OP4);
  not not_146 (not_146_out, OP2);
  not not_147 (not_147_out, OP0);
  not not_148 (not_148_out, OP5);
  not not_149 (not_149_out, OP4);
  not not_150 (not_150_out, OP3);
  not not_151 (not_151_out, OP2);
  not not_152 (not_152_out, OP1);
  not not_153 (not_153_out, OP5);
  not not_154 (not_154_out, OP4);
  not not_155 (not_155_out, OP3);
  not not_156 (not_156_out, OP2);
  not not_157 (not_157_out, OP1);
  not not_158 (not_158_out, OP0);
  not not_159 (not_159_out, F4);
  not not_160 (not_160_out, F3);
  not not_161 (not_161_out, F2);
  not not_162 (not_162_out, F1);
  not not_163 (not_163_out, F0);
  not not_164 (not_164_out, OP5);
  not not_165 (not_165_out, OP4);
  not not_166 (not_166_out, OP3);
  not not_167 (not_167_out, OP2);
  not not_168 (not_168_out, OP1);
  not not_169 (not_169_out, OP0);
  not not_170 (not_170_out, F4);
  not not_171 (not_171_out, F3);
  not not_172 (not_172_out, F2);
  not not_173 (not_173_out, F1);
  not not_174 (not_174_out, OP5);
  not not_175 (not_175_out, OP4);
  not not_176 (not_176_out, OP3);
  not not_177 (not_177_out, OP2);
  not not_178 (not_178_out, OP1);
  not not_179 (not_179_out, OP0);
  not not_180 (not_180_out, F4);
  not not_181 (not_181_out, F3);
  not not_182 (not_182_out, F2);
  not not_183 (not_183_out, F0);
  not not_184 (not_184_out, OP5);
  not not_185 (not_185_out, OP4);
  not not_186 (not_186_out, OP3);
  not not_187 (not_187_out, OP2);
  not not_188 (not_188_out, OP1);
  not not_189 (not_189_out, OP0);
  not not_190 (not_190_out, F4);
  not not_191 (not_191_out, F3);
  not not_192 (not_192_out, F1);
  not not_193 (not_193_out, F0);
  not not_194 (not_194_out, OP5);
  not not_195 (not_195_out, OP4);
  not not_196 (not_196_out, OP3);
  not not_197 (not_197_out, OP2);
  not not_198 (not_198_out, OP1);
  not not_199 (not_199_out, OP0);
  not not_200 (not_200_out, F4);
  not not_201 (not_201_out, F2);
  not not_202 (not_202_out, OP5);
  not not_203 (not_203_out, OP4);
  not not_204 (not_204_out, OP2);
  not not_205 (not_205_out, OP1);
  not not_206 (not_206_out, OP0);
  not not_207 (not_207_out, OP5);
  not not_208 (not_208_out, OP4);
  not not_209 (not_209_out, OP1);
  not not_210 (not_210_out, OP0);
  not not_211 (not_211_out, OP5);
  not not_212 (not_212_out, OP4);
  not not_213 (not_213_out, OP2);
  not not_214 (not_214_out, OP1);
  not not_215 (not_215_out, OP4);
  not not_216 (not_216_out, OP3);
  not not_217 (not_217_out, OP2);
  not not_218 (not_218_out, OP4);
  not not_219 (not_219_out, OP2);
  not not_220 (not_220_out, OP4);
  not not_221 (not_221_out, OP3);
  not not_222 (not_222_out, OP2);
  not not_223 (not_223_out, OP1);
  not not_224 (not_224_out, OP0);
  not not_225 (not_225_out, OP5);
  not not_226 (not_226_out, OP4);
  not not_227 (not_227_out, OP3);
  not not_228 (not_228_out, OP2);
  not not_229 (not_229_out, OP1);
  not not_230 (not_230_out, OP0);
  not not_231 (not_231_out, F4);
  not not_232 (not_232_out, F3);
  not not_233 (not_233_out, F1);
  not not_234 (not_234_out, OP5);
  not not_235 (not_235_out, OP4);
  not not_236 (not_236_out, OP3);
  not not_237 (not_237_out, OP2);
  not not_238 (not_238_out, OP1);
  not not_239 (not_239_out, OP0);
  not not_240 (not_240_out, F4);
  not not_241 (not_241_out, F3);
  not not_242 (not_242_out, OP5);
  not not_243 (not_243_out, OP4);
  not not_244 (not_244_out, OP3);
  not not_245 (not_245_out, OP2);
  not not_246 (not_246_out, OP1);
  not not_247 (not_247_out, OP0);
  not not_248 (not_248_out, F4);
  not not_249 (not_249_out, F2);
  not not_250 (not_250_out, F0);
  not not_251 (not_251_out, OP5);
  not not_252 (not_252_out, OP4);
  not not_253 (not_253_out, OP3);
  not not_254 (not_254_out, OP2);
  not not_255 (not_255_out, OP1);
  not not_256 (not_256_out, OP0);
  not not_257 (not_257_out, F4);
  not not_258 (not_258_out, F2);
  not not_259 (not_259_out, OP5);
  not not_260 (not_260_out, OP4);
  not not_261 (not_261_out, OP2);
  not not_262 (not_262_out, OP0);
  not not_263 (not_263_out, OP5);
  not not_264 (not_264_out, OP4);
  not not_265 (not_265_out, OP1);
  not not_266 (not_266_out, OP5);
  not not_267 (not_267_out, OP4);
  not not_268 (not_268_out, OP3);
  not not_269 (not_269_out, OP2);
  not not_270 (not_270_out, OP1);
  not not_271 (not_271_out, OP0);
  not not_272 (not_272_out, F4);
  not not_273 (not_273_out, F3);
  not not_274 (not_274_out, F0);
  not not_275 (not_275_out, OP5);
  not not_276 (not_276_out, OP4);
  not not_277 (not_277_out, OP3);
  not not_278 (not_278_out, OP2);
  not not_279 (not_279_out, OP1);
  and and_1 (and_1_out, not_1_out, not_2_out, not_3_out, not_4_out, not_5_out, not_6_out, not_7_out, not_8_out, not_9_out, not_10_out, F1, F0);
  and and_2 (and_2_out, not_11_out, not_12_out, not_13_out, not_14_out, not_15_out, not_16_out, F5, not_17_out, not_18_out, not_19_out, not_20_out, not_21_out);
  and and_3 (and_3_out, not_22_out, not_23_out, not_24_out, not_25_out, not_26_out, not_27_out, F5, not_28_out, not_29_out, not_30_out, not_31_out, F0);
  and and_4 (and_4_out, not_32_out, not_33_out, not_34_out, not_35_out, not_36_out, not_37_out, F5, not_38_out, not_39_out, F2, not_40_out, not_41_out);
  and and_5 (and_5_out, not_42_out, not_43_out, not_44_out, not_45_out, not_46_out, not_47_out, F5, not_48_out, F3, not_49_out, F1, not_50_out);
  and and_6 (and_6_out, not_51_out, not_52_out, OP3, not_53_out, not_54_out, not_55_out);
  and and_7 (and_7_out, not_56_out, not_57_out, OP3, OP2, not_58_out, not_59_out);
  and and_8 (and_8_out, not_60_out, not_61_out, OP3, not_62_out, not_63_out, OP0);
  and and_9 (and_9_out, not_64_out, not_65_out, OP3, not_66_out, OP1, not_67_out);
  and and_10 (and_10_out, OP5, not_68_out, not_69_out, not_70_out, OP1, OP0);
  and and_11 (and_11_out, OP5, not_71_out, OP3, not_72_out, OP1, OP0);
  and and_12 (and_12_out, not_73_out, not_74_out, not_75_out, not_76_out, not_77_out, not_78_out, F5, not_79_out, not_80_out, F2, F1, not_81_out);
  and and_13 (and_13_out, OP5, not_82_out, not_83_out, not_84_out, not_85_out, not_86_out);
  and and_14 (and_14_out, not_87_out, not_88_out, not_89_out, not_90_out, not_91_out, OP0);
  and and_15 (and_15_out, not_92_out, not_93_out, not_94_out, not_95_out, not_96_out, not_97_out, not_98_out, not_99_out, not_100_out, not_101_out, F1, not_102_out);
  and and_16 (and_16_out, not_103_out, not_104_out, not_105_out, not_106_out, not_107_out, not_108_out, F5, not_109_out, not_110_out, not_111_out, F1, not_112_out);
  and and_17 (and_17_out, not_113_out, not_114_out, not_115_out, not_116_out, not_117_out, not_118_out, F5, not_119_out, not_120_out, F2, not_121_out, not_122_out);
  and and_18 (and_18_out, not_123_out, not_124_out, not_125_out, not_126_out, not_127_out, not_128_out, F5, not_129_out, not_130_out, F2, F1, F0);
  and and_19 (and_19_out, not_131_out, not_132_out, not_133_out, not_134_out, not_135_out, not_136_out, F5, not_137_out, F3, not_138_out, F1, not_139_out);
  and and_20 (and_20_out, not_140_out, not_141_out, OP3, OP2, not_142_out, not_143_out);
  and and_21 (and_21_out, not_144_out, not_145_out, OP3, not_146_out, OP1, not_147_out);
  and and_22 (and_22_out, not_148_out, not_149_out, not_150_out, not_151_out, not_152_out, OP0);
  and and_23 (and_23_out, not_153_out, not_154_out, not_155_out, not_156_out, not_157_out, not_158_out, F5, not_159_out, not_160_out, not_161_out, not_162_out, not_163_out);
  and and_24 (and_24_out, not_164_out, not_165_out, not_166_out, not_167_out, not_168_out, not_169_out, F5, not_170_out, not_171_out, not_172_out, not_173_out, F0);
  and and_25 (and_25_out, not_174_out, not_175_out, not_176_out, not_177_out, not_178_out, not_179_out, F5, not_180_out, not_181_out, not_182_out, F1, not_183_out);
  and and_26 (and_26_out, not_184_out, not_185_out, not_186_out, not_187_out, not_188_out, not_189_out, F5, not_190_out, not_191_out, F2, not_192_out, not_193_out);
  and and_27 (and_27_out, not_194_out, not_195_out, not_196_out, not_197_out, not_198_out, not_199_out, F5, not_200_out, F3, not_201_out, F1, F0);
  and and_28 (and_28_out, not_202_out, not_203_out, OP3, not_204_out, not_205_out, not_206_out);
  and and_29 (and_29_out, not_207_out, not_208_out, OP3, OP2, not_209_out, not_210_out);
  and and_30 (and_30_out, not_211_out, not_212_out, OP3, not_213_out, not_214_out, OP0);
  and and_31 (and_31_out, OP5, not_215_out, not_216_out, not_217_out, OP1, OP0);
  and and_32 (and_32_out, OP5, not_218_out, OP3, not_219_out, OP1, OP0);
  and and_33 (and_33_out, OP5, not_220_out, not_221_out, not_222_out, not_223_out, not_224_out);
  and and_34 (and_34_out, not_225_out, not_226_out, not_227_out, not_228_out, not_229_out, not_230_out, F5, not_231_out, not_232_out, F2, not_233_out, F0);
  and and_35 (and_35_out, not_234_out, not_235_out, not_236_out, not_237_out, not_238_out, not_239_out, F5, not_240_out, not_241_out, F2, F1, F0);
  and and_36 (and_36_out, not_242_out, not_243_out, not_244_out, not_245_out, not_246_out, not_247_out, F5, not_248_out, F3, not_249_out, F1, not_250_out);
  and and_37 (and_37_out, not_251_out, not_252_out, not_253_out, not_254_out, not_255_out, not_256_out, F5, not_257_out, F3, not_258_out, F1, F0);
  and and_38 (and_38_out, not_259_out, not_260_out, OP3, not_261_out, OP1, not_262_out);
  and and_39 (and_39_out, not_263_out, not_264_out, OP3, OP2, not_265_out, OP0);
  and and_40 (and_40_out, not_266_out, not_267_out, not_268_out, not_269_out, not_270_out, not_271_out, F5, not_272_out, not_273_out, F2, F1, not_274_out);
  and and_41 (and_41_out, not_275_out, not_276_out, not_277_out, not_278_out, not_279_out, OP0);
  or or_1 (S1, and_15_out, and_16_out, and_17_out, and_18_out, and_19_out, and_20_out, and_21_out, and_22_out);
  or or_2 (S2, and_23_out, and_24_out, and_25_out, and_26_out, and_27_out, and_28_out, and_29_out, and_30_out, and_31_out, and_32_out, and_33_out);
  or or_3 (S3, and_34_out, and_35_out, and_36_out, and_37_out, and_38_out, and_39_out, and_40_out, and_41_out);
  or or_4 (S0, and_1_out, and_2_out, and_3_out, and_4_out, and_5_out, and_6_out, and_7_out, and_8_out, and_9_out, and_10_out, and_11_out, and_12_out, and_13_out, and_14_out);
endmodule

// 控制信号生成
module \控制信号生成  (
  input  OP0,
  input  OP1,
  input  OP2,
  input  OP3,
  input  OP4,
  input  OP5,
  input  F0,
  input  F1,
  input  F2,
  input  F3,
  input  F4,
  input  F5,
  output MemToReg,
  output MemWrite,
  output ALU_SRC,
  output RegWrite,
  output SysCALL,
  output SignedExt,
  output RegDst,
  output BEQ,
  output BNE,
  output JR,
  output JMP,
  output JAL
);

  wire and_1_out, and_2_out, and_4_out, and_5_out, and_6_out, and_7_out, and_8_out, and_9_out, and_10_out,
       and_11_out, and_12_out, and_13_out, and_14_out, and_15_out, and_16_out, and_17_out, and_18_out,
       and_19_out, and_20_out, and_21_out, and_22_out, and_23_out, and_24_out, and_25_out, and_26_out,
       and_27_out, and_28_out, and_29_out, and_30_out, and_31_out, and_32_out, and_34_out, and_35_out,
       and_36_out, and_37_out, and_38_out, and_39_out, and_40_out, and_41_out, and_42_out, and_43_out,
       and_44_out, and_45_out, and_46_out, and_47_out, and_48_out, and_49_out, and_50_out, and_51_out,
       and_52_out, and_53_out, and_54_out, and_58_out, and_59_out, and_60_out, not_1_out, not_2_out,
       not_3_out, not_4_out, not_5_out, not_6_out, not_7_out, not_8_out, not_9_out, not_10_out, not_11_out,
       not_12_out, not_13_out, not_14_out, not_15_out, not_16_out, not_17_out, not_18_out, not_19_out,
       not_20_out, not_21_out, not_22_out, not_23_out, not_24_out, not_25_out, not_26_out, not_27_out,
       not_28_out, not_29_out, not_30_out, not_31_out, not_32_out, not_33_out, not_34_out, not_35_out,
       not_36_out, not_37_out, not_38_out, not_39_out, not_40_out, not_41_out, not_42_out, not_43_out,
       not_44_out, not_45_out, not_46_out, not_47_out, not_48_out, not_49_out, not_50_out, not_51_out,
       not_52_out, not_53_out, not_54_out, not_55_out, not_56_out, not_57_out, not_58_out, not_59_out,
       not_60_out, not_61_out, not_62_out, not_63_out, not_64_out, not_65_out, not_66_out, not_67_out,
       not_68_out, not_69_out, not_70_out, not_71_out, not_72_out, not_73_out, not_74_out, not_75_out,
       not_76_out, not_77_out, not_78_out, not_79_out, not_80_out, not_81_out, not_82_out, not_83_out,
       not_84_out, not_85_out, not_86_out, not_87_out, not_88_out, not_89_out, not_90_out, not_91_out,
       not_92_out, not_93_out, not_94_out, not_95_out, not_96_out, not_97_out, not_98_out, not_99_out,
       not_100_out, not_101_out, not_102_out, not_103_out, not_104_out, not_105_out, not_106_out,
       not_107_out, not_108_out, not_109_out, not_110_out, not_111_out, not_112_out, not_113_out,
       not_114_out, not_115_out, not_116_out, not_117_out, not_118_out, not_119_out, not_120_out,
       not_121_out, not_122_out, not_123_out, not_124_out, not_125_out, not_126_out, not_127_out,
       not_128_out, not_129_out, not_130_out, not_131_out, not_132_out, not_133_out, not_134_out,
       not_135_out, not_136_out, not_137_out, not_138_out, not_139_out, not_140_out, not_141_out,
       not_142_out, not_143_out, not_144_out, not_145_out, not_146_out, not_147_out, not_148_out,
       not_149_out, not_150_out, not_151_out, not_152_out, not_153_out, not_154_out, not_155_out,
       not_156_out, not_157_out, not_158_out, not_159_out, not_160_out, not_161_out, not_162_out,
       not_163_out, not_164_out, not_165_out, not_166_out, not_167_out, not_168_out, not_169_out,
       not_170_out, not_171_out, not_172_out, not_173_out, not_174_out, not_175_out, not_176_out,
       not_177_out, not_178_out, not_179_out, not_180_out, not_181_out, not_182_out, not_183_out,
       not_184_out, not_185_out, not_186_out, not_187_out, not_188_out, not_189_out, not_190_out,
       not_191_out, not_192_out, not_193_out, not_194_out, not_195_out, not_196_out, not_197_out,
       not_198_out, not_199_out, not_200_out, not_201_out, not_202_out, not_203_out, not_204_out,
       not_205_out, not_206_out, not_207_out, not_208_out, not_209_out, not_210_out, not_211_out,
       not_212_out, not_213_out, not_214_out, not_215_out, not_216_out, not_217_out, not_218_out,
       not_219_out, not_220_out, not_221_out, not_222_out, not_223_out, not_224_out, not_225_out,
       not_226_out, not_227_out, not_228_out, not_229_out, not_230_out, not_231_out, not_232_out,
       not_233_out, not_234_out, not_235_out, not_236_out, not_237_out, not_238_out, not_239_out,
       not_240_out, not_241_out, not_242_out, not_243_out, not_244_out, not_245_out, not_246_out,
       not_247_out, not_248_out, not_249_out, not_250_out, not_251_out, not_252_out, not_253_out,
       not_254_out, not_255_out, not_256_out, not_257_out, not_258_out, not_259_out, not_260_out,
       not_261_out, not_262_out, not_263_out, not_264_out, not_265_out, not_266_out, not_267_out,
       not_268_out, not_269_out, not_270_out, not_271_out, not_272_out, not_273_out, not_274_out,
       not_275_out, not_276_out, not_277_out, not_278_out, not_279_out, not_280_out, not_281_out,
       not_282_out, not_283_out, not_284_out, not_285_out, not_286_out, not_287_out, not_288_out,
       not_289_out, not_290_out, not_291_out, not_292_out, not_293_out, not_294_out, not_295_out,
       not_296_out, not_297_out, not_298_out, not_299_out, not_300_out, not_301_out, not_302_out,
       not_303_out, not_304_out, not_305_out, not_306_out, not_307_out, not_308_out, not_309_out,
       not_310_out, not_311_out, not_312_out, not_313_out, not_314_out, not_315_out, not_316_out,
       not_317_out, not_318_out, not_319_out, not_320_out, not_321_out, not_322_out, not_323_out,
       not_324_out, not_325_out, not_326_out, not_327_out, not_328_out, not_329_out, not_330_out,
       not_331_out, not_332_out, not_333_out, not_334_out, not_335_out, not_336_out, not_337_out,
       not_338_out, not_339_out, not_340_out, not_341_out, not_342_out, not_343_out, not_344_out,
       not_345_out, not_346_out, not_347_out, not_348_out, not_349_out, not_350_out, not_351_out,
       not_352_out, not_353_out, not_354_out, not_355_out, not_356_out, not_357_out, not_358_out,
       not_359_out, not_360_out, not_361_out, not_362_out, not_363_out, not_364_out, not_365_out,
       not_366_out, not_367_out, not_368_out, not_369_out, not_370_out, not_371_out, not_372_out,
       not_373_out, not_374_out, not_375_out, not_376_out, not_377_out, not_378_out, not_379_out,
       not_380_out, not_381_out, not_382_out, not_383_out, not_384_out, not_385_out, not_386_out,
       not_387_out, not_388_out, not_389_out, not_390_out, not_391_out, not_392_out, not_393_out,
       not_394_out, not_395_out, not_396_out, not_397_out, not_398_out, not_399_out, not_400_out,
       not_401_out, not_402_out, not_403_out, not_404_out, not_405_out, not_406_out, not_407_out,
       not_408_out, not_409_out, not_410_out, not_411_out, not_412_out, not_413_out, not_414_out;

  not not_1 (not_1_out, OP4);
  not not_2 (not_2_out, OP3);
  not not_3 (not_3_out, OP2);
  not not_4 (not_4_out, OP4);
  not not_5 (not_5_out, OP3);
  not not_6 (not_6_out, OP2);
  not not_7 (not_7_out, OP1);
  not not_8 (not_8_out, OP0);
  not not_9 (not_9_out, OP4);
  not not_10 (not_10_out, OP2);
  not not_11 (not_11_out, OP5);
  not not_12 (not_12_out, OP4);
  not not_13 (not_13_out, OP2);
  not not_14 (not_14_out, OP1);
  not not_15 (not_15_out, OP0);
  not not_16 (not_16_out, OP5);
  not not_17 (not_17_out, OP4);
  not not_18 (not_18_out, OP1);
  not not_19 (not_19_out, OP0);
  not not_20 (not_20_out, OP5);
  not not_21 (not_21_out, OP4);
  not not_22 (not_22_out, OP2);
  not not_23 (not_23_out, OP1);
  not not_24 (not_24_out, OP5);
  not not_25 (not_25_out, OP4);
  not not_26 (not_26_out, OP2);
  not not_27 (not_27_out, OP0);
  not not_28 (not_28_out, OP5);
  not not_29 (not_29_out, OP4);
  not not_30 (not_30_out, OP1);
  not not_31 (not_31_out, OP4);
  not not_32 (not_32_out, OP3);
  not not_33 (not_33_out, OP2);
  not not_34 (not_34_out, OP4);
  not not_35 (not_35_out, OP2);
  not not_36 (not_36_out, OP4);
  not not_37 (not_37_out, OP3);
  not not_38 (not_38_out, OP2);
  not not_39 (not_39_out, OP1);
  not not_40 (not_40_out, OP0);
  not not_41 (not_41_out, OP5);
  not not_42 (not_42_out, OP4);
  not not_43 (not_43_out, OP3);
  not not_44 (not_44_out, OP2);
  not not_45 (not_45_out, OP1);
  not not_46 (not_46_out, OP0);
  not not_47 (not_47_out, F5);
  not not_48 (not_48_out, F4);
  not not_49 (not_49_out, F3);
  not not_50 (not_50_out, F2);
  not not_51 (not_51_out, F1);
  not not_52 (not_52_out, F0);
  not not_53 (not_53_out, OP5);
  not not_54 (not_54_out, OP4);
  not not_55 (not_55_out, OP3);
  not not_56 (not_56_out, OP2);
  not not_57 (not_57_out, OP1);
  not not_58 (not_58_out, OP0);
  not not_59 (not_59_out, F5);
  not not_60 (not_60_out, F4);
  not not_61 (not_61_out, F3);
  not not_62 (not_62_out, F2);
  not not_63 (not_63_out, OP5);
  not not_64 (not_64_out, OP4);
  not not_65 (not_65_out, OP3);
  not not_66 (not_66_out, OP2);
  not not_67 (not_67_out, OP1);
  not not_68 (not_68_out, OP0);
  not not_69 (not_69_out, F5);
  not not_70 (not_70_out, F4);
  not not_71 (not_71_out, F3);
  not not_72 (not_72_out, F2);
  not not_73 (not_73_out, F0);
  not not_74 (not_74_out, OP5);
  not not_75 (not_75_out, OP4);
  not not_76 (not_76_out, OP3);
  not not_77 (not_77_out, OP2);
  not not_78 (not_78_out, OP1);
  not not_79 (not_79_out, OP0);
  not not_80 (not_80_out, F4);
  not not_81 (not_81_out, F3);
  not not_82 (not_82_out, F2);
  not not_83 (not_83_out, F1);
  not not_84 (not_84_out, F0);
  not not_85 (not_85_out, OP5);
  not not_86 (not_86_out, OP4);
  not not_87 (not_87_out, OP3);
  not not_88 (not_88_out, OP2);
  not not_89 (not_89_out, OP1);
  not not_90 (not_90_out, OP0);
  not not_91 (not_91_out, F4);
  not not_92 (not_92_out, F3);
  not not_93 (not_93_out, F2);
  not not_94 (not_94_out, F1);
  not not_95 (not_95_out, OP5);
  not not_96 (not_96_out, OP4);
  not not_97 (not_97_out, OP3);
  not not_98 (not_98_out, OP2);
  not not_99 (not_99_out, OP1);
  not not_100 (not_100_out, OP0);
  not not_101 (not_101_out, F4);
  not not_102 (not_102_out, F3);
  not not_103 (not_103_out, F2);
  not not_104 (not_104_out, F0);
  not not_105 (not_105_out, OP5);
  not not_106 (not_106_out, OP4);
  not not_107 (not_107_out, OP3);
  not not_108 (not_108_out, OP2);
  not not_109 (not_109_out, OP1);
  not not_110 (not_110_out, OP0);
  not not_111 (not_111_out, F4);
  not not_112 (not_112_out, F3);
  not not_113 (not_113_out, F1);
  not not_114 (not_114_out, F0);
  not not_115 (not_115_out, OP5);
  not not_116 (not_116_out, OP4);
  not not_117 (not_117_out, OP3);
  not not_118 (not_118_out, OP2);
  not not_119 (not_119_out, OP1);
  not not_120 (not_120_out, OP0);
  not not_121 (not_121_out, F4);
  not not_122 (not_122_out, F3);
  not not_123 (not_123_out, F1);
  not not_124 (not_124_out, OP5);
  not not_125 (not_125_out, OP4);
  not not_126 (not_126_out, OP3);
  not not_127 (not_127_out, OP2);
  not not_128 (not_128_out, OP1);
  not not_129 (not_129_out, OP0);
  not not_130 (not_130_out, F4);
  not not_131 (not_131_out, F3);
  not not_132 (not_132_out, OP5);
  not not_133 (not_133_out, OP4);
  not not_134 (not_134_out, OP3);
  not not_135 (not_135_out, OP2);
  not not_136 (not_136_out, OP1);
  not not_137 (not_137_out, OP0);
  not not_138 (not_138_out, F4);
  not not_139 (not_139_out, F2);
  not not_140 (not_140_out, F0);
  not not_141 (not_141_out, OP5);
  not not_142 (not_142_out, OP4);
  not not_143 (not_143_out, OP3);
  not not_144 (not_144_out, OP2);
  not not_145 (not_145_out, OP1);
  not not_146 (not_146_out, OP0);
  not not_147 (not_147_out, F4);
  not not_148 (not_148_out, F2);
  not not_149 (not_149_out, OP5);
  not not_150 (not_150_out, OP4);
  not not_151 (not_151_out, OP3);
  not not_152 (not_152_out, OP2);
  not not_153 (not_153_out, OP5);
  not not_154 (not_154_out, OP4);
  not not_155 (not_155_out, OP2);
  not not_156 (not_156_out, OP1);
  not not_157 (not_157_out, OP0);
  not not_158 (not_158_out, OP5);
  not not_159 (not_159_out, OP4);
  not not_160 (not_160_out, OP1);
  not not_161 (not_161_out, OP0);
  not not_162 (not_162_out, OP5);
  not not_163 (not_163_out, OP4);
  not not_164 (not_164_out, OP2);
  not not_165 (not_165_out, OP1);
  not not_166 (not_166_out, OP5);
  not not_167 (not_167_out, OP4);
  not not_168 (not_168_out, OP2);
  not not_169 (not_169_out, OP0);
  not not_170 (not_170_out, OP5);
  not not_171 (not_171_out, OP4);
  not not_172 (not_172_out, OP1);
  not not_173 (not_173_out, OP4);
  not not_174 (not_174_out, OP3);
  not not_175 (not_175_out, OP2);
  not not_176 (not_176_out, OP5);
  not not_177 (not_177_out, OP4);
  not not_178 (not_178_out, OP3);
  not not_179 (not_179_out, OP2);
  not not_180 (not_180_out, OP1);
  not not_181 (not_181_out, OP0);
  not not_182 (not_182_out, F5);
  not not_183 (not_183_out, F4);
  not not_184 (not_184_out, F3);
  not not_185 (not_185_out, F1);
  not not_186 (not_186_out, F0);
  not not_187 (not_187_out, OP5);
  not not_188 (not_188_out, OP4);
  not not_189 (not_189_out, OP3);
  not not_190 (not_190_out, OP2);
  not not_191 (not_191_out, OP1);
  not not_192 (not_192_out, OP0);
  not not_193 (not_193_out, F4);
  not not_194 (not_194_out, F3);
  not not_195 (not_195_out, F0);
  not not_196 (not_196_out, OP4);
  not not_197 (not_197_out, OP3);
  not not_198 (not_198_out, OP2);
  not not_199 (not_199_out, OP1);
  not not_200 (not_200_out, OP0);
  not not_201 (not_201_out, OP5);
  not not_202 (not_202_out, OP4);
  not not_203 (not_203_out, OP3);
  not not_204 (not_204_out, OP2);
  not not_205 (not_205_out, OP1);
  not not_206 (not_206_out, OP0);
  not not_207 (not_207_out, F5);
  not not_208 (not_208_out, F4);
  not not_209 (not_209_out, F1);
  not not_210 (not_210_out, F0);
  not not_211 (not_211_out, OP5);
  not not_212 (not_212_out, OP4);
  not not_213 (not_213_out, OP3);
  not not_214 (not_214_out, OP1);
  not not_215 (not_215_out, OP0);
  not not_216 (not_216_out, OP5);
  not not_217 (not_217_out, OP4);
  not not_218 (not_218_out, OP3);
  not not_219 (not_219_out, OP1);
  not not_220 (not_220_out, OP5);
  not not_221 (not_221_out, OP4);
  not not_222 (not_222_out, OP2);
  not not_223 (not_223_out, OP1);
  not not_224 (not_224_out, OP0);
  not not_225 (not_225_out, OP5);
  not not_226 (not_226_out, OP4);
  not not_227 (not_227_out, OP2);
  not not_228 (not_228_out, OP1);
  not not_229 (not_229_out, OP5);
  not not_230 (not_230_out, OP4);
  not not_231 (not_231_out, OP2);
  not not_232 (not_232_out, OP0);
  not not_233 (not_233_out, OP4);
  not not_234 (not_234_out, OP3);
  not not_235 (not_235_out, OP2);
  not not_236 (not_236_out, OP4);
  not not_237 (not_237_out, OP2);
  not not_238 (not_238_out, OP4);
  not not_239 (not_239_out, OP3);
  not not_240 (not_240_out, OP2);
  not not_241 (not_241_out, OP1);
  not not_242 (not_242_out, OP0);
  not not_243 (not_243_out, OP5);
  not not_244 (not_244_out, OP4);
  not not_245 (not_245_out, OP3);
  not not_246 (not_246_out, OP2);
  not not_247 (not_247_out, OP1);
  not not_248 (not_248_out, OP0);
  not not_249 (not_249_out, F5);
  not not_250 (not_250_out, F4);
  not not_251 (not_251_out, F3);
  not not_252 (not_252_out, F2);
  not not_253 (not_253_out, F1);
  not not_254 (not_254_out, F0);
  not not_255 (not_255_out, OP5);
  not not_256 (not_256_out, OP4);
  not not_257 (not_257_out, OP3);
  not not_258 (not_258_out, OP2);
  not not_259 (not_259_out, OP1);
  not not_260 (not_260_out, OP0);
  not not_261 (not_261_out, F5);
  not not_262 (not_262_out, F4);
  not not_263 (not_263_out, F3);
  not not_264 (not_264_out, F2);
  not not_265 (not_265_out, OP5);
  not not_266 (not_266_out, OP4);
  not not_267 (not_267_out, OP3);
  not not_268 (not_268_out, OP2);
  not not_269 (not_269_out, OP1);
  not not_270 (not_270_out, OP0);
  not not_271 (not_271_out, F5);
  not not_272 (not_272_out, F4);
  not not_273 (not_273_out, F3);
  not not_274 (not_274_out, F2);
  not not_275 (not_275_out, F0);
  not not_276 (not_276_out, OP5);
  not not_277 (not_277_out, OP4);
  not not_278 (not_278_out, OP3);
  not not_279 (not_279_out, OP2);
  not not_280 (not_280_out, OP1);
  not not_281 (not_281_out, OP0);
  not not_282 (not_282_out, F4);
  not not_283 (not_283_out, F3);
  not not_284 (not_284_out, F2);
  not not_285 (not_285_out, F1);
  not not_286 (not_286_out, F0);
  not not_287 (not_287_out, OP5);
  not not_288 (not_288_out, OP4);
  not not_289 (not_289_out, OP3);
  not not_290 (not_290_out, OP2);
  not not_291 (not_291_out, OP1);
  not not_292 (not_292_out, OP0);
  not not_293 (not_293_out, F4);
  not not_294 (not_294_out, F3);
  not not_295 (not_295_out, F2);
  not not_296 (not_296_out, F1);
  not not_297 (not_297_out, OP5);
  not not_298 (not_298_out, OP4);
  not not_299 (not_299_out, OP3);
  not not_300 (not_300_out, OP2);
  not not_301 (not_301_out, OP1);
  not not_302 (not_302_out, OP0);
  not not_303 (not_303_out, F4);
  not not_304 (not_304_out, F3);
  not not_305 (not_305_out, F2);
  not not_306 (not_306_out, F0);
  not not_307 (not_307_out, OP5);
  not not_308 (not_308_out, OP4);
  not not_309 (not_309_out, OP3);
  not not_310 (not_310_out, OP2);
  not not_311 (not_311_out, OP1);
  not not_312 (not_312_out, OP0);
  not not_313 (not_313_out, F4);
  not not_314 (not_314_out, F3);
  not not_315 (not_315_out, F1);
  not not_316 (not_316_out, F0);
  not not_317 (not_317_out, OP5);
  not not_318 (not_318_out, OP4);
  not not_319 (not_319_out, OP3);
  not not_320 (not_320_out, OP2);
  not not_321 (not_321_out, OP1);
  not not_322 (not_322_out, OP0);
  not not_323 (not_323_out, F4);
  not not_324 (not_324_out, F3);
  not not_325 (not_325_out, F1);
  not not_326 (not_326_out, OP5);
  not not_327 (not_327_out, OP4);
  not not_328 (not_328_out, OP3);
  not not_329 (not_329_out, OP2);
  not not_330 (not_330_out, OP1);
  not not_331 (not_331_out, OP0);
  not not_332 (not_332_out, F4);
  not not_333 (not_333_out, F3);
  not not_334 (not_334_out, OP5);
  not not_335 (not_335_out, OP4);
  not not_336 (not_336_out, OP3);
  not not_337 (not_337_out, OP2);
  not not_338 (not_338_out, OP1);
  not not_339 (not_339_out, OP0);
  not not_340 (not_340_out, F4);
  not not_341 (not_341_out, F2);
  not not_342 (not_342_out, F0);
  not not_343 (not_343_out, OP5);
  not not_344 (not_344_out, OP4);
  not not_345 (not_345_out, OP3);
  not not_346 (not_346_out, OP2);
  not not_347 (not_347_out, OP1);
  not not_348 (not_348_out, OP0);
  not not_349 (not_349_out, F4);
  not not_350 (not_350_out, F2);
  not not_351 (not_351_out, OP5);
  not not_352 (not_352_out, OP4);
  not not_353 (not_353_out, OP3);
  not not_354 (not_354_out, OP2);
  not not_355 (not_355_out, OP1);
  not not_356 (not_356_out, OP0);
  not not_357 (not_357_out, F5);
  not not_358 (not_358_out, F4);
  not not_359 (not_359_out, F3);
  not not_360 (not_360_out, F1);
  not not_361 (not_361_out, F0);
  not not_362 (not_362_out, OP5);
  not not_363 (not_363_out, OP4);
  not not_364 (not_364_out, OP3);
  not not_365 (not_365_out, OP2);
  not not_366 (not_366_out, OP1);
  not not_367 (not_367_out, OP0);
  not not_368 (not_368_out, F4);
  not not_369 (not_369_out, F3);
  not not_370 (not_370_out, F0);
  not not_371 (not_371_out, OP5);
  not not_372 (not_372_out, OP4);
  not not_373 (not_373_out, OP3);
  not not_374 (not_374_out, OP1);
  not not_375 (not_375_out, OP0);
  not not_376 (not_376_out, OP5);
  not not_377 (not_377_out, OP4);
  not not_378 (not_378_out, OP3);
  not not_379 (not_379_out, OP1);
  not not_380 (not_380_out, OP5);
  not not_381 (not_381_out, OP4);
  not not_382 (not_382_out, OP3);
  not not_383 (not_383_out, OP2);
  not not_384 (not_384_out, OP1);
  not not_385 (not_385_out, OP0);
  not not_386 (not_386_out, F5);
  not not_387 (not_387_out, F4);
  not not_388 (not_388_out, F2);
  not not_389 (not_389_out, F1);
  not not_390 (not_390_out, F0);
  not not_391 (not_391_out, OP5);
  not not_392 (not_392_out, OP4);
  not not_393 (not_393_out, OP3);
  not not_394 (not_394_out, OP2);
  not not_395 (not_395_out, OP1);
  not not_396 (not_396_out, OP0);
  not not_397 (not_397_out, F5);
  not not_398 (not_398_out, F4);
  not not_399 (not_399_out, F2);
  not not_400 (not_400_out, F1);
  not not_401 (not_401_out, F0);
  not not_402 (not_402_out, OP5);
  not not_403 (not_403_out, OP4);
  not not_404 (not_404_out, OP3);
  not not_405 (not_405_out, OP2);
  not not_406 (not_406_out, OP0);
  not not_407 (not_407_out, OP5);
  not not_408 (not_408_out, OP4);
  not not_409 (not_409_out, OP3);
  not not_410 (not_410_out, OP2);
  not not_411 (not_411_out, OP5);
  not not_412 (not_412_out, OP4);
  not not_413 (not_413_out, OP3);
  not not_414 (not_414_out, OP2);
  and and_1 (and_1_out, OP5, not_1_out, not_2_out, not_3_out, OP1, OP0);
  and and_2 (and_2_out, OP5, not_4_out, not_5_out, not_6_out, not_7_out, not_8_out);
  and and_3 (MemWrite, OP5, not_9_out, OP3, not_10_out, OP1, OP0);
  and and_4 (and_4_out, not_11_out, not_12_out, OP3, not_13_out, not_14_out, not_15_out);
  and and_5 (and_5_out, not_16_out, not_17_out, OP3, OP2, not_18_out, not_19_out);
  and and_6 (and_6_out, not_20_out, not_21_out, OP3, not_22_out, not_23_out, OP0);
  and and_7 (and_7_out, not_24_out, not_25_out, OP3, not_26_out, OP1, not_27_out);
  and and_8 (and_8_out, not_28_out, not_29_out, OP3, OP2, not_30_out, OP0);
  and and_9 (and_9_out, OP5, not_31_out, not_32_out, not_33_out, OP1, OP0);
  and and_10 (and_10_out, OP5, not_34_out, OP3, not_35_out, OP1, OP0);
  and and_11 (and_11_out, OP5, not_36_out, not_37_out, not_38_out, not_39_out, not_40_out);
  and and_12 (and_12_out, not_41_out, not_42_out, not_43_out, not_44_out, not_45_out, not_46_out, not_47_out, not_48_out, not_49_out, not_50_out, not_51_out, not_52_out);
  and and_13 (and_13_out, not_53_out, not_54_out, not_55_out, not_56_out, not_57_out, not_58_out, not_59_out, not_60_out, not_61_out, not_62_out, F1, F0);
  and and_14 (and_14_out, not_63_out, not_64_out, not_65_out, not_66_out, not_67_out, not_68_out, not_69_out, not_70_out, not_71_out, not_72_out, F1, not_73_out);
  and and_15 (and_15_out, not_74_out, not_75_out, not_76_out, not_77_out, not_78_out, not_79_out, F5, not_80_out, not_81_out, not_82_out, not_83_out, not_84_out);
  and and_16 (and_16_out, not_85_out, not_86_out, not_87_out, not_88_out, not_89_out, not_90_out, F5, not_91_out, not_92_out, not_93_out, not_94_out, F0);
  and and_17 (and_17_out, not_95_out, not_96_out, not_97_out, not_98_out, not_99_out, not_100_out, F5, not_101_out, not_102_out, not_103_out, F1, not_104_out);
  and and_18 (and_18_out, not_105_out, not_106_out, not_107_out, not_108_out, not_109_out, not_110_out, F5, not_111_out, not_112_out, F2, not_113_out, not_114_out);
  and and_19 (and_19_out, not_115_out, not_116_out, not_117_out, not_118_out, not_119_out, not_120_out, F5, not_121_out, not_122_out, F2, not_123_out, F0);
  and and_20 (and_20_out, not_124_out, not_125_out, not_126_out, not_127_out, not_128_out, not_129_out, F5, not_130_out, not_131_out, F2, F1, F0);
  and and_21 (and_21_out, not_132_out, not_133_out, not_134_out, not_135_out, not_136_out, not_137_out, F5, not_138_out, F3, not_139_out, F1, not_140_out);
  and and_22 (and_22_out, not_141_out, not_142_out, not_143_out, not_144_out, not_145_out, not_146_out, F5, not_147_out, F3, not_148_out, F1, F0);
  and and_23 (and_23_out, not_149_out, not_150_out, not_151_out, not_152_out, OP1, OP0);
  and and_24 (and_24_out, not_153_out, not_154_out, OP3, not_155_out, not_156_out, not_157_out);
  and and_25 (and_25_out, not_158_out, not_159_out, OP3, OP2, not_160_out, not_161_out);
  and and_26 (and_26_out, not_162_out, not_163_out, OP3, not_164_out, not_165_out, OP0);
  and and_27 (and_27_out, not_166_out, not_167_out, OP3, not_168_out, OP1, not_169_out);
  and and_28 (and_28_out, not_170_out, not_171_out, OP3, OP2, not_172_out, OP0);
  and and_29 (and_29_out, OP5, not_173_out, not_174_out, not_175_out, OP1, OP0);
  and and_30 (and_30_out, not_176_out, not_177_out, not_178_out, not_179_out, not_180_out, not_181_out, not_182_out, not_183_out, not_184_out, F2, not_185_out, not_186_out);
  and and_31 (and_31_out, not_187_out, not_188_out, not_189_out, not_190_out, not_191_out, not_192_out, F5, not_193_out, not_194_out, F2, F1, not_195_out);
  and and_32 (and_32_out, OP5, not_196_out, not_197_out, not_198_out, not_199_out, not_200_out);
  and and_33 (SysCALL, not_201_out, not_202_out, not_203_out, not_204_out, not_205_out, not_206_out, not_207_out, not_208_out, F3, F2, not_209_out, not_210_out);
  and and_34 (and_34_out, not_211_out, not_212_out, not_213_out, OP2, not_214_out, not_215_out);
  and and_35 (and_35_out, not_216_out, not_217_out, not_218_out, OP2, not_219_out, OP0);
  and and_36 (and_36_out, not_220_out, not_221_out, OP3, not_222_out, not_223_out, not_224_out);
  and and_37 (and_37_out, not_225_out, not_226_out, OP3, not_227_out, not_228_out, OP0);
  and and_38 (and_38_out, not_229_out, not_230_out, OP3, not_231_out, OP1, not_232_out);
  and and_39 (and_39_out, OP5, not_233_out, not_234_out, not_235_out, OP1, OP0);
  and and_40 (and_40_out, OP5, not_236_out, OP3, not_237_out, OP1, OP0);
  and and_41 (and_41_out, OP5, not_238_out, not_239_out, not_240_out, not_241_out, not_242_out);
  and and_42 (and_42_out, not_243_out, not_244_out, not_245_out, not_246_out, not_247_out, not_248_out, not_249_out, not_250_out, not_251_out, not_252_out, not_253_out, not_254_out);
  and and_43 (and_43_out, not_255_out, not_256_out, not_257_out, not_258_out, not_259_out, not_260_out, not_261_out, not_262_out, not_263_out, not_264_out, F1, F0);
  and and_44 (and_44_out, not_265_out, not_266_out, not_267_out, not_268_out, not_269_out, not_270_out, not_271_out, not_272_out, not_273_out, not_274_out, F1, not_275_out);
  and and_45 (and_45_out, not_276_out, not_277_out, not_278_out, not_279_out, not_280_out, not_281_out, F5, not_282_out, not_283_out, not_284_out, not_285_out, not_286_out);
  and and_46 (and_46_out, not_287_out, not_288_out, not_289_out, not_290_out, not_291_out, not_292_out, F5, not_293_out, not_294_out, not_295_out, not_296_out, F0);
  and and_47 (and_47_out, not_297_out, not_298_out, not_299_out, not_300_out, not_301_out, not_302_out, F5, not_303_out, not_304_out, not_305_out, F1, not_306_out);
  and and_48 (and_48_out, not_307_out, not_308_out, not_309_out, not_310_out, not_311_out, not_312_out, F5, not_313_out, not_314_out, F2, not_315_out, not_316_out);
  and and_49 (and_49_out, not_317_out, not_318_out, not_319_out, not_320_out, not_321_out, not_322_out, F5, not_323_out, not_324_out, F2, not_325_out, F0);
  and and_50 (and_50_out, not_326_out, not_327_out, not_328_out, not_329_out, not_330_out, not_331_out, F5, not_332_out, not_333_out, F2, F1, F0);
  and and_51 (and_51_out, not_334_out, not_335_out, not_336_out, not_337_out, not_338_out, not_339_out, F5, not_340_out, F3, not_341_out, F1, not_342_out);
  and and_52 (and_52_out, not_343_out, not_344_out, not_345_out, not_346_out, not_347_out, not_348_out, F5, not_349_out, F3, not_350_out, F1, F0);
  and and_53 (and_53_out, not_351_out, not_352_out, not_353_out, not_354_out, not_355_out, not_356_out, not_357_out, not_358_out, not_359_out, F2, not_360_out, not_361_out);
  and and_54 (and_54_out, not_362_out, not_363_out, not_364_out, not_365_out, not_366_out, not_367_out, F5, not_368_out, not_369_out, F2, F1, not_370_out);
  and and_55 (BEQ, not_371_out, not_372_out, not_373_out, OP2, not_374_out, not_375_out);
  and and_56 (BNE, not_376_out, not_377_out, not_378_out, OP2, not_379_out, OP0);
  and and_57 (JR, not_380_out, not_381_out, not_382_out, not_383_out, not_384_out, not_385_out, not_386_out, not_387_out, F3, not_388_out, not_389_out, not_390_out);
  and and_58 (and_58_out, not_391_out, not_392_out, not_393_out, not_394_out, not_395_out, not_396_out, not_397_out, not_398_out, F3, not_399_out, not_400_out, not_401_out);
  and and_59 (and_59_out, not_402_out, not_403_out, not_404_out, not_405_out, OP1, not_406_out);
  and and_60 (and_60_out, not_407_out, not_408_out, not_409_out, not_410_out, OP1, OP0);
  and and_61 (JAL, not_411_out, not_412_out, not_413_out, not_414_out, OP1, OP0);
  or or_1 (MemToReg, and_1_out, and_2_out);
  or or_2 (ALU_SRC, and_4_out, and_5_out, and_6_out, and_7_out, and_8_out, and_9_out, and_10_out, and_11_out);
  or or_3 (SignedExt, and_34_out, and_35_out, and_36_out, and_37_out, and_38_out, and_39_out, and_40_out, and_41_out);
  or or_4 (JMP, and_58_out, and_59_out, and_60_out);
  or or_5 (RegWrite, and_12_out, and_13_out, and_14_out, and_15_out, and_16_out, and_17_out, and_18_out, and_19_out, and_20_out, and_21_out, and_22_out, and_23_out, and_24_out, and_25_out, and_26_out, and_27_out, and_28_out, and_29_out, and_30_out, and_31_out, and_32_out);
  or or_6 (RegDst, and_42_out, and_43_out, and_44_out, and_45_out, and_46_out, and_47_out, and_48_out, and_49_out, and_50_out, and_51_out, and_52_out, and_53_out, and_54_out);
endmodule

// ALU
module MIPS_ALU (
  input  [4:0] shamt,
  input  [31:0] X,
  input  [31:0] Y,
  input  [3:0] AluOP,
  output Equal,
  output [31:0] Result,
  output [31:0] Result_2
);

  wire [0:0] comparator_1_lt, comparator_2_lt;
  wire [31:0] adder_1_out, AND_out, divider_1_out, divider_1_rem, multiplier_1_cout, multiplier_1_out,
       NOR_out, OR_out, shifter_1_out, shifter_2_out, shifter_3_out, subtractor_1_out, XOR_out;

  assign AND_out = X & Y;  // AND_Gate AND, 32 bits wide
  assign OR_out = X | Y;  // OR_Gate OR, 32 bits wide
  Shifter #(.width(32)) shifter_1 (.in(Y), .\dist (shamt), .out(shifter_1_out));
  Shifter #(.width(32), .shift("ar")) shifter_2 (.in(Y), .\dist (shamt), .out(shifter_2_out));
  Shifter #(.width(32), .shift("lr")) shifter_3 (.in(Y), .\dist (shamt), .out(shifter_3_out));
  Multiplier #(.width(32)) multiplier_1 (.a(X), .b(Y), .out(multiplier_1_out), .cout(multiplier_1_cout));  // open: cin
  Divider #(.width(32)) divider_1 (.a(X), .b(Y), .out(divider_1_out), .rem(divider_1_rem));  // open: upper
  Adder #(.width(32)) adder_1 (.a(X), .b(Y), .out(adder_1_out));  // open: cin, cout
  Subtractor #(.width(32)) subtractor_1 (.a(X), .b(Y), .out(subtractor_1_out));  // open: bin, bout
  assign XOR_out = X ^ Y;  // XOR_Gate XOR, 32 bits wide
  assign NOR_out = ~(X | Y);  // NOR_Gate NOR, 32 bits wide
  Comparator #(.width(32)) comparator_1 (.a(X), .b(Y), .eq(Equal), .lt(comparator_1_lt[0]));  // open: gt
  Comparator #(.width(32), .mode("unsigned")) comparator_2 (.a(X), .b(Y), .lt(comparator_2_lt[0]));  // open: gt, eq
  Multiplexer #(.select(4), .width(32), .enable("false")) multiplexer_1 (
    .in0(shifter_1_out), .in1(shifter_2_out), .in2(shifter_3_out), .in3(multiplier_1_out),
    .in4(divider_1_out), .in5(adder_1_out), .in6(subtractor_1_out), .in7(AND_out), .in8(OR_out),
    .in9(XOR_out), .in10(NOR_out), .in11({{31{1'b0}}, comparator_1_lt[0]}),
    .in12({{31{1'b0}}, comparator_2_lt[0]}), .in13({32{1'b0}}), .in14({32{1'b0}}), .in15({32{1'b0}}),
    .out(Result), .sel(AluOP));
  Multiplexer #(.select(4), .width(32), .enable("false")) multiplexer_2 (
    .in0({32{1'b0}}), .in1({32{1'b0}}), .in2({32{1'b0}}), .in3(multiplier_1_cout), .in4(divider_1_rem),
    .in5({32{1'b0}}), .in6({32{1'b0}}), .in7({32{1'b0}}), .in8({32{1'b0}}), .in9({32{1'b0}}),
    .in10({32{1'b0}}), .in11({32{1'b0}}), .in12({32{1'b0}}), .in13({32{1'b0}}), .in14({32{1'b0}}),
    .in15({32{1'b0}}), .out(Result_2), .sel(AluOP));

  // Other names for the same wires on the sheet: Result2[31:0] = Result_2; S[3:0] = AluOP

  // Notes on the sheet:
  //   不要改变此引脚区域内容，也不要改变ALU封装形式
  //   输入引脚
  //   输出引脚
endmodule

module MIPS_Regifile (
  input  [31:0] Din,
  input  Clk,
  input  WE,
  input  [4:0] R1_num,
  input  [4:0] W_num,
  input  [4:0] R2_num,
  output [31:0] R1,
  output [31:0] R2
);

  // RegisterFile registerfile_1: pin names not known; wires that end beside it: Din, Clk, WE, W_num, R1_num, R2_num, R1, R2
endmodule

module \_4控制信号生成  (
  input  OP0,
  input  OP1,
  input  OP2,
  input  OP3,
  input  OP4,
  input  OP5,
  input  F0,
  input  F1,
  input  F2,
  input  F3,
  input  F4,
  input  F5,
  output SLLV,
  output LB,
  output BLTZ
);

  wire not_1_out, not_2_out, not_3_out, not_4_out, not_5_out, not_6_out, not_7_out, not_8_out, not_9_out,
       not_10_out, not_11_out, not_12_out, not_13_out, not_14_out, not_15_out, not_16_out, not_17_out,
       not_18_out, not_19_out, not_20_out, not_21_out;

  not not_1 (not_1_out, OP5);
  not not_2 (not_2_out, OP4);
  not not_3 (not_3_out, OP3);
  not not_4 (not_4_out, OP2);
  not not_5 (not_5_out, OP1);
  not not_6 (not_6_out, OP0);
  not not_7 (not_7_out, F5);
  not not_8 (not_8_out, F4);
  not not_9 (not_9_out, F3);
  not not_10 (not_10_out, F1);
  not not_11 (not_11_out, F0);
  not not_12 (not_12_out, OP4);
  not not_13 (not_13_out, OP3);
  not not_14 (not_14_out, OP2);
  not not_15 (not_15_out, OP1);
  not not_16 (not_16_out, OP0);
  not not_17 (not_17_out, OP5);
  not not_18 (not_18_out, OP4);
  not not_19 (not_19_out, OP3);
  not not_20 (not_20_out, OP2);
  not not_21 (not_21_out, OP1);
  and and_1 (SLLV, not_1_out, not_2_out, not_3_out, not_4_out, not_5_out, not_6_out, not_7_out, not_8_out, not_9_out, F2, not_10_out, not_11_out);
  and and_2 (LB, OP5, not_12_out, not_13_out, not_14_out, not_15_out, not_16_out);
  and and_3 (BLTZ, not_17_out, not_18_out, not_19_out, not_20_out, not_21_out, OP0);
endmodule

module \单周期单级中断  (
);

  wire and_1_out, and_2_out, and_3_out, and_4_out, and_5_out, and_6_out, and_8_out, and_9_out, and_10_out,
       BLTZ, BLTZ_SIGN, CLK, comparator_2_eq, comparator_3_eq, comparator_4_lt, d_ff_1_q, d_ff_2_q, d_ff_3_q,
       d_ff_4_q, decoder_1_out1, decoder_1_out2, decoder_1_out3, ERET, Go, IE_q, IR1, IR1_q, IR2, IR2_q, IR3,
       IR3_q, IR_CPU, JAL, LB, mips_alu_1_equal, multiplexer_2_out, not_1_out, not_2_out, not_3_out,
       not_4_out, or_1_out, or_5_out, or_6_out, or_7_out, or_8_out, priority_encoder_1_gs, RST, RST1, RST2,
       RST3, SignedExt, SLLV, Syscall, syscall_equal, W1, W2, W3, \硬布线控制器_1_alu_src , \硬布线控制器_1_beq ,
       \硬布线控制器_1_bne , \硬布线控制器_1_jmp , \硬布线控制器_1_jr , \硬布线控制器_1_memtoreg , \硬布线控制器_1_memwrite ,
       \硬布线控制器_1_regdst , \硬布线控制器_1_regwrite ;
  wire [1:0] EPC_2_q, mips_alu_1_result, priority_encoder_1_out;
  wire [3:0] \硬布线控制器_1_alu_op ;
  wire [4:0] multiplexer_8_out, multiplexer_9_out, multiplexer_10_out, multiplexer_12_out,
       multiplexer_15_out, rom_1_data;
  wire [5:0] FUNC, OP;
  wire [7:0] multiplexer_19_out;
  wire [9:0] mips_alu_1_result_2;
  wire [15:0] \总周期数 , \无条件分支数 , \条件分支成功数 ;
  wire [25:11] rom_1_data_2;
  wire [27:0] shifter_1_out;
  wire [31:0] adder_1_out, adder_2_out, bit_extender_1_out, bit_extender_2_out, bit_extender_3_out, BLTZ_PC,
       BLTZ_RS, epc, LedData, multiplexer_1_out, multiplexer_3_out, multiplexer_4_out, multiplexer_5_out,
       multiplexer_6_out, multiplexer_7_out, multiplexer_11_out, multiplexer_13_out, multiplexer_14_out,
       multiplexer_17_out, multiplexer_18_out, PC, ram_1_data, realpc, shifter_2_out, shifter_3_out, show;
  wire [31:12] mips_alu_1_result_3;

  Button \u_总复位  (.out(RST));
  Button _1 (.out(IR1));
  Button _2 (.out(IR2));
  Button _3 (.out(IR3));
  Button \u_继续运行  (.out(Go));
  LED led_1 (.in(W1));
  LED led_2 (.in(W2));
  LED led_3 (.in(W3));
  or or_1 (or_1_out, JAL, \硬布线控制器_1_jmp );
  Multiplexer #(.width(32), .enable("false")) multiplexer_1 (
    .in0(adder_1_out), .in1(adder_2_out), .out(multiplexer_1_out), .sel(or_8_out));
  Multiplexer #(.enable("false")) multiplexer_2 (.in0(1'b1), .in1(Go), .out(multiplexer_2_out), .sel(and_1_out));
  Hex_Digit_Display hex_digit_display_1 (.value(LedData[31:28]));  // open: dp
  Multiplexer #(.width(32), .enable("false")) multiplexer_3 (
    .in0(multiplexer_1_out), .in1({PC[31:28], shifter_1_out}), .out(multiplexer_3_out), .sel(or_1_out));
  Multiplexer #(.width(32), .enable("false")) multiplexer_4 (
    .in0(multiplexer_3_out), .in1(BLTZ_RS), .out(multiplexer_4_out), .sel(\硬布线控制器_1_jr ));
  Register #(.width(32)) u_PC (.D(multiplexer_7_out), .en(multiplexer_2_out), .Q(PC), .clk(CLK));  // open: clr
  Counter #(.width(16), .max('hffff)) counter_1 (
    .count(multiplexer_2_out), .Q(\总周期数 ), .clk(CLK), .clr(RST));  // open: load, D, carry
  Hex_Digit_Display hex_digit_display_2 (.value(LedData[27:24]));  // open: dp
  Hex_Digit_Display hex_digit_display_3 (.value(LedData[23:20]));  // open: dp
  Counter #(.width(16), .max('hffff)) counter_2 (
    .count(\硬布线控制器_1_jmp ), .Q(\无条件分支数 ), .clk(CLK), .clr(RST));  // open: load, D, carry
  Multiplexer #(.width(32), .enable("false")) multiplexer_5 (
    .in0(multiplexer_4_out), .in1(BLTZ_PC), .out(multiplexer_5_out), .sel(BLTZ_SIGN));
  Multiplexer #(.width(32), .enable("false")) multiplexer_6 (
    .in0(multiplexer_5_out), .in1(realpc), .out(multiplexer_6_out), .sel(IR_CPU));
  Hex_Digit_Display hex_digit_display_4 (.value(LedData[15:12]));  // open: dp
  Hex_Digit_Display hex_digit_display_5 (.value(LedData[19:16]));  // open: dp
  Adder #(.width(32)) adder_1 (.a(PC), .b(32'h4), .out(adder_1_out));  // open: cin, cout
  Multiplexer #(.width(32), .enable("false")) multiplexer_7 (
    .in0(multiplexer_6_out), .in1(epc), .out(multiplexer_7_out), .sel(ERET));
  or or_2 (W1, IR1_q, d_ff_1_q);
  or or_3 (W2, IR2_q, d_ff_2_q);
  or or_4 (W3, IR3_q, d_ff_3_q);
  Hex_Digit_Display hex_digit_display_6 (.value(LedData[7:4]));  // open: dp
  Hex_Digit_Display hex_digit_display_7 (.value(LedData[11:8]));  // open: dp
  Clock clock_1 (.out(CLK));
  ROM #(.addrWidth(10), .dataWidth(32)) rom_1 (
    .addr(PC[11:2]), .data({OP, rom_1_data_2, rom_1_data, FUNC}));  // open: sel
  D_Flip_Flop d_ff_1 (.clk(IR1), .D(1'b1), .Q(d_ff_1_q), .reset(IR1_q));  // open: Qn, preset, en
  D_Flip_Flop d_ff_2 (.clk(IR2), .D(1'b1), .Q(d_ff_2_q), .reset(IR2_q));  // open: Qn, preset, en
  D_Flip_Flop d_ff_3 (.clk(IR3), .D(1'b1), .Q(d_ff_3_q), .reset(IR3_q));  // open: Qn, preset, en
  Hex_Digit_Display hex_digit_display_8 (.value(LedData[3:0]));  // open: dp
  or or_5 (or_5_out, d_ff_1_q, IR1_q);
  or or_6 (or_6_out, d_ff_2_q, IR2_q);
  or or_7 (or_7_out, d_ff_3_q, IR3_q);
  \硬布线控制器  \u_硬布线控制器_1  (
    .Func(FUNC), .OP(OP), .ALU_OP(\硬布线控制器_1_alu_op ), .MemToReg(\硬布线控制器_1_memtoreg ),
    .MemWrite(\硬布线控制器_1_memwrite ), .ALU_SRC(\硬布线控制器_1_alu_src ), .RegWrite(\硬布线控制器_1_regwrite ),
    .SysCALL(Syscall), .SignedExt(SignedExt), .RegDst(\硬布线控制器_1_regdst ), .JR(\硬布线控制器_1_jr ),
    .JMP(\硬布线控制器_1_jmp ), .Beq(\硬布线控制器_1_beq ), .JAL(JAL), .Bne(\硬布线控制器_1_bne ), .SLLV(SLLV), .LB(LB),
    .BLTZ(BLTZ));
  Multiplexer #(.width(5), .enable("false")) multiplexer_8 (
    .in0(rom_1_data_2[25:21]), .in1(5'b00010), .out(multiplexer_8_out), .sel(Syscall));
  Multiplexer #(.width(5), .enable("false")) multiplexer_9 (
    .in0(rom_1_data_2[20:16]), .in1(5'b00100), .out(multiplexer_9_out), .sel(Syscall));
  Multiplexer #(.width(5), .enable("false")) multiplexer_10 (
    .in0(rom_1_data_2[20:16]), .in1(rom_1_data_2[15:11]), .out(multiplexer_10_out), .sel(\硬布线控制器_1_regdst ));
  Multiplexer #(.width(32), .enable("false")) multiplexer_11 (
    .in0(multiplexer_18_out), .in1(adder_1_out), .out(multiplexer_11_out), .sel(JAL));
  assign bit_extender_1_out = {{16{1'b0}}, {rom_1_data_2[15:11], rom_1_data, FUNC}};  // Bit_Extender bit_extender_1
  assign bit_extender_2_out = {{16{rom_1_data_2[15]}}, {rom_1_data_2[15:11], rom_1_data, FUNC}};  // Bit_Extender bit_extender_2
  Shifter #(.width(28)) shifter_1 (
    .in({OP[1:0], rom_1_data_2, rom_1_data, FUNC}), .\dist (5'b00010), .out(shifter_1_out));
  and and_1 (and_1_out, Syscall, not_1_out);
  and and_2 (and_2_out, or_5_out, ~RST1);  // AND_Gate
  Multiplexer #(.width(5), .enable("false")) multiplexer_12 (
    .in0(multiplexer_10_out), .in1({5{1'b1}}), .out(multiplexer_12_out), .sel(JAL));
  Multiplexer #(.width(32), .enable("false")) multiplexer_13 (
    .in0(bit_extender_1_out), .in1(bit_extender_2_out), .out(multiplexer_13_out), .sel(SignedExt));
  not not_1 (not_1_out, syscall_equal);
  D_Flip_Flop u_IR1 (.clk(CLK), .D(and_2_out), .Q(IR1_q));  // open: Qn, preset, en, reset
  D_Flip_Flop u_IR2 (.clk(CLK), .D(and_3_out), .Q(IR2_q));  // open: Qn, preset, en, reset
  and and_3 (and_3_out, or_6_out, ~RST2);  // AND_Gate
  D_Flip_Flop u_IR3 (.clk(CLK), .D(and_4_out), .Q(IR3_q));  // open: Qn, preset, en, reset
  and and_4 (and_4_out, or_7_out, ~RST3);  // AND_Gate
  MIPS_Regifile mips_regifile_1 (
    .Din(multiplexer_11_out), .Clk(CLK), .R1(BLTZ_RS), .R2(show), .WE(\硬布线控制器_1_regwrite ),
    .W_num(multiplexer_12_out), .R1_num(multiplexer_8_out), .R2_num(multiplexer_9_out));
  Shifter #(.width(32)) shifter_2 (.in(multiplexer_13_out), .\dist (5'b00010), .out(shifter_2_out));
  Comparator #(.width(32)) comparator_1 (.a(BLTZ_RS), .b(32'h22), .eq(syscall_equal));  // open: gt, lt
  and and_5 (and_5_out, \硬布线控制器_1_beq , mips_alu_1_equal);
  Multiplexer #(.width(32), .enable("false")) multiplexer_14 (
    .in0(show), .in1(multiplexer_13_out), .out(multiplexer_14_out), .sel(\硬布线控制器_1_alu_src ));
  Adder #(.width(32)) adder_2 (.a(shifter_2_out), .b(adder_1_out), .out(adder_2_out));  // open: cin, cout
  Shifter #(.width(32)) shifter_3 (.in(multiplexer_13_out), .\dist (5'b00010), .out(shifter_3_out));
  Priority_Encoder #(.select(2)) priority_encoder_1 (
    .in0(1'b0), .in1(IR1_q), .in2(IR2_q), .in3(IR3_q), .out(priority_encoder_1_out),
    .gs(priority_encoder_1_gs));  // open: en_out, en_in
  Comparator #(.width(6)) comparator_2 (.a(OP), .b(6'b010000), .eq(comparator_2_eq));  // open: gt, lt
  Comparator #(.width(6)) comparator_3 (.a(6'b011000), .b(FUNC), .eq(comparator_3_eq));  // open: gt, lt
  or or_8 (or_8_out, and_5_out, and_6_out);
  and and_6 (and_6_out, \硬布线控制器_1_bne , not_2_out);
  not not_2 (not_2_out, mips_alu_1_equal);
  MIPS_ALU mips_alu_1 (
    .X(BLTZ_RS), .Y(multiplexer_14_out), .AluOP(\硬布线控制器_1_alu_op ), .Equal(mips_alu_1_equal),
    .Result({mips_alu_1_result_3, mips_alu_1_result_2, mips_alu_1_result}), .shamt(multiplexer_15_out));  // open: Result_2
  Multiplexer #(.width(5), .enable("false")) multiplexer_15 (
    .in0(rom_1_data), .in1(BLTZ_RS[4:0]), .out(multiplexer_15_out), .sel(SLLV));
  Multiplexer #(.select(2), .width(32), .enable("false")) multiplexer_16 (
    .in1(32'h4), .in2(32'h68), .in3(32'hcc), .out(realpc), .sel(priority_encoder_1_out));  // open: in0
  and and_7 (ERET, comparator_2_eq, comparator_3_eq);
  not not_3 (not_3_out, ERET);
  Counter #(.width(16), .max('hffff)) counter_3 (
    .count(or_8_out), .Q(\条件分支成功数 ), .clk(CLK), .clr(RST));  // open: load, D, carry
  Adder #(.width(32)) adder_3 (.a(shifter_3_out), .b(adder_1_out), .out(BLTZ_PC));  // open: cin, cout
  Register #(.width(32)) u_EPC (.D(PC), .en(and_8_out), .Q(epc), .clk(CLK));  // open: clr
  and and_8 (and_8_out, not_3_out, IR_CPU);
  Comparator #(.width(32)) comparator_4 (.a(BLTZ_RS), .b({32{1'b0}}), .lt(comparator_4_lt));  // open: gt, eq
  and and_9 (and_9_out, not_3_out, d_ff_4_q);
  D_Flip_Flop d_ff_4 (.clk(CLK), .D(and_8_out), .Q(d_ff_4_q), .en(IR_CPU));  // open: Qn, preset, reset
  Register #(.width(32)) register_1 (.D(show), .Q(LedData), .clk(and_10_out));  // open: en, clr
  and and_10 (and_10_out, Syscall, syscall_equal);
  RAM #(.addrWidth(10), .dataWidth(32), .bus("separate")) ram_1 (
    .addr(mips_alu_1_result_2), .din(show), .data(ram_1_data), .str(\硬布线控制器_1_memwrite ), .clk(CLK));  // open: sel, ld, clr
  and and_11 (BLTZ_SIGN, comparator_4_lt, BLTZ);
  D_Flip_Flop IE (.clk(CLK), .D(1'b1), .Q(IE_q), .preset(ERET), .en(not_4_out), .reset(and_9_out));  // open: Qn
  not not_4 (not_4_out, IE_q);
  Multiplexer #(.width(32), .enable("false")) multiplexer_17 (
    .in0({mips_alu_1_result_3, mips_alu_1_result_2, mips_alu_1_result}), .in1(ram_1_data),
    .out(multiplexer_17_out), .sel(\硬布线控制器_1_memtoreg ));
  Multiplexer #(.width(32), .enable("false")) multiplexer_18 (
    .in0(multiplexer_17_out), .in1(bit_extender_3_out), .out(multiplexer_18_out), .sel(LB));
  Decoder #(.select(2), .enable("false")) decoder_1 (
    .out1(decoder_1_out1), .out2(decoder_1_out2), .out3(decoder_1_out3), .sel(EPC_2_q));  // open: out0
  Register #(.width(2)) EPC_2 (.D(priority_encoder_1_out), .Q(EPC_2_q), .clk(and_8_out));  // open: en, clr
  and and_12 (IR_CPU, priority_encoder_1_gs, IE_q);
  Multiplexer #(.select(2), .width(8), .enable("false")) multiplexer_19 (
    .in0(multiplexer_17_out[7:0]), .in1(multiplexer_17_out[15:8]), .in2(multiplexer_17_out[23:16]),
    .in3(multiplexer_17_out[31:24]), .out(multiplexer_19_out), .sel(mips_alu_1_result));
  assign bit_extender_3_out = {{24{multiplexer_19_out[7]}}, multiplexer_19_out};  // Bit_Extender bit_extender_3
  and and_13 (RST1, ERET, decoder_1_out1);
  and and_14 (RST2, decoder_1_out2, ERET);
  and and_15 (RST3, decoder_1_out3, ERET);

  // Other names for the same wires on the sheet: JR_PC[31:0] = BLTZ_RS; SLLV_RS[31:0] = BLTZ_RS;
  //   syscall_num[31:0] = BLTZ_RS

  // Notes on the sheet:
  //   中断源
  //   中断等待指示
  //   1号中断
  //   1号中断等待指示灯
  //   2号中断
  //   2号中断等待指示灯
  //   3号中断
  //   3号中断等待指示灯
  //   数码管输出
  //   指令存储器
  //   OP
  //   rs
  //   指令字
  //   contents of rom_1 (hex, n*v repeats v):
  //   20110001 8100005 20110001 20120002 20130003 8100009 20110001 20120002 20130003 810000d 20110001
  //   20120002 20130003 8100011 20110001 20120002 20130003 c1000f8 20100001 20110001 118fc0 112020
  //   20020022 c 118882 12200001 8100015 112020 20020022 c 20110001 118880 112020 20020022 c 12200001
  //   810001f 20110001 118fc0 112020 20020022 c 1188c3 112020 20020022 c 118903 112020 20020022 c 118903
  //   112020 20020022 c 118903 112020 20020022 c 118903 112020 20020022 c 118903 112020 20020022 c 118903
  //   112020 20020022 c 118903 112020 20020022 c 20100001 109fc0 139fc3 8021 2012000c 24160003 26100001
  //   3210000f 20080008 20090001 139900 2709825 132020 20020022 c 1094022 1500fff9 22100001 2018000f
  //   2188024 108700 20080008 20090001 139902 2709825 132021 20020022 c 1094022 1500fff9 108702 2c9b022
  //   12c00001 8100050 4020 1084027 84400 3508ffff 82021 20020022 c 2010ffff 20110000 ae300000 22100001
  //   22310004 ae300000 22100001 22310004 ae300000 22100001 22310004 ae300000 22100001 22310004 ae300000
  //   22100001 22310004 ae300000 22100001 22310004 ae300000 22100001 22310004 ae300000 22100001 22310004
  //   ae300000 22100001 22310004 ae300000 22100001 22310004 ae300000 22100001 22310004 ae300000 22100001
  //   22310004 ae300000 22100001 22310004 ae300000 22100001 22310004 ae300000 22100001 22310004 ae300000
  //   22100001 22310004 22100001 8020 2011003c 8e130000 8e340000 274402a 11000002 ae330000 ae140000
  //   2231fffc 1611fff8 102020 20020022 c 22100004 2011003c 1611fff2 20020032 c 20080001 20090003 20110876
  //   112020 20020022 c 200b0008 1118804 1318804 112020 20020022 c 216bffff 1560fff9 2002000a c 2008ffff
  //   20117777 112020 20020022 c 200b0010 2288826 112020 20020022 c 216bffff 1560fffa 2002000a c 20090000
  //   200b0010 34118483 20120404 118c00 129400 36318281 22520404 ad310000 2328820 21290004 216bffff
  //   1560fffb 200b0020 20090000 81310000 112020 20020022 c 21290001 216bffff 1560fff9 2002000a c 2011fff1
  //   112020 20020022 c 22310001 620fffb 2002000a c 2002000a c 20100000 22100001 102020 20020022 c
  //   22100002 102020 20020022 c 22100003 102020 20020022 c 22100004 102020 20020022 c 22100005 102020
  //   20020022 c 22100006 102020 20020022 c 22100007 102020 20020022 c 22100008 102020 20020022 20020022 c
  //   3e00008
  //   rt
  //   rd
  //   中断信号采样电路
  //   JMP
  //   JR
  //   OP
  //   Func
  //   Func
  //   同步清零信号
  //   同步清零信号
  //   同步清零信号
  //   Beq
  //   Bne
  //   MemToReg
  //   MemWrite
  //   AluOP
  //   AluSrcB
  //   RegWrite
  //   JAL
  //   RegDst
  //   Syscall
  //   Reset
  //   Reset
  //   Reset
  //   与中断屏蔽位与
  //   与中断屏蔽位与
  //   与中断屏蔽位与
endmodule
