// Logisim project main.circ as structural Verilog: 21 circuits, main circuit ◇单周期MIPS
module \单周期MIPS  (
  input  IR1,
  input  IR2,
  input  IR3,
  output RegWrite,
  output MemWrite,
  output [31:0] PC,
  output [31:0] IR,
  output [31:0] RDin,
  output [31:0] MDin,
  output [31:0] LedData
);

  wire and_1_out, and_2_out, and_4_out, and_5_out, BGEZ, BGEZ_SIGN, CLK, comparator_1_lt, CONDI, equal, Go,
       IR1_t, IR2_t, IR3_t, IRA, IRB, IRC, LB, multiplexer_3_out, not_1_out, not_2_out, not_equal, SignedExt,
       Syscall, UNCONDI, W1, W2, W3, \单周期硬布线控制器_1_alu_src , \单周期硬布线控制器_1_beq , \单周期硬布线控制器_1_bne ,
       \单周期硬布线控制器_1_jal , \单周期硬布线控制器_1_memtoreg , \单周期硬布线控制器_1_regdst ;
  wire [0:0] \单周期硬布线控制器_1_jr ;
  wire [3:0] \单周期硬布线控制器_1_alu_op ;
  wire [4:0] multiplexer_5_out, multiplexer_6_out, multiplexer_8_out, multiplexer_9_out;
  wire [7:0] multiplexer_14_out, multiplexer_15_out;
  wire [15:0] \总周期数 , \无条件分支数 , \条件分支成功数 ;
  wire [27:0] adder_1_out;
  wire [31:0] adder_2_out, BGEZ_PC, BGEZ_RS, bit_extender_1_out, bit_extender_2_out, bit_extender_3_out,
       mips_alu_1_result, multiplexer_1_out, multiplexer_2_out, multiplexer_4_out, multiplexer_7_out,
       multiplexer_11_out, multiplexer_12_out, multiplexer_13_out, PC_q, ram_1_data, shifter_1_out,
       shifter_2_out, shifter_3_out;
  wire [31:8] multiplexer_14_out_2;

  Clock clock_1 (.out(CLK));
  Button _1 (.out(IRA));
  Button _2 (.out(IRB));
  Button _3 (.out(IRC));
  or or_1 (CONDI, and_4_out, and_2_out);
  Button \u_继续运行  (.out(Go));
  LED led_1 (.in(W1));
  LED led_2 (.in(W2));
  LED led_3 (.in(W3));
  Multiplexer #(.width(32), .enable("false")) multiplexer_1 (
    .in0({shifter_1_out[31:28], adder_1_out}), .in1(adder_2_out), .out(multiplexer_1_out), .sel(CONDI));
  Hex_Digit_Display hex_digit_display_1 (.value(LedData[31:28]));  // open: dp
  Multiplexer #(.select(2), .width(32), .enable("false")) multiplexer_2 (
    .in0(multiplexer_1_out), .in1(BGEZ_RS), .in2(shifter_1_out), .in3(BGEZ_RS), .out(multiplexer_2_out),
    .sel({UNCONDI, \单周期硬布线控制器_1_jr [0]}));
  Multiplexer #(.enable("false")) multiplexer_3 (.in0(1'b1), .in1(Go), .out(multiplexer_3_out), .sel(and_1_out));
  Hex_Digit_Display hex_digit_display_2 (.value(LedData[23:20]));  // open: dp
  Hex_Digit_Display hex_digit_display_3 (.value(LedData[27:24]));  // open: dp
  Multiplexer #(.width(32), .enable("false")) multiplexer_4 (
    .in0(multiplexer_2_out), .in1(BGEZ_PC), .out(multiplexer_4_out), .sel(BGEZ_SIGN));
  Register #(.width(32)) u_PC (.D(multiplexer_4_out), .en(multiplexer_3_out), .Q(PC_q), .clk(CLK), .clr(1'b0));
  Counter #(.width(16), .max('hffff)) counter_1 (
    .load(1'b0), .count(multiplexer_3_out), .Q(\总周期数 ), .clk(CLK), .clr(1'b0));  // open: D, carry
  Hex_Digit_Display hex_digit_display_4 (.value(LedData[19:16]));  // open: dp
  Hex_Digit_Display hex_digit_display_5 (.value(LedData[15:12]));  // open: dp
  PC_JUDGE pc_judge_1 (.PC_raw32b(PC_q), .PC_judge(PC));
  Adder #(.width(32)) adder_1 (.a(PC_q), .b(32'h4), .out({shifter_1_out[31:28], adder_1_out}));  // open: cin, cout
  and and_1 (and_1_out, Syscall, not_equal);
  Hex_Digit_Display hex_digit_display_6 (.value(LedData[11:8]));  // open: dp
  Hex_Digit_Display hex_digit_display_7 (.value(LedData[7:4]));  // open: dp
  // Probe on \总周期数 
  // Mips_Probe mips_probe_1: pin names not known; wires that end beside it: IR
  ROM #(.addrWidth(10), .dataWidth(32)) rom_1 (.addr(PC_q[11:2]), .data(IR));  // open: sel
  Hex_Digit_Display hex_digit_display_8 (.value(LedData[3:0]));  // open: dp
  assign bit_extender_1_out = {{16{1'b0}}, IR[15:0]};  // Bit_Extender bit_extender_1
  assign bit_extender_2_out = {{16{IR[15]}}, IR[15:0]};  // Bit_Extender bit_extender_2
  or or_2 (IR1_t, IR1, IRA);
  \单周期硬布线控制器  \u_单周期硬布线控制器_1  (
    .Func(IR[5:0]), .OP(IR[31:26]), .ALU_OP(\单周期硬布线控制器_1_alu_op ), .MemToReg(\单周期硬布线控制器_1_memtoreg ),
    .MemWrite(MemWrite), .ALU_SRC(\单周期硬布线控制器_1_alu_src ), .RegWrite(RegWrite), .SysCALL(Syscall),
    .SignedExt(SignedExt), .RegDst(\单周期硬布线控制器_1_regdst ), .JR(\单周期硬布线控制器_1_jr [0]), .JMP(UNCONDI),
    .Beq(\单周期硬布线控制器_1_beq ), .JAL(\单周期硬布线控制器_1_jal ), .Bne(\单周期硬布线控制器_1_bne ), .LB(LB), .BGEZ(BGEZ));
  Multiplexer #(.width(5), .enable("false")) multiplexer_5 (
    .in0(IR[25:21]), .in1(5'b00010), .out(multiplexer_5_out), .sel(Syscall));
  Multiplexer #(.width(5), .enable("false")) multiplexer_6 (
    .in0(IR[20:16]), .in1(IR[15:11]), .out(multiplexer_6_out), .sel(\单周期硬布线控制器_1_regdst ));
  Multiplexer #(.width(32), .enable("false")) multiplexer_7 (
    .in0(bit_extender_1_out), .in1(bit_extender_2_out), .out(multiplexer_7_out), .sel(SignedExt));
  Shifter #(.width(28)) shifter_1 (.in(IR[27:0]), .\dist (5'b00010), .out(shifter_1_out[27:0]));
  Comparator #(.width(32)) comparator_1 (.a(BGEZ_RS), .b({32{1'b0}}), .lt(comparator_1_lt));  // open: gt, eq
  and and_2 (and_2_out, \单周期硬布线控制器_1_beq , equal);
  Multiplexer #(.width(5), .enable("false")) multiplexer_8 (
    .in0(IR[20:16]), .in1(5'b00100), .out(multiplexer_8_out), .sel(Syscall));
  Multiplexer #(.width(5), .enable("false")) multiplexer_9 (
    .in0(multiplexer_6_out), .in1({5{1'b1}}), .out(multiplexer_9_out), .sel(\单周期硬布线控制器_1_jal ));
  Multiplexer #(.width(32), .enable("false")) multiplexer_10 (
    .in0(multiplexer_13_out), .in1({shifter_1_out[31:28], adder_1_out}), .out(RDin), .sel(\单周期硬布线控制器_1_jal ));
  not not_1 (not_1_out, comparator_1_lt);
  or or_3 (IR2_t, IR2, IRB);
  and and_3 (BGEZ_SIGN, not_1_out, BGEZ);
  and and_4 (and_4_out, \单周期硬布线控制器_1_bne , not_2_out);
  not not_2 (not_2_out, equal);
  MIPS_Regifile mips_regifile_1 (
    .Din(RDin), .Clk(CLK), .R1(BGEZ_RS), .R2(MDin), .WE(RegWrite), .W_num(multiplexer_9_out),
    .R1_num(multiplexer_5_out), .R2_num(multiplexer_8_out));
  or or_4 (IR3_t, IR3, IRC);
  Multiplexer #(.width(32), .enable("false")) multiplexer_11 (
    .in0(MDin), .in1(multiplexer_7_out), .out(multiplexer_11_out), .sel(\单周期硬布线控制器_1_alu_src ));
  Shifter #(.width(32)) shifter_2 (.in(multiplexer_7_out), .\dist (5'b00010), .out(shifter_2_out));
  Shifter #(.width(32)) shifter_3 (.in(multiplexer_7_out), .\dist (5'b00010), .out(shifter_3_out));
  Counter #(.width(16), .max('hffff)) counter_2 (
    .load(1'b0), .count(CONDI), .Q(\条件分支成功数 ), .clk(CLK), .clr(1'b0));  // open: D, carry
  and and_5 (and_5_out, equal, Syscall);
  not not_3 (not_equal, equal);
  MIPS_ALU mips_alu_1 (
    .X(BGEZ_RS), .Y(multiplexer_12_out), .AluOP(\单周期硬布线控制器_1_alu_op ), .Equal(equal),
    .Result(mips_alu_1_result), .shamt(IR[10:6]));  // open: Result_2
  Multiplexer #(.width(32), .enable("false")) multiplexer_12 (
    .in0(multiplexer_11_out), .in1(32'h22), .out(multiplexer_12_out), .sel(Syscall));
  Adder #(.width(32)) adder_2 (
    .a(shifter_2_out), .b({shifter_1_out[31:28], adder_1_out}), .out(adder_2_out));  // open: cin, cout
  Adder #(.width(32)) adder_3 (
    .a(shifter_3_out), .b({shifter_1_out[31:28], adder_1_out}), .out(BGEZ_PC));  // open: cin, cout
  Register #(.width(32)) register_1 (.D(MDin), .en(and_5_out), .Q(LedData), .clk(CLK), .clr(1'b0));
  Multiplexer #(.width(32), .enable("false")) multiplexer_13 (
    .in0({multiplexer_14_out_2, multiplexer_14_out}), .in1(bit_extender_3_out), .out(multiplexer_13_out),
    .sel(LB));
  Counter #(.width(16), .max('hffff)) counter_3 (
    .load(1'b0), .count(UNCONDI), .Q(\无条件分支数 ), .clk(CLK), .clr(1'b0));  // open: D, carry
  RAM #(.addrWidth(10), .dataWidth(32), .bus("separate")) ram_1 (
    .addr(mips_alu_1_result[11:2]), .din(MDin), .data(ram_1_data), .str(MemWrite), .clk(CLK), .clr(1'b0));  // open: sel, ld
  Multiplexer #(.width(32), .enable("false")) multiplexer_14 (
    .in0(mips_alu_1_result), .in1(ram_1_data), .out({multiplexer_14_out_2, multiplexer_14_out}),
    .sel(\单周期硬布线控制器_1_memtoreg ));
  Multiplexer #(.select(2), .width(8), .enable("false")) multiplexer_15 (
    .in0(multiplexer_14_out), .in1(multiplexer_14_out_2[15:8]), .in2(multiplexer_14_out_2[23:16]),
    .in3(multiplexer_14_out_2[31:24]), .out(multiplexer_15_out), .sel(mips_alu_1_result[1:0]));
  assign bit_extender_3_out = {{24{multiplexer_15_out[7]}}, multiplexer_15_out};  // Bit_Extender bit_extender_3

  // Other names for the same wires on the sheet: SHMAT[4:0] = IR[10:6]; PC_judge[31:0] = PC; R1[31:0] = BGEZ_RS;
  //   R2[31:0] = MDin

  // Notes on the sheet:
  //   中断源
  //   中断等待指示
  //   总复位信号应将除ROM以外所有存储组件全部清零
  //   数码管输出
  //   指令存储器
  //   数码管输出应该用寄存器锁存，否则显示数据只能一闪而过
  //   OP
  //   指令字
  //   contents of rom_1 (hex, n*v repeats v):
  //   20110001 8000c05 20110001 20120002 20130003 8000c09 20110001 20120002 20130003 8000c0d 20110001
  //   20120002 20130003 8000c11 20110001 20120002 20130003 c000cb8 20100001 20110001 118fc0 112020
  //   20020022 c 118882 12200001 8000c15 112020 20020022 c 20110001 118880 112020 20020022 c 12200001
  //   8000c1f 20110001 118fc0 112020 20020022 c 1188c3 112020 20020022 c 118903 112020 20020022 c 118903
  //   112020 20020022 c 118903 112020 20020022 c 118903 112020 20020022 c 118903 112020 20020022 c 118903
  //   112020 20020022 c 118903 112020 20020022 c 20100001 109fc0 139fc3 8021 2012000c 24160003 26100001
  //   3210000f 20080008 20090001 139900 2709825 132020 20020022 c 1094022 1500fff9 22100001 2018000f
  //   2188024 108700 20080008 20090001 139902 2709825 132021 20020022 c 1094022 1500fff9 108702 2c9b022
  //   12c00001 8000c50 4020 1084027 84400 3508ffff 82021 20020022 c 2010ffff 20110000 ae300000 22100001
  //   22310004 ae300000 22100001 22310004 ae300000 22100001 22310004 ae300000 22100001 22310004 ae300000
  //   22100001 22310004 ae300000 22100001 22310004 ae300000 22100001 22310004 ae300000 22100001 22310004
  //   ae300000 22100001 22310004 ae300000 22100001 22310004 ae300000 22100001 22310004 ae300000 22100001
  //   22310004 ae300000 22100001 22310004 ae300000 22100001 22310004 ae300000 22100001 22310004 ae300000
  //   22100001 22310004 22100001 8020 2011003c 8e130000 8e340000 274402a 11000002 ae330000 ae140000
  //   2231fffc 1611fff8 102020 20020022 c 22100004 2011003c 1611fff2 20020032 c 20100000 22100001 102020
  //   20020022 c 22100002 102020 20020022 c 22100003 102020 20020022 c 22100004 102020 20020022 c 22100005
  //   102020 20020022 c 22100006 102020 20020022 c 22100007 102020 20020022 c 22100008 102020 20020022
  //   20020022 c 3e00008
  //   JMP
  //   JR
  //   OP
  //   Func
  //   Func
  //   rs
  //   rt
  //   rd
  //   Beq
  //   Bne
  //   MemToReg
  //   MemWrite
  //   AluOP
  //   AluSrcB
  //   RegWrite
  //   JAL
  //   RegDst
  //   Syscall
endmodule

// 单周期硬布线控制器
module \单周期硬布线控制器  (
  input  [5:0] OP,
  input  [5:0] Func,
  output [3:0] ALU_OP,
  output MemToReg,
  output MemWrite,
  output ALU_SRC,
  output RegWrite,
  output SysCALL,
  output SignedExt,
  output RegDst,
  output Beq,
  output Bne,
  output JR,
  output JMP,
  output JAL,
  output LB,
  output BGEZ
);

  \运算控制器自动生成  \u_运算控制器自动生成_1  (
    .OP0(OP[0]), .OP1(OP[1]), .OP2(OP[2]), .OP3(OP[3]), .OP4(OP[4]), .OP5(OP[5]), .F0(Func[0]), .F1(Func[1]),
    .F2(Func[2]), .F3(Func[3]), .F4(Func[4]), .F5(Func[5]), .S0(ALU_OP[0]), .S1(ALU_OP[1]), .S2(ALU_OP[2]),
    .S3(ALU_OP[3]));
  \控制信号自动生成  \u_控制信号自动生成_1  (
    .OP0(OP[0]), .OP1(OP[1]), .OP2(OP[2]), .OP3(OP[3]), .OP4(OP[4]), .OP5(OP[5]), .F0(Func[0]), .F1(Func[1]),
    .F2(Func[2]), .F3(Func[3]), .F4(Func[4]), .F5(Func[5]), .MemToReg(MemToReg), .MemWrite(MemWrite),
    .ALU_SRC(ALU_SRC), .RegWrite(RegWrite), .SysCALL(SysCALL), .SignedExt(SignedExt), .RegDst(RegDst),
    .BEQ(Beq), .BNE(Bne), .JR(JR), .JMP(JMP), .JAL(JAL));
  new_4 new_4_1 (
    .OP0(OP[0]), .OP1(OP[1]), .OP2(OP[2]), .OP3(OP[3]), .OP4(OP[4]), .OP5(OP[5]), .F0(Func[0]), .F1(Func[1]),
    .F2(Func[2]), .F3(Func[3]), .F4(Func[4]), .F5(Func[5]), .LB(LB), .BEGZ(BGEZ));

  // Other names for the same wires on the sheet: OP_CODE[5:0] = OP

  // Notes on the sheet:
  //   运算器控制器，根据指令生成运算器功能选择信号
  //   控制信号生成，产生数据通路需要的其他控制信号
endmodule

// 运算器控制器
module \运算控制器自动生成  (
  input  OP0,
  input  OP1,
  input  OP2,
  input  OP3,
  input  OP4,
  input  OP5,
  input  F0,
  input  F1,
  input  F2,
  input  F3,
  input  F4,
  input  F5,
  output S0,
  output S1,
  output S2,
  output S3
);

  wire and_1_out, and_2_out, and_3_out, and_4_out, and_5_out, and_6_out, and_7_out, and_8_out, and_9_out,
       and_10_out, and_11_out, and_12_out, and_13_out, and_14_out, and_15_out, and_16_out, and_17_out,
       and_18_out, and_19_out, and_20_out, and_21_out, and_22_out, and_23_out, and_24_out, and_25_out,
       and_26_out, and_27_out, and_28_out, and_29_out, and_30_out, and_31_out, and_32_out, and_33_out,
       and_34_out, and_35_out, and_36_out, and_37_out, and_38_out, and_39_out, and_40_out, and_41_out,
       and_42_out, and_43_out, not_1_out, not_2_out, not_3_out, not_4_out, not_5_out, not_6_out, not_7_out,
       not_8_out, not_9_out, not_10_out, not_11_out, not_12_out, not_13_out, not_14_out, not_15_out,
       not_16_out, not_17_out, not_18_out, not_19_out, not_20_out, not_21_out, not_22_out, not_23_out,
       not_24_out, not_25_out, not_26_out, not_27_out, not_28_out, not_29_out, not_30_out, not_31_out,
       not_32_out, not_33_out, not_34_out, not_35_out, not_36_out, not_37_out, not_38_out, not_39_out,
       not_40_out, not_41_out, not_42_out, not_43_out, not_44_out, not_45_out, not_46_out, not_47_out,
       not_48_out, not_49_out, not_50_out, not_51_out, not_52_out, not_53_out, not_54_out, not_55_out,
       not_56_out, not_57_out, not_58_out, not_59_out, not_60_out, not_61_out, not_62_out, not_63_out,
       not_64_out, not_65_out, not_66_out, not_67_out, not_68_out, not_69_out, not_70_out, not_71_out,
       not_72_out, not_73_out, not_74_out, not_75_out, not_76_out, not_77_out, not_78_out, not_79_out,
       not_80_out, not_81_out, not_82_out, not_83_out, not_84_out, not_85_out, not_86_out, not_87_out,
       not_88_out, not_89_out, not_90_out, not_91_out, not_92_out, not_93_out, not_94_out, not_95_out,
       not_96_out, not_97_out, not_98_out, not_99_out, not_100_out, not_101_out, not_102_out, not_103_out,
       not_104_out, not_105_out, not_106_out, not_107_out, not_108_out, not_109_out, not_110_out,
       not_111_out, not_112_out, not_113_out, not_114_out, not_115_out, not_116_out, not_117_out,
       not_118_out, not_119_out, not_120_out, not_121_out, not_122_out, not_123_out, not_124_out,
       not_125_out, not_126_out, not_127_out, not_128_out, not_129_out, not_130_out, not_131_out,
       not_132_out, not_133_out, not_134_out, not_135_out, not_136_out, not_137_out, not_138_out,
       not_139_out, not_140_out, not_141_out, not_142_out, not_143_out, not_144_out, not_145_out,
       not_146_out, not_147_out, not_148_out, not_149_out, not_150_out, not_151_out, not_152_out,
       not_153_out, not_154_out, not_155_out, not_156_out, not_157_out, not_158_out, not_159_out,
       not_160_out, not_161_out, not_162_out, not_163_out, not_164_out, not_165_out, not_166_out,
       not_167_out, not_168_out, not_169_out, not_170_out, not_171_out, not_172_out, not_173_out,
       not_174_out, not_175_out, not_176_out, not_177_out, not_178_out, not_179_out, not_180_out,
       not_181_out, not_182_out, not_183_out, not_184_out, not_185_out, not_186_out, not_187_out,
       not_188_out, not_189_out, not_190_out, not_191_out, not_192_out, not_193_out, not_194_out,
       not_195_out, not_196_out, not_197_out, not_198_out, not_199_out, not_200_out, not_201_out,
       not_202_out, not_203_out, not_204_out, not_205_out, not_206_out, not_207_out, not_208_out,
       not_209_out, not_210_out, not_211_out, not_212_out, not_213_out, not_214_out, not_215_out,
       not_216_out, not_217_out, not_218_out, not_219_out, not_220_out, not_221_out, not_222_out,
       not_223_out, not_224_out, not_225_out, not_226_out, not_227_out, not_228_out, not_229_out,
       not_230_out, not_231_out, not_232_out, not_233_out, not_234_out, not_235_out, not_236_out,
       not_237_out, not_238_out, not_239_out, not_240_out, not_241_out, not_242_out, not_243_out,
       not_244_out, not_245_out, not_246_out, not_247_out, not_248_out, not_249_out, not_250_out,
       not_251_out, not_252_out, not_253_out, not_254_out, not_255_out, not_256_out, not_257_out,
       not_258_out, not_259_out, not_260_out, not_261_out, not_262_out, not_263_out, not_264_out,
       not_265_out, not_266_out, not_267_out, not_268_out, not_269_out, not_270_out, not_271_out,
       not_272_out, not_273_out, not_274_out, not_275_out, not_276_out, not_277_out, not_278_out,
       not_279_out, not_280_out, not_281_out, not_282_out, not_283_out, not_284_out, not_285_out;

  not not_1 (not_1_out, OP5);
  not not_2 (not_2_out, OP4);
  not not_3 (not_3_out, OP3);
  not not_4 (not_4_out, OP2);
  not not_5 (not_5_out, OP1);
  not not_6 (not_6_out, OP0);
  not not_7 (not_7_out, F5);
  not not_8 (not_8_out, F4);
  not not_9 (not_9_out, F3);
  not not_10 (not_10_out, F2);
  not not_11 (not_11_out, OP5);
  not not_12 (not_12_out, OP4);
  not not_13 (not_13_out, OP3);
  not not_14 (not_14_out, OP2);
  not not_15 (not_15_out, OP1);
  not not_16 (not_16_out, OP0);
  not not_17 (not_17_out, F4);
  not not_18 (not_18_out, F3);
  not not_19 (not_19_out, F2);
  not not_20 (not_20_out, F1);
  not not_21 (not_21_out, F0);
  not not_22 (not_22_out, OP5);
  not not_23 (not_23_out, OP4);
  not not_24 (not_24_out, OP3);
  not not_25 (not_25_out, OP2);
  not not_26 (not_26_out, OP1);
  not not_27 (not_27_out, OP0);
  not not_28 (not_28_out, F4);
  not not_29 (not_29_out, F3);
  not not_30 (not_30_out, F2);
  not not_31 (not_31_out, F1);
  not not_32 (not_32_out, OP5);
  not not_33 (not_33_out, OP4);
  not not_34 (not_34_out, OP3);
  not not_35 (not_35_out, OP2);
  not not_36 (not_36_out, OP1);
  not not_37 (not_37_out, OP0);
  not not_38 (not_38_out, F4);
  not not_39 (not_39_out, F3);
  not not_40 (not_40_out, F1);
  not not_41 (not_41_out, F0);
  not not_42 (not_42_out, OP5);
  not not_43 (not_43_out, OP4);
  not not_44 (not_44_out, OP3);
  not not_45 (not_45_out, OP2);
  not not_46 (not_46_out, OP1);
  not not_47 (not_47_out, OP0);
  not not_48 (not_48_out, F4);
  not not_49 (not_49_out, F2);
  not not_50 (not_50_out, F0);
  not not_51 (not_51_out, OP5);
  not not_52 (not_52_out, OP4);
  not not_53 (not_53_out, OP2);
  not not_54 (not_54_out, OP1);
  not not_55 (not_55_out, OP0);
  not not_56 (not_56_out, OP5);
  not not_57 (not_57_out, OP4);
  not not_58 (not_58_out, OP1);
  not not_59 (not_59_out, OP0);
  not not_60 (not_60_out, OP5);
  not not_61 (not_61_out, OP4);
  not not_62 (not_62_out, OP2);
  not not_63 (not_63_out, OP1);
  not not_64 (not_64_out, OP5);
  not not_65 (not_65_out, OP4);
  not not_66 (not_66_out, OP2);
  not not_67 (not_67_out, OP0);
  not not_68 (not_68_out, OP4);
  not not_69 (not_69_out, OP3);
  not not_70 (not_70_out, OP2);
  not not_71 (not_71_out, OP4);
  not not_72 (not_72_out, OP2);
  not not_73 (not_73_out, OP5);
  not not_74 (not_74_out, OP4);
  not not_75 (not_75_out, OP3);
  not not_76 (not_76_out, OP2);
  not not_77 (not_77_out, OP1);
  not not_78 (not_78_out, OP0);
  not not_79 (not_79_out, F4);
  not not_80 (not_80_out, F3);
  not not_81 (not_81_out, F0);
  not not_82 (not_82_out, OP4);
  not not_83 (not_83_out, OP3);
  not not_84 (not_84_out, OP2);
  not not_85 (not_85_out, OP1);
  not not_86 (not_86_out, OP0);
  not not_87 (not_87_out, OP5);
  not not_88 (not_88_out, OP4);
  not not_89 (not_89_out, OP3);
  not not_90 (not_90_out, OP2);
  not not_91 (not_91_out, OP1);
  not not_92 (not_92_out, OP5);
  not not_93 (not_93_out, OP4);
  not not_94 (not_94_out, OP3);
  not not_95 (not_95_out, OP2);
  not not_96 (not_96_out, OP1);
  not not_97 (not_97_out, OP0);
  not not_98 (not_98_out, F5);
  not not_99 (not_99_out, F4);
  not not_100 (not_100_out, F3);
  not not_101 (not_101_out, F2);
  not not_102 (not_102_out, F0);
  not not_103 (not_103_out, OP5);
  not not_104 (not_104_out, OP4);
  not not_105 (not_105_out, OP3);
  not not_106 (not_106_out, OP2);
  not not_107 (not_107_out, OP1);
  not not_108 (not_108_out, OP0);
  not not_109 (not_109_out, F4);
  not not_110 (not_110_out, F3);
  not not_111 (not_111_out, F2);
  not not_112 (not_112_out, F0);
  not not_113 (not_113_out, OP5);
  not not_114 (not_114_out, OP4);
  not not_115 (not_115_out, OP3);
  not not_116 (not_116_out, OP2);
  not not_117 (not_117_out, OP1);
  not not_118 (not_118_out, OP0);
  not not_119 (not_119_out, F4);
  not not_120 (not_120_out, F3);
  not not_121 (not_121_out, F1);
  not not_122 (not_122_out, F0);
  not not_123 (not_123_out, OP5);
  not not_124 (not_124_out, OP4);
  not not_125 (not_125_out, OP3);
  not not_126 (not_126_out, OP2);
  not not_127 (not_127_out, OP1);
  not not_128 (not_128_out, OP0);
  not not_129 (not_129_out, F4);
  not not_130 (not_130_out, F3);
  not not_131 (not_131_out, OP5);
  not not_132 (not_132_out, OP4);
  not not_133 (not_133_out, OP3);
  not not_134 (not_134_out, OP2);
  not not_135 (not_135_out, OP1);
  not not_136 (not_136_out, OP0);
  not not_137 (not_137_out, F4);
  not not_138 (not_138_out, F2);
  not not_139 (not_139_out, F0);
  not not_140 (not_140_out, OP5);
  not not_141 (not_141_out, OP4);
  not not_142 (not_142_out, OP1);
  not not_143 (not_143_out, OP0);
  not not_144 (not_144_out, OP5);
  not not_145 (not_145_out, OP4);
  not not_146 (not_146_out, OP2);
  not not_147 (not_147_out, OP0);
  not not_148 (not_148_out, OP5);
  not not_149 (not_149_out, OP4);
  not not_150 (not_150_out, OP3);
  not not_151 (not_151_out, OP2);
  not not_152 (not_152_out, OP1);
  not not_153 (not_153_out, OP5);
  not not_154 (not_154_out, OP4);
  not not_155 (not_155_out, OP3);
  not not_156 (not_156_out, OP2);
  not not_157 (not_157_out, OP1);
  not not_158 (not_158_out, OP0);
  not not_159 (not_159_out, F4);
  not not_160 (not_160_out, F3);
  not not_161 (not_161_out, F2);
  not not_162 (not_162_out, F1);
  not not_163 (not_163_out, F0);
  not not_164 (not_164_out, OP5);
  not not_165 (not_165_out, OP4);
  not not_166 (not_166_out, OP3);
  not not_167 (not_167_out, OP2);
  not not_168 (not_168_out, OP1);
  not not_169 (not_169_out, OP0);
  not not_170 (not_170_out, F4);
  not not_171 (not_171_out, F3);
  not not_172 (not_172_out, F2);
  not not_173 (not_173_out, F1);
  not not_174 (not_174_out, OP5);
  not not_175 (not_175_out, OP4);
  not not_176 (not_176_out, OP3);
  not not_177 (not_177_out, OP2);
  not not_178 (not_178_out, OP1);
  not not_179 (not_179_out, OP0);
  not not_180 (not_180_out, F4);
  not not_181 (not_181_out, F3);
  not not_182 (not_182_out, F2);
  not not_183 (not_183_out, F0);
  not not_184 (not_184_out, OP5);
  not not_185 (not_185_out, OP4);
  not not_186 (not_186_out, OP3);
  not not_187 (not_187_out, OP2);
  not not_188 (not_188_out, OP1);
  not not_189 (not_189_out, OP0);
  not not_190 (not_190_out, F4);
  not not_191 (not_191_out, F3);
  not not_192 (not_192_out, F1);
  not not_193 (not_193_out, F0);
  not not_194 (not_194_out, OP5);
  not not_195 (not_195_out, OP4);
  not not_196 (not_196_out, OP3);
  not not_197 (not_197_out, OP2);
  not not_198 (not_198_out, OP1);
  not not_199 (not_199_out, OP0);
  not not_200 (not_200_out, F4);
  not not_201 (not_201_out, F2);
  not not_202 (not_202_out, OP5);
  not not_203 (not_203_out, OP4);
  not not_204 (not_204_out, OP2);
  not not_205 (not_205_out, OP1);
  not not_206 (not_206_out, OP0);
  not not_207 (not_207_out, OP5);
  not not_208 (not_208_out, OP4);
  not not_209 (not_209_out, OP1);
  not not_210 (not_210_out, OP0);
  not not_211 (not_211_out, OP5);
  not not_212 (not_212_out, OP4);
  not not_213 (not_213_out, OP2);
  not not_214 (not_214_out, OP1);
  not not_215 (not_215_out, OP4);
  not not_216 (not_216_out, OP3);
  not not_217 (not_217_out, OP2);
  not not_218 (not_218_out, OP4);
  not not_219 (not_219_out, OP2);
  not not_220 (not_220_out, OP5);
  not not_221 (not_221_out, OP4);
  not not_222 (not_222_out, OP2);
  not not_223 (not_223_out, OP4);
  not not_224 (not_224_out, OP3);
  not not_225 (not_225_out, OP2);
  not not_226 (not_226_out, OP1);
  not not_227 (not_227_out, OP0);
  not not_228 (not_228_out, OP5);
  not not_229 (not_229_out, OP4);
  not not_230 (not_230_out, OP3);
  not not_231 (not_231_out, OP2);
  not not_232 (not_232_out, OP1);
  not not_233 (not_233_out, OP0);
  not not_234 (not_234_out, F4);
  not not_235 (not_235_out, F3);
  not not_236 (not_236_out, F1);
  not not_237 (not_237_out, OP5);
  not not_238 (not_238_out, OP4);
  not not_239 (not_239_out, OP3);
  not not_240 (not_240_out, OP2);
  not not_241 (not_241_out, OP1);
  not not_242 (not_242_out, OP0);
  not not_243 (not_243_out, F4);
  not not_244 (not_244_out, F3);
  not not_245 (not_245_out, OP5);
  not not_246 (not_246_out, OP4);
  not not_247 (not_247_out, OP3);
  not not_248 (not_248_out, OP2);
  not not_249 (not_249_out, OP1);
  not not_250 (not_250_out, OP0);
  not not_251 (not_251_out, F4);
  not not_252 (not_252_out, F2);
  not not_253 (not_253_out, F0);
  not not_254 (not_254_out, OP5);
  not not_255 (not_255_out, OP4);
  not not_256 (not_256_out, OP3);
  not not_257 (not_257_out, OP2);
  not not_258 (not_258_out, OP1);
  not not_259 (not_259_out, OP0);
  not not_260 (not_260_out, F4);
  not not_261 (not_261_out, F2);
  not not_262 (not_262_out, OP5);
  not not_263 (not_263_out, OP4);
  not not_264 (not_264_out, OP2);
  not not_265 (not_265_out, OP0);
  not not_266 (not_266_out, OP5);
  not not_267 (not_267_out, OP4);
  not not_268 (not_268_out, OP1);
  not not_269 (not_269_out, OP5);
  not not_270 (not_270_out, OP4);
  not not_271 (not_271_out, OP3);
  not not_272 (not_272_out, OP2);
  not not_273 (not_273_out, OP1);
  not not_274 (not_274_out, OP0);
  not not_275 (not_275_out, F4);
  not not_276 (not_276_out, F3);
  not not_277 (not_277_out, F0);
  not not_278 (not_278_out, OP5);
  not not_279 (not_279_out, OP4);
  not not_280 (not_280_out, OP2);
  not not_281 (not_281_out, OP5);
  not not_282 (not_282_out, OP4);
  not not_283 (not_283_out, OP3);
  not not_284 (not_284_out, OP2);
  not not_285 (not_285_out, OP1);
  and and_1 (and_1_out, not_1_out, not_2_out, not_3_out, not_4_out, not_5_out, not_6_out, not_7_out, not_8_out, not_9_out, not_10_out, F1, F0);
  and and_2 (and_2_out, not_11_out, not_12_out, not_13_out, not_14_out, not_15_out, not_16_out, F5, not_17_out, not_18_out, not_19_out, not_20_out, not_21_out);
  and and_3 (and_3_out, not_22_out, not_23_out, not_24_out, not_25_out, not_26_out, not_27_out, F5, not_28_out, not_29_out, not_30_out, not_31_out, F0);
  and and_4 (and_4_out, not_32_out, not_33_out, not_34_out, not_35_out, not_36_out, not_37_out, F5, not_38_out, not_39_out, F2, not_40_out, not_41_out);
  and and_5 (and_5_out, not_42_out, not_43_out, not_44_out, not_45_out, not_46_out, not_47_out, F5, not_48_out, F3, not_49_out, F1, not_50_out);
  and and_6 (and_6_out, not_51_out, not_52_out, OP3, not_53_out, not_54_out, not_55_out);
  and and_7 (and_7_out, not_56_out, not_57_out, OP3, OP2, not_58_out, not_59_out);
  and and_8 (and_8_out, not_60_out, not_61_out, OP3, not_62_out, not_63_out, OP0);
  and and_9 (and_9_out, not_64_out, not_65_out, OP3, not_66_out, OP1, not_67_out);
  and and_10 (and_10_out, OP5, not_68_out, not_69_out, not_70_out, OP1, OP0);
  and and_11 (and_11_out, OP5, not_71_out, OP3, not_72_out, OP1, OP0);
  and and_12 (and_12_out, not_73_out, not_74_out, not_75_out, not_76_out, not_77_out, not_78_out, F5, not_79_out, not_80_out, F2, F1, not_81_out);
  and and_13 (and_13_out, OP5, not_82_out, not_83_out, not_84_out, not_85_out, not_86_out);
  and and_14 (and_14_out, not_87_out, not_88_out, not_89_out, not_90_out, not_91_out, OP0);
  and and_15 (and_15_out, not_92_out, not_93_out, not_94_out, not_95_out, not_96_out, not_97_out, not_98_out, not_99_out, not_100_out, not_101_out, F1, not_102_out);
  and and_16 (and_16_out, not_103_out, not_104_out, not_105_out, not_106_out, not_107_out, not_108_out, F5, not_109_out, not_110_out, not_111_out, F1, not_112_out);
  and and_17 (and_17_out, not_113_out, not_114_out, not_115_out, not_116_out, not_117_out, not_118_out, F5, not_119_out, not_120_out, F2, not_121_out, not_122_out);
  and and_18 (and_18_out, not_123_out, not_124_out, not_125_out, not_126_out, not_127_out, not_128_out, F5, not_129_out, not_130_out, F2, F1, F0);
  and and_19 (and_19_out, not_131_out, not_132_out, not_133_out, not_134_out, not_135_out, not_136_out, F5, not_137_out, F3, not_138_out, F1, not_139_out);
  and and_20 (and_20_out, not_140_out, not_141_out, OP3, OP2, not_142_out, not_143_out);
  and and_21 (and_21_out, not_144_out, not_145_out, OP3, not_146_out, OP1, not_147_out);
  and and_22 (and_22_out, not_148_out, not_149_out, not_150_out, not_151_out, not_152_out, OP0);
  and and_23 (and_23_out, not_153_out, not_154_out, not_155_out, not_156_out, not_157_out, not_158_out, F5, not_159_out, not_160_out, not_161_out, not_162_out, not_163_out);
  and and_24 (and_24_out, not_164_out, not_165_out, not_166_out, not_167_out, not_168_out, not_169_out, F5, not_170_out, not_171_out, not_172_out, not_173_out, F0);
  and and_25 (and_25_out, not_174_out, not_175_out, not_176_out, not_177_out, not_178_out, not_179_out, F5, not_180_out, not_181_out, not_182_out, F1, not_183_out);
  and and_26 (and_26_out, not_184_out, not_185_out, not_186_out, not_187_out, not_188_out, not_189_out, F5, not_190_out, not_191_out, F2, not_192_out, not_193_out);
  and and_27 (and_27_out, not_194_out, not_195_out, not_196_out, not_197_out, not_198_out, not_199_out, F5, not_200_out, F3, not_201_out, F1, F0);
  and and_28 (and_28_out, not_202_out, not_203_out, OP3, not_204_out, not_205_out, not_206_out);
  and and_29 (and_29_out, not_207_out, not_208_out, OP3, OP2, not_209_out, not_210_out);
  and and_30 (and_30_out, not_211_out, not_212_out, OP3, not_213_out, not_214_out, OP0);
  and and_31 (and_31_out, OP5, not_215_out, not_216_out, not_217_out, OP1, OP0);
  and and_32 (and_32_out, OP5, not_218_out, OP3, not_219_out, OP1, OP0);
  and and_33 (and_33_out, not_220_out, not_221_out, OP3, not_222_out, OP1, OP0);
  and and_34 (and_34_out, OP5, not_223_out, not_224_out, not_225_out, not_226_out, not_227_out);
  and and_35 (and_35_out, not_228_out, not_229_out, not_230_out, not_231_out, not_232_out, not_233_out, F5, not_234_out, not_235_out, F2, not_236_out, F0);
  and and_36 (and_36_out, not_237_out, not_238_out, not_239_out, not_240_out, not_241_out, not_242_out, F5, not_243_out, not_244_out, F2, F1, F0);
  and and_37 (and_37_out, not_245_out, not_246_out, not_247_out, not_248_out, not_249_out, not_250_out, F5, not_251_out, F3, not_252_out, F1, not_253_out);
  and and_38 (and_38_out, not_254_out, not_255_out, not_256_out, not_257_out, not_258_out, not_259_out, F5, not_260_out, F3, not_261_out, F1, F0);
  and and_39 (and_39_out, not_262_out, not_263_out, OP3, not_264_out, OP1, not_265_out);
  and and_40 (and_40_out, not_266_out, not_267_out, OP3, OP2, not_268_out, OP0);
  and and_41 (and_41_out, not_269_out, not_270_out, not_271_out, not_272_out, not_273_out, not_274_out, F5, not_275_out, not_276_out, F2, F1, not_277_out);
  and and_42 (and_42_out, not_278_out, not_279_out, OP3, not_280_out, OP1, OP0);
  and and_43 (and_43_out, not_281_out, not_282_out, not_283_out, not_284_out, not_285_out, OP0);
  or or_1 (S1, and_15_out, and_16_out, and_17_out, and_18_out, and_19_out, and_20_out, and_21_out, and_22_out);
  or or_2 (S3, and_35_out, and_36_out, and_37_out, and_38_out, and_39_out, and_40_out, and_41_out, and_42_out, and_43_out);
  or or_3 (S0, and_1_out, and_2_out, and_3_out, and_4_out, and_5_out, and_6_out, and_7_out, and_8_out, and_9_out, and_10_out, and_11_out, and_12_out, and_13_out, and_14_out);
  or or_4 (S2, and_23_out, and_24_out, and_25_out, and_26_out, and_27_out, and_28_out, and_29_out, and_30_out, and_31_out, and_32_out, and_33_out, and_34_out);
endmodule

// 控制信号生成
module \控制信号自动生成  (
  input  OP0,
  input  OP1,
  input  OP2,
  input  OP3,
  input  OP4,
  input  OP5,
  input  F0,
  input  F1,
  input  F2,
  input  F3,
  input  F4,
  input  F5,
  output MemToReg,
  output MemWrite,
  output ALU_SRC,
  output RegWrite,
  output SysCALL,
  output SignedExt,
  output RegDst,
  output BEQ,
  output BNE,
  output JR,
  output JMP,
  output JAL
);

  wire and_1_out, and_2_out, and_4_out, and_5_out, and_6_out, and_7_out, and_8_out, and_9_out, and_10_out,
       and_11_out, and_12_out, and_13_out, and_14_out, and_15_out, and_16_out, and_17_out, and_18_out,
       and_19_out, and_20_out, and_21_out, and_22_out, and_23_out, and_24_out, and_25_out, and_26_out,
       and_27_out, and_28_out, and_29_out, and_30_out, and_31_out, and_32_out, and_33_out, and_35_out,
       and_36_out, and_37_out, and_38_out, and_39_out, and_40_out, and_41_out, and_42_out, and_43_out,
       and_44_out, and_45_out, and_46_out, and_47_out, and_48_out, and_49_out, and_50_out, and_51_out,
       and_52_out, and_56_out, and_57_out, and_58_out, not_1_out, not_2_out, not_3_out, not_4_out, not_5_out,
       not_6_out, not_7_out, not_8_out, not_9_out, not_10_out, not_11_out, not_12_out, not_13_out,
       not_14_out, not_15_out, not_16_out, not_17_out, not_18_out, not_19_out, not_20_out, not_21_out,
       not_22_out, not_23_out, not_24_out, not_25_out, not_26_out, not_27_out, not_28_out, not_29_out,
       not_30_out, not_31_out, not_32_out, not_33_out, not_34_out, not_35_out, not_36_out, not_37_out,
       not_38_out, not_39_out, not_40_out, not_41_out, not_42_out, not_43_out, not_44_out, not_45_out,
       not_46_out, not_47_out, not_48_out, not_49_out, not_50_out, not_51_out, not_52_out, not_53_out,
       not_54_out, not_55_out, not_56_out, not_57_out, not_58_out, not_59_out, not_60_out, not_61_out,
       not_62_out, not_63_out, not_64_out, not_65_out, not_66_out, not_67_out, not_68_out, not_69_out,
       not_70_out, not_71_out, not_72_out, not_73_out, not_74_out, not_75_out, not_76_out, not_77_out,
       not_78_out, not_79_out, not_80_out, not_81_out, not_82_out, not_83_out, not_84_out, not_85_out,
       not_86_out, not_87_out, not_88_out, not_89_out, not_90_out, not_91_out, not_92_out, not_93_out,
       not_94_out, not_95_out, not_96_out, not_97_out, not_98_out, not_99_out, not_100_out, not_101_out,
       not_102_out, not_103_out, not_104_out, not_105_out, not_106_out, not_107_out, not_108_out,
       not_109_out, not_110_out, not_111_out, not_112_out, not_113_out, not_114_out, not_115_out,
       not_116_out, not_117_out, not_118_out, not_119_out, not_120_out, not_121_out, not_122_out,
       not_123_out, not_124_out, not_125_out, not_126_out, not_127_out, not_128_out, not_129_out,
       not_130_out, not_131_out, not_132_out, not_133_out, not_134_out, not_135_out, not_136_out,
       not_137_out, not_138_out, not_139_out, not_140_out, not_141_out, not_142_out, not_143_out,
       not_144_out, not_145_out, not_146_out, not_147_out, not_148_out, not_149_out, not_150_out,
       not_151_out, not_152_out, not_153_out, not_154_out, not_155_out, not_156_out, not_157_out,
       not_158_out, not_159_out, not_160_out, not_161_out, not_162_out, not_163_out, not_164_out,
       not_165_out, not_166_out, not_167_out, not_168_out, not_169_out, not_170_out, not_171_out,
       not_172_out, not_173_out, not_174_out, not_175_out, not_176_out, not_177_out, not_178_out,
       not_179_out, not_180_out, not_181_out, not_182_out, not_183_out, not_184_out, not_185_out,
       not_186_out, not_187_out, not_188_out, not_189_out, not_190_out, not_191_out, not_192_out,
       not_193_out, not_194_out, not_195_out, not_196_out, not_197_out, not_198_out, not_199_out,
       not_200_out, not_201_out, not_202_out, not_203_out, not_204_out, not_205_out, not_206_out,
       not_207_out, not_208_out, not_209_out, not_210_out, not_211_out, not_212_out, not_213_out,
       not_214_out, not_215_out, not_216_out, not_217_out, not_218_out, not_219_out, not_220_out,
       not_221_out, not_222_out, not_223_out, not_224_out, not_225_out, not_226_out, not_227_out,
       not_228_out, not_229_out, not_230_out, not_231_out, not_232_out, not_233_out, not_234_out,
       not_235_out, not_236_out, not_237_out, not_238_out, not_239_out, not_240_out, not_241_out,
       not_242_out, not_243_out, not_244_out, not_245_out, not_246_out, not_247_out, not_248_out,
       not_249_out, not_250_out, not_251_out, not_252_out, not_253_out, not_254_out, not_255_out,
       not_256_out, not_257_out, not_258_out, not_259_out, not_260_out, not_261_out, not_262_out,
       not_263_out, not_264_out, not_265_out, not_266_out, not_267_out, not_268_out, not_269_out,
       not_270_out, not_271_out, not_272_out, not_273_out, not_274_out, not_275_out, not_276_out,
       not_277_out, not_278_out, not_279_out, not_280_out, not_281_out, not_282_out, not_283_out,
       not_284_out, not_285_out, not_286_out, not_287_out, not_288_out, not_289_out, not_290_out,
       not_291_out, not_292_out, not_293_out, not_294_out, not_295_out, not_296_out, not_297_out,
       not_298_out, not_299_out, not_300_out, not_301_out, not_302_out, not_303_out, not_304_out,
       not_305_out, not_306_out, not_307_out, not_308_out, not_309_out, not_310_out, not_311_out,
       not_312_out, not_313_out, not_314_out, not_315_out, not_316_out, not_317_out, not_318_out,
       not_319_out, not_320_out, not_321_out, not_322_out, not_323_out, not_324_out, not_325_out,
       not_326_out, not_327_out, not_328_out, not_329_out, not_330_out, not_331_out, not_332_out,
       not_333_out, not_334_out, not_335_out, not_336_out, not_337_out, not_338_out, not_339_out,
       not_340_out, not_341_out, not_342_out, not_343_out, not_344_out, not_345_out, not_346_out,
       not_347_out, not_348_out, not_349_out, not_350_out, not_351_out, not_352_out, not_353_out,
       not_354_out, not_355_out, not_356_out, not_357_out, not_358_out, not_359_out, not_360_out,
       not_361_out, not_362_out, not_363_out, not_364_out, not_365_out, not_366_out, not_367_out,
       not_368_out, not_369_out, not_370_out, not_371_out, not_372_out, not_373_out, not_374_out,
       not_375_out, not_376_out, not_377_out, not_378_out, not_379_out, not_380_out, not_381_out,
       not_382_out, not_383_out, not_384_out, not_385_out, not_386_out, not_387_out, not_388_out,
       not_389_out, not_390_out, not_391_out, not_392_out, not_393_out, not_394_out, not_395_out,
       not_396_out, not_397_out;

  not not_1 (not_1_out, OP4);
  not not_2 (not_2_out, OP3);
  not not_3 (not_3_out, OP2);
  not not_4 (not_4_out, OP4);
  not not_5 (not_5_out, OP3);
  not not_6 (not_6_out, OP2);
  not not_7 (not_7_out, OP1);
  not not_8 (not_8_out, OP0);
  not not_9 (not_9_out, OP4);
  not not_10 (not_10_out, OP2);
  not not_11 (not_11_out, OP5);
  not not_12 (not_12_out, OP4);
  not not_13 (not_13_out, OP2);
  not not_14 (not_14_out, OP1);
  not not_15 (not_15_out, OP0);
  not not_16 (not_16_out, OP5);
  not not_17 (not_17_out, OP4);
  not not_18 (not_18_out, OP1);
  not not_19 (not_19_out, OP0);
  not not_20 (not_20_out, OP5);
  not not_21 (not_21_out, OP4);
  not not_22 (not_22_out, OP2);
  not not_23 (not_23_out, OP1);
  not not_24 (not_24_out, OP5);
  not not_25 (not_25_out, OP4);
  not not_26 (not_26_out, OP2);
  not not_27 (not_27_out, OP0);
  not not_28 (not_28_out, OP5);
  not not_29 (not_29_out, OP4);
  not not_30 (not_30_out, OP1);
  not not_31 (not_31_out, OP4);
  not not_32 (not_32_out, OP3);
  not not_33 (not_33_out, OP2);
  not not_34 (not_34_out, OP4);
  not not_35 (not_35_out, OP2);
  not not_36 (not_36_out, OP5);
  not not_37 (not_37_out, OP4);
  not not_38 (not_38_out, OP2);
  not not_39 (not_39_out, OP4);
  not not_40 (not_40_out, OP3);
  not not_41 (not_41_out, OP2);
  not not_42 (not_42_out, OP1);
  not not_43 (not_43_out, OP0);
  not not_44 (not_44_out, OP5);
  not not_45 (not_45_out, OP4);
  not not_46 (not_46_out, OP3);
  not not_47 (not_47_out, OP2);
  not not_48 (not_48_out, OP1);
  not not_49 (not_49_out, OP0);
  not not_50 (not_50_out, F5);
  not not_51 (not_51_out, F4);
  not not_52 (not_52_out, F3);
  not not_53 (not_53_out, F2);
  not not_54 (not_54_out, F1);
  not not_55 (not_55_out, F0);
  not not_56 (not_56_out, OP5);
  not not_57 (not_57_out, OP4);
  not not_58 (not_58_out, OP3);
  not not_59 (not_59_out, OP2);
  not not_60 (not_60_out, OP1);
  not not_61 (not_61_out, OP0);
  not not_62 (not_62_out, F5);
  not not_63 (not_63_out, F4);
  not not_64 (not_64_out, F3);
  not not_65 (not_65_out, F2);
  not not_66 (not_66_out, OP5);
  not not_67 (not_67_out, OP4);
  not not_68 (not_68_out, OP3);
  not not_69 (not_69_out, OP2);
  not not_70 (not_70_out, OP1);
  not not_71 (not_71_out, OP0);
  not not_72 (not_72_out, F5);
  not not_73 (not_73_out, F4);
  not not_74 (not_74_out, F3);
  not not_75 (not_75_out, F2);
  not not_76 (not_76_out, F0);
  not not_77 (not_77_out, OP5);
  not not_78 (not_78_out, OP4);
  not not_79 (not_79_out, OP3);
  not not_80 (not_80_out, OP2);
  not not_81 (not_81_out, OP1);
  not not_82 (not_82_out, OP0);
  not not_83 (not_83_out, F4);
  not not_84 (not_84_out, F3);
  not not_85 (not_85_out, F2);
  not not_86 (not_86_out, F1);
  not not_87 (not_87_out, F0);
  not not_88 (not_88_out, OP5);
  not not_89 (not_89_out, OP4);
  not not_90 (not_90_out, OP3);
  not not_91 (not_91_out, OP2);
  not not_92 (not_92_out, OP1);
  not not_93 (not_93_out, OP0);
  not not_94 (not_94_out, F4);
  not not_95 (not_95_out, F3);
  not not_96 (not_96_out, F2);
  not not_97 (not_97_out, F1);
  not not_98 (not_98_out, OP5);
  not not_99 (not_99_out, OP4);
  not not_100 (not_100_out, OP3);
  not not_101 (not_101_out, OP2);
  not not_102 (not_102_out, OP1);
  not not_103 (not_103_out, OP0);
  not not_104 (not_104_out, F4);
  not not_105 (not_105_out, F3);
  not not_106 (not_106_out, F2);
  not not_107 (not_107_out, F0);
  not not_108 (not_108_out, OP5);
  not not_109 (not_109_out, OP4);
  not not_110 (not_110_out, OP3);
  not not_111 (not_111_out, OP2);
  not not_112 (not_112_out, OP1);
  not not_113 (not_113_out, OP0);
  not not_114 (not_114_out, F4);
  not not_115 (not_115_out, F3);
  not not_116 (not_116_out, F1);
  not not_117 (not_117_out, F0);
  not not_118 (not_118_out, OP5);
  not not_119 (not_119_out, OP4);
  not not_120 (not_120_out, OP3);
  not not_121 (not_121_out, OP2);
  not not_122 (not_122_out, OP1);
  not not_123 (not_123_out, OP0);
  not not_124 (not_124_out, F4);
  not not_125 (not_125_out, F3);
  not not_126 (not_126_out, F1);
  not not_127 (not_127_out, OP5);
  not not_128 (not_128_out, OP4);
  not not_129 (not_129_out, OP3);
  not not_130 (not_130_out, OP2);
  not not_131 (not_131_out, OP1);
  not not_132 (not_132_out, OP0);
  not not_133 (not_133_out, F4);
  not not_134 (not_134_out, F3);
  not not_135 (not_135_out, OP5);
  not not_136 (not_136_out, OP4);
  not not_137 (not_137_out, OP3);
  not not_138 (not_138_out, OP2);
  not not_139 (not_139_out, OP1);
  not not_140 (not_140_out, OP0);
  not not_141 (not_141_out, F4);
  not not_142 (not_142_out, F2);
  not not_143 (not_143_out, F0);
  not not_144 (not_144_out, OP5);
  not not_145 (not_145_out, OP4);
  not not_146 (not_146_out, OP3);
  not not_147 (not_147_out, OP2);
  not not_148 (not_148_out, OP1);
  not not_149 (not_149_out, OP0);
  not not_150 (not_150_out, F4);
  not not_151 (not_151_out, F2);
  not not_152 (not_152_out, OP5);
  not not_153 (not_153_out, OP4);
  not not_154 (not_154_out, OP3);
  not not_155 (not_155_out, OP2);
  not not_156 (not_156_out, OP5);
  not not_157 (not_157_out, OP4);
  not not_158 (not_158_out, OP2);
  not not_159 (not_159_out, OP1);
  not not_160 (not_160_out, OP0);
  not not_161 (not_161_out, OP5);
  not not_162 (not_162_out, OP4);
  not not_163 (not_163_out, OP1);
  not not_164 (not_164_out, OP0);
  not not_165 (not_165_out, OP5);
  not not_166 (not_166_out, OP4);
  not not_167 (not_167_out, OP2);
  not not_168 (not_168_out, OP1);
  not not_169 (not_169_out, OP5);
  not not_170 (not_170_out, OP4);
  not not_171 (not_171_out, OP2);
  not not_172 (not_172_out, OP0);
  not not_173 (not_173_out, OP5);
  not not_174 (not_174_out, OP4);
  not not_175 (not_175_out, OP1);
  not not_176 (not_176_out, OP4);
  not not_177 (not_177_out, OP3);
  not not_178 (not_178_out, OP2);
  not not_179 (not_179_out, OP5);
  not not_180 (not_180_out, OP4);
  not not_181 (not_181_out, OP3);
  not not_182 (not_182_out, OP2);
  not not_183 (not_183_out, OP1);
  not not_184 (not_184_out, OP0);
  not not_185 (not_185_out, F4);
  not not_186 (not_186_out, F3);
  not not_187 (not_187_out, F0);
  not not_188 (not_188_out, OP5);
  not not_189 (not_189_out, OP4);
  not not_190 (not_190_out, OP2);
  not not_191 (not_191_out, OP4);
  not not_192 (not_192_out, OP3);
  not not_193 (not_193_out, OP2);
  not not_194 (not_194_out, OP1);
  not not_195 (not_195_out, OP0);
  not not_196 (not_196_out, OP5);
  not not_197 (not_197_out, OP4);
  not not_198 (not_198_out, OP3);
  not not_199 (not_199_out, OP2);
  not not_200 (not_200_out, OP1);
  not not_201 (not_201_out, OP0);
  not not_202 (not_202_out, F5);
  not not_203 (not_203_out, F4);
  not not_204 (not_204_out, F1);
  not not_205 (not_205_out, F0);
  not not_206 (not_206_out, OP5);
  not not_207 (not_207_out, OP4);
  not not_208 (not_208_out, OP2);
  not not_209 (not_209_out, OP1);
  not not_210 (not_210_out, OP0);
  not not_211 (not_211_out, OP5);
  not not_212 (not_212_out, OP4);
  not not_213 (not_213_out, OP2);
  not not_214 (not_214_out, OP1);
  not not_215 (not_215_out, OP5);
  not not_216 (not_216_out, OP4);
  not not_217 (not_217_out, OP2);
  not not_218 (not_218_out, OP0);
  not not_219 (not_219_out, OP5);
  not not_220 (not_220_out, OP4);
  not not_221 (not_221_out, OP2);
  not not_222 (not_222_out, OP4);
  not not_223 (not_223_out, OP3);
  not not_224 (not_224_out, OP2);
  not not_225 (not_225_out, OP1);
  not not_226 (not_226_out, OP0);
  not not_227 (not_227_out, OP5);
  not not_228 (not_228_out, OP4);
  not not_229 (not_229_out, OP3);
  not not_230 (not_230_out, OP2);
  not not_231 (not_231_out, OP1);
  not not_232 (not_232_out, OP0);
  not not_233 (not_233_out, F5);
  not not_234 (not_234_out, F4);
  not not_235 (not_235_out, F3);
  not not_236 (not_236_out, F2);
  not not_237 (not_237_out, F1);
  not not_238 (not_238_out, F0);
  not not_239 (not_239_out, OP5);
  not not_240 (not_240_out, OP4);
  not not_241 (not_241_out, OP3);
  not not_242 (not_242_out, OP2);
  not not_243 (not_243_out, OP1);
  not not_244 (not_244_out, OP0);
  not not_245 (not_245_out, F5);
  not not_246 (not_246_out, F4);
  not not_247 (not_247_out, F3);
  not not_248 (not_248_out, F2);
  not not_249 (not_249_out, OP5);
  not not_250 (not_250_out, OP4);
  not not_251 (not_251_out, OP3);
  not not_252 (not_252_out, OP2);
  not not_253 (not_253_out, OP1);
  not not_254 (not_254_out, OP0);
  not not_255 (not_255_out, F5);
  not not_256 (not_256_out, F4);
  not not_257 (not_257_out, F3);
  not not_258 (not_258_out, F2);
  not not_259 (not_259_out, F0);
  not not_260 (not_260_out, OP5);
  not not_261 (not_261_out, OP4);
  not not_262 (not_262_out, OP3);
  not not_263 (not_263_out, OP2);
  not not_264 (not_264_out, OP1);
  not not_265 (not_265_out, OP0);
  not not_266 (not_266_out, F4);
  not not_267 (not_267_out, F3);
  not not_268 (not_268_out, F2);
  not not_269 (not_269_out, F1);
  not not_270 (not_270_out, F0);
  not not_271 (not_271_out, OP5);
  not not_272 (not_272_out, OP4);
  not not_273 (not_273_out, OP3);
  not not_274 (not_274_out, OP2);
  not not_275 (not_275_out, OP1);
  not not_276 (not_276_out, OP0);
  not not_277 (not_277_out, F4);
  not not_278 (not_278_out, F3);
  not not_279 (not_279_out, F2);
  not not_280 (not_280_out, F1);
  not not_281 (not_281_out, OP5);
  not not_282 (not_282_out, OP4);
  not not_283 (not_283_out, OP3);
  not not_284 (not_284_out, OP2);
  not not_285 (not_285_out, OP1);
  not not_286 (not_286_out, OP0);
  not not_287 (not_287_out, F4);
  not not_288 (not_288_out, F3);
  not not_289 (not_289_out, F2);
  not not_290 (not_290_out, F0);
  not not_291 (not_291_out, OP5);
  not not_292 (not_292_out, OP4);
  not not_293 (not_293_out, OP3);
  not not_294 (not_294_out, OP2);
  not not_295 (not_295_out, OP1);
  not not_296 (not_296_out, OP0);
  not not_297 (not_297_out, F4);
  not not_298 (not_298_out, F3);
  not not_299 (not_299_out, F1);
  not not_300 (not_300_out, F0);
  not not_301 (not_301_out, OP5);
  not not_302 (not_302_out, OP4);
  not not_303 (not_303_out, OP3);
  not not_304 (not_304_out, OP2);
  not not_305 (not_305_out, OP1);
  not not_306 (not_306_out, OP0);
  not not_307 (not_307_out, F4);
  not not_308 (not_308_out, F3);
  not not_309 (not_309_out, F1);
  not not_310 (not_310_out, OP5);
  not not_311 (not_311_out, OP4);
  not not_312 (not_312_out, OP3);
  not not_313 (not_313_out, OP2);
  not not_314 (not_314_out, OP1);
  not not_315 (not_315_out, OP0);
  not not_316 (not_316_out, F4);
  not not_317 (not_317_out, F3);
  not not_318 (not_318_out, OP5);
  not not_319 (not_319_out, OP4);
  not not_320 (not_320_out, OP3);
  not not_321 (not_321_out, OP2);
  not not_322 (not_322_out, OP1);
  not not_323 (not_323_out, OP0);
  not not_324 (not_324_out, F4);
  not not_325 (not_325_out, F2);
  not not_326 (not_326_out, F0);
  not not_327 (not_327_out, OP5);
  not not_328 (not_328_out, OP4);
  not not_329 (not_329_out, OP3);
  not not_330 (not_330_out, OP2);
  not not_331 (not_331_out, OP1);
  not not_332 (not_332_out, OP0);
  not not_333 (not_333_out, F4);
  not not_334 (not_334_out, F2);
  not not_335 (not_335_out, OP5);
  not not_336 (not_336_out, OP4);
  not not_337 (not_337_out, OP3);
  not not_338 (not_338_out, OP2);
  not not_339 (not_339_out, OP1);
  not not_340 (not_340_out, OP0);
  not not_341 (not_341_out, F5);
  not not_342 (not_342_out, F4);
  not not_343 (not_343_out, F1);
  not not_344 (not_344_out, F0);
  not not_345 (not_345_out, OP5);
  not not_346 (not_346_out, OP4);
  not not_347 (not_347_out, OP3);
  not not_348 (not_348_out, OP2);
  not not_349 (not_349_out, OP1);
  not not_350 (not_350_out, OP0);
  not not_351 (not_351_out, F4);
  not not_352 (not_352_out, F3);
  not not_353 (not_353_out, F0);
  not not_354 (not_354_out, OP5);
  not not_355 (not_355_out, OP4);
  not not_356 (not_356_out, OP3);
  not not_357 (not_357_out, OP1);
  not not_358 (not_358_out, OP0);
  not not_359 (not_359_out, OP5);
  not not_360 (not_360_out, OP4);
  not not_361 (not_361_out, OP3);
  not not_362 (not_362_out, OP1);
  not not_363 (not_363_out, OP5);
  not not_364 (not_364_out, OP4);
  not not_365 (not_365_out, OP3);
  not not_366 (not_366_out, OP2);
  not not_367 (not_367_out, OP1);
  not not_368 (not_368_out, OP0);
  not not_369 (not_369_out, F5);
  not not_370 (not_370_out, F4);
  not not_371 (not_371_out, F2);
  not not_372 (not_372_out, F1);
  not not_373 (not_373_out, F0);
  not not_374 (not_374_out, OP5);
  not not_375 (not_375_out, OP4);
  not not_376 (not_376_out, OP3);
  not not_377 (not_377_out, OP2);
  not not_378 (not_378_out, OP1);
  not not_379 (not_379_out, OP0);
  not not_380 (not_380_out, F5);
  not not_381 (not_381_out, F4);
  not not_382 (not_382_out, F2);
  not not_383 (not_383_out, F1);
  not not_384 (not_384_out, F0);
  not not_385 (not_385_out, OP5);
  not not_386 (not_386_out, OP4);
  not not_387 (not_387_out, OP3);
  not not_388 (not_388_out, OP2);
  not not_389 (not_389_out, OP0);
  not not_390 (not_390_out, OP5);
  not not_391 (not_391_out, OP4);
  not not_392 (not_392_out, OP3);
  not not_393 (not_393_out, OP2);
  not not_394 (not_394_out, OP5);
  not not_395 (not_395_out, OP4);
  not not_396 (not_396_out, OP3);
  not not_397 (not_397_out, OP2);
  and and_1 (and_1_out, OP5, not_1_out, not_2_out, not_3_out, OP1, OP0);
  and and_2 (and_2_out, OP5, not_4_out, not_5_out, not_6_out, not_7_out, not_8_out);
  and and_3 (MemWrite, OP5, not_9_out, OP3, not_10_out, OP1, OP0);
  and and_4 (and_4_out, not_11_out, not_12_out, OP3, not_13_out, not_14_out, not_15_out);
  and and_5 (and_5_out, not_16_out, not_17_out, OP3, OP2, not_18_out, not_19_out);
  and and_6 (and_6_out, not_20_out, not_21_out, OP3, not_22_out, not_23_out, OP0);
  and and_7 (and_7_out, not_24_out, not_25_out, OP3, not_26_out, OP1, not_27_out);
  and and_8 (and_8_out, not_28_out, not_29_out, OP3, OP2, not_30_out, OP0);
  and and_9 (and_9_out, OP5, not_31_out, not_32_out, not_33_out, OP1, OP0);
  and and_10 (and_10_out, OP5, not_34_out, OP3, not_35_out, OP1, OP0);
  and and_11 (and_11_out, not_36_out, not_37_out, OP3, not_38_out, OP1, OP0);
  and and_12 (and_12_out, OP5, not_39_out, not_40_out, not_41_out, not_42_out, not_43_out);
  and and_13 (and_13_out, not_44_out, not_45_out, not_46_out, not_47_out, not_48_out, not_49_out, not_50_out, not_51_out, not_52_out, not_53_out, not_54_out, not_55_out);
  and and_14 (and_14_out, not_56_out, not_57_out, not_58_out, not_59_out, not_60_out, not_61_out, not_62_out, not_63_out, not_64_out, not_65_out, F1, F0);
  and and_15 (and_15_out, not_66_out, not_67_out, not_68_out, not_69_out, not_70_out, not_71_out, not_72_out, not_73_out, not_74_out, not_75_out, F1, not_76_out);
  and and_16 (and_16_out, not_77_out, not_78_out, not_79_out, not_80_out, not_81_out, not_82_out, F5, not_83_out, not_84_out, not_85_out, not_86_out, not_87_out);
  and and_17 (and_17_out, not_88_out, not_89_out, not_90_out, not_91_out, not_92_out, not_93_out, F5, not_94_out, not_95_out, not_96_out, not_97_out, F0);
  and and_18 (and_18_out, not_98_out, not_99_out, not_100_out, not_101_out, not_102_out, not_103_out, F5, not_104_out, not_105_out, not_106_out, F1, not_107_out);
  and and_19 (and_19_out, not_108_out, not_109_out, not_110_out, not_111_out, not_112_out, not_113_out, F5, not_114_out, not_115_out, F2, not_116_out, not_117_out);
  and and_20 (and_20_out, not_118_out, not_119_out, not_120_out, not_121_out, not_122_out, not_123_out, F5, not_124_out, not_125_out, F2, not_126_out, F0);
  and and_21 (and_21_out, not_127_out, not_128_out, not_129_out, not_130_out, not_131_out, not_132_out, F5, not_133_out, not_134_out, F2, F1, F0);
  and and_22 (and_22_out, not_135_out, not_136_out, not_137_out, not_138_out, not_139_out, not_140_out, F5, not_141_out, F3, not_142_out, F1, not_143_out);
  and and_23 (and_23_out, not_144_out, not_145_out, not_146_out, not_147_out, not_148_out, not_149_out, F5, not_150_out, F3, not_151_out, F1, F0);
  and and_24 (and_24_out, not_152_out, not_153_out, not_154_out, not_155_out, OP1, OP0);
  and and_25 (and_25_out, not_156_out, not_157_out, OP3, not_158_out, not_159_out, not_160_out);
  and and_26 (and_26_out, not_161_out, not_162_out, OP3, OP2, not_163_out, not_164_out);
  and and_27 (and_27_out, not_165_out, not_166_out, OP3, not_167_out, not_168_out, OP0);
  and and_28 (and_28_out, not_169_out, not_170_out, OP3, not_171_out, OP1, not_172_out);
  and and_29 (and_29_out, not_173_out, not_174_out, OP3, OP2, not_175_out, OP0);
  and and_30 (and_30_out, OP5, not_176_out, not_177_out, not_178_out, OP1, OP0);
  and and_31 (and_31_out, not_179_out, not_180_out, not_181_out, not_182_out, not_183_out, not_184_out, F5, not_185_out, not_186_out, F2, F1, not_187_out);
  and and_32 (and_32_out, not_188_out, not_189_out, OP3, not_190_out, OP1, OP0);
  and and_33 (and_33_out, OP5, not_191_out, not_192_out, not_193_out, not_194_out, not_195_out);
  and and_34 (SysCALL, not_196_out, not_197_out, not_198_out, not_199_out, not_200_out, not_201_out, not_202_out, not_203_out, F3, F2, not_204_out, not_205_out);
  and and_35 (and_35_out, not_206_out, not_207_out, OP3, not_208_out, not_209_out, not_210_out);
  and and_36 (and_36_out, not_211_out, not_212_out, OP3, not_213_out, not_214_out, OP0);
  and and_37 (and_37_out, not_215_out, not_216_out, OP3, not_217_out, OP1, not_218_out);
  and and_38 (and_38_out, not_219_out, not_220_out, OP3, not_221_out, OP1, OP0);
  and and_39 (and_39_out, OP5, not_222_out, not_223_out, not_224_out, not_225_out, not_226_out);
  and and_40 (and_40_out, not_227_out, not_228_out, not_229_out, not_230_out, not_231_out, not_232_out, not_233_out, not_234_out, not_235_out, not_236_out, not_237_out, not_238_out);
  and and_41 (and_41_out, not_239_out, not_240_out, not_241_out, not_242_out, not_243_out, not_244_out, not_245_out, not_246_out, not_247_out, not_248_out, F1, F0);
  and and_42 (and_42_out, not_249_out, not_250_out, not_251_out, not_252_out, not_253_out, not_254_out, not_255_out, not_256_out, not_257_out, not_258_out, F1, not_259_out);
  and and_43 (and_43_out, not_260_out, not_261_out, not_262_out, not_263_out, not_264_out, not_265_out, F5, not_266_out, not_267_out, not_268_out, not_269_out, not_270_out);
  and and_44 (and_44_out, not_271_out, not_272_out, not_273_out, not_274_out, not_275_out, not_276_out, F5, not_277_out, not_278_out, not_279_out, not_280_out, F0);
  and and_45 (and_45_out, not_281_out, not_282_out, not_283_out, not_284_out, not_285_out, not_286_out, F5, not_287_out, not_288_out, not_289_out, F1, not_290_out);
  and and_46 (and_46_out, not_291_out, not_292_out, not_293_out, not_294_out, not_295_out, not_296_out, F5, not_297_out, not_298_out, F2, not_299_out, not_300_out);
  and and_47 (and_47_out, not_301_out, not_302_out, not_303_out, not_304_out, not_305_out, not_306_out, F5, not_307_out, not_308_out, F2, not_309_out, F0);
  and and_48 (and_48_out, not_310_out, not_311_out, not_312_out, not_313_out, not_314_out, not_315_out, F5, not_316_out, not_317_out, F2, F1, F0);
  and and_49 (and_49_out, not_318_out, not_319_out, not_320_out, not_321_out, not_322_out, not_323_out, F5, not_324_out, F3, not_325_out, F1, not_326_out);
  and and_50 (and_50_out, not_327_out, not_328_out, not_329_out, not_330_out, not_331_out, not_332_out, F5, not_333_out, F3, not_334_out, F1, F0);
  and and_51 (and_51_out, not_335_out, not_336_out, not_337_out, not_338_out, not_339_out, not_340_out, not_341_out, not_342_out, F3, F2, not_343_out, not_344_out);
  and and_52 (and_52_out, not_345_out, not_346_out, not_347_out, not_348_out, not_349_out, not_350_out, F5, not_351_out, not_352_out, F2, F1, not_353_out);
  and and_53 (BEQ, not_354_out, not_355_out, not_356_out, OP2, not_357_out, not_358_out);
  and and_54 (BNE, not_359_out, not_360_out, not_361_out, OP2, not_362_out, OP0);
  and and_55 (JR, not_363_out, not_364_out, not_365_out, not_366_out, not_367_out, not_368_out, not_369_out, not_370_out, F3, not_371_out, not_372_out, not_373_out);
  and and_56 (and_56_out, not_374_out, not_375_out, not_376_out, not_377_out, not_378_out, not_379_out, not_380_out, not_381_out, F3, not_382_out, not_383_out, not_384_out);
  and and_57 (and_57_out, not_385_out, not_386_out, not_387_out, not_388_out, OP1, not_389_out);
  and and_58 (and_58_out, not_390_out, not_391_out, not_392_out, not_393_out, OP1, OP0);
  and and_59 (JAL, not_394_out, not_395_out, not_396_out, not_397_out, OP1, OP0);
  or or_1 (MemToReg, and_1_out, and_2_out);
  or or_2 (ALU_SRC, and_4_out, and_5_out, and_6_out, and_7_out, and_8_out, and_9_out, and_10_out, and_11_out, and_12_out);
  or or_3 (SignedExt, and_35_out, and_36_out, and_37_out, and_38_out, and_39_out);
  or or_4 (JMP, and_56_out, and_57_out, and_58_out);
  or or_5 (RegWrite, and_13_out, and_14_out, and_15_out, and_16_out, and_17_out, and_18_out, and_19_out, and_20_out, and_21_out, and_22_out, and_23_out, and_24_out, and_25_out, and_26_out, and_27_out, and_28_out, and_29_out, and_30_out, and_31_out, and_32_out, and_33_out);
  or or_6 (RegDst, and_40_out, and_41_out, and_42_out, and_43_out, and_44_out, and_45_out, and_46_out, and_47_out, and_48_out, and_49_out, and_50_out, and_51_out, and_52_out);
endmodule

// ALU
module MIPS_ALU (
  input  [4:0] shamt,
  input  [31:0] X,
  input  [31:0] Y,
  input  [3:0] AluOP,
  output Equal,
  output [31:0] Result,
  output [31:0] Result_2
);

  wire [0:0] comparator_1_lt, comparator_2_lt;
  wire [31:0] adder_1_out, AND_out, divider_1_out, divider_1_rem, multiplier_1_cout, multiplier_1_out,
       NOR_out, OR_out, shifter_1_out, shifter_2_out, shifter_3_out, subtractor_1_out, XOR_out;

  assign AND_out = X & Y;  // AND_Gate AND, 32 bits wide
  assign OR_out = X | Y;  // OR_Gate OR, 32 bits wide
  Shifter #(.width(32)) shifter_1 (.in(Y), .\dist (shamt), .out(shifter_1_out));
  Shifter #(.width(32), .shift("ar")) shifter_2 (.in(Y), .\dist (shamt), .out(shifter_2_out));
  Shifter #(.width(32), .shift("lr")) shifter_3 (.in(Y), .\dist (shamt), .out(shifter_3_out));
  Multiplier #(.width(32)) multiplier_1 (.a(X), .b(Y), .out(multiplier_1_out), .cout(multiplier_1_cout));  // open: cin
  Divider #(.width(32)) divider_1 (.a(X), .b(Y), .out(divider_1_out), .rem(divider_1_rem));  // open: upper
  Adder #(.width(32)) adder_1 (.a(X), .b(Y), .out(adder_1_out));  // open: cin, cout
  Subtractor #(.width(32)) subtractor_1 (.a(X), .b(Y), .out(subtractor_1_out));  // open: bin, bout
  assign XOR_out = X ^ Y;  // XOR_Gate XOR, 32 bits wide
  assign NOR_out = ~(X | Y);  // NOR_Gate NOR, 32 bits wide
  Comparator #(.width(32)) comparator_1 (.a(X), .b(Y), .eq(Equal), .lt(comparator_1_lt[0]));  // open: gt
  Comparator #(.width(32), .mode("unsigned")) comparator_2 (.a(X), .b(Y), .lt(comparator_2_lt[0]));  // open: gt, eq
  Multiplexer #(.select(4), .width(32), .enable("false")) multiplexer_1 (
    .in0(shifter_1_out), .in1(shifter_2_out), .in2(shifter_3_out), .in3(multiplier_1_out),
    .in4(divider_1_out), .in5(adder_1_out), .in6(subtractor_1_out), .in7(AND_out), .in8(OR_out),
    .in9(XOR_out), .in10(NOR_out), .in11({{31{1'b0}}, comparator_1_lt[0]}),
    .in12({{31{1'b0}}, comparator_2_lt[0]}), .in13({32{1'b0}}), .in14({32{1'b0}}), .in15({32{1'b0}}),
    .out(Result), .sel(AluOP));
  Multiplexer #(.select(4), .width(32), .enable("false")) multiplexer_2 (
    .in0({32{1'b0}}), .in1({32{1'b0}}), .in2({32{1'b0}}), .in3(multiplier_1_cout), .in4(divider_1_rem),
    .in5({32{1'b0}}), .in6({32{1'b0}}), .in7({32{1'b0}}), .in8({32{1'b0}}), .in9({32{1'b0}}),
    .in10({32{1'b0}}), .in11({32{1'b0}}), .in12({32{1'b0}}), .in13({32{1'b0}}), .in14({32{1'b0}}),
    .in15({32{1'b0}}), .out(Result_2), .sel(AluOP));

  // Other names for the same wires on the sheet: Result2[31:0] = Result_2; S[3:0] = AluOP

  // Notes on the sheet:
  //   不要改变此引脚区域内容，也不要改变ALU封装形式
  //   输入引脚
  //   输出引脚
endmodule

module MIPS_Regifile (
  input  [31:0] Din,
  input  Clk,
  input  WE,
  input  [4:0] R1_num,
  input  [4:0] W_num,
  input  [4:0] R2_num,
  output [31:0] R1,
  output [31:0] R2
);

  // RegisterFile registerfile_1: pin names not known; wires that end beside it: Din, Clk, WE, W_num, R1_num, R2_num, R1, R2

  // Notes on the sheet:
  //   Sometimes, raising edge has bad competition problem in 气泡流水线. Use the FallingEdge one below!
endmodule

module \理想流水线  (
  output RegWrite,
  output MemWrite,
  output [31:0] IF_PC,
  output [31:0] ID_PC,
  output [31:0] EX_PC,
  output [31:0] M_PC,
  output [31:0] WB_PC,
  output [31:0] RDin,
  output [31:0] MDin,
  output [31:0] LedData
);

  wire AluSrc, and_2_out, and_3_out, BGEZ, BGEZ_SIGN, CLK, comparator_1_lt, Con_flag, Equal,
       ex_mem_1_equal_out, ex_mem_1_jal_out, ex_mem_1_lb_out, ex_mem_1_memtoreg_out, ex_mem_1_regdst_out,
       ex_mem_1_regwrite_out, ex_mem_1_syscall_out, Go, id_ex_1_beq_out, id_ex_1_bne_out, id_ex_1_jal_out,
       id_ex_1_lb_out, id_ex_1_memtoreg_out, id_ex_1_memwrite_out, id_ex_1_regdst_out, id_ex_1_regwrite_out,
       IR1, IR2, IR3, J, JMP, JR, mem_wb_1_equal_out, mem_wb_1_jal_out, mem_wb_1_memtoreg_out,
       mem_wb_1_regdst_out, mem_wb_1_syscall_out, multiplexer_4_out, not_1_out, not_2_out, not_3_out,
       not_4_out, Pause, RST, Show, SignExt, Syscall, W1, W2, W3, Write, \单周期硬布线控制器_1_alu_src ,
       \单周期硬布线控制器_1_beq , \单周期硬布线控制器_1_bgez , \单周期硬布线控制器_1_bne , \单周期硬布线控制器_1_jal , \单周期硬布线控制器_1_jmp ,
       \单周期硬布线控制器_1_jr , \单周期硬布线控制器_1_lb , \单周期硬布线控制器_1_memtoreg , \单周期硬布线控制器_1_memwrite ,
       \单周期硬布线控制器_1_regdst , \单周期硬布线控制器_1_regwrite , \单周期硬布线控制器_1_syscall ;
  wire [3:0] id_ex_1_aluop_out, \单周期硬布线控制器_1_alu_op ;
  wire [4:0] multiplexer_5_out, multiplexer_6_out, multiplexer_10_out, W_num;
  wire [15:0] \LoadUse次数 , \总周期数 , \插入气泡数 , \无条件分支数 , \条件分支成功数 ;
  wire [27:0] shifter_3_out;
  wire [31:0] adder_1_out, adder_3_out, BGEZ_PC, bit_extender_1_out, bit_extender_2_out,
       ex_mem_1_aluresult_out, ex_mem_1_ir_out, ex_mem_1_pc_out, if_id_1_ir_out, if_id_1_pc_out, Immediate,
       IR, mem_wb_1_aluresult_out, mem_wb_1_ir_out, mem_wb_1_memorydata_out, mem_wb_1_pc_out,
       mips_alu_1_result, mips_probe_1_p1, mips_regifile_1_r1, mips_regifile_1_r2, multiplexer_1_out,
       multiplexer_2_out, multiplexer_3_out, multiplexer_7_out, multiplexer_8_out, multiplexer_9_out,
       multiplexer_12_out, PC_add4, R1, R2, ram_1_data, shifter_1_out, shifter_2_out;

  Button \u_总复位  (.out(RST));
  Button _1 (.out(IR1));
  Button _2 (.out(IR2));
  Button _3 (.out(IR3));
  Button \u_继续运行  (.out(Go));
  LED led_1 (.in(W1));
  LED led_2 (.in(W2));
  LED led_3 (.in(W3));
  Comparator #(.width(32)) comparator_1 (.a(R1), .b({32{1'b0}}), .lt(comparator_1_lt));  // open: gt, eq
  nand nand_1 (Write, not_2_out, Pause);
  Multiplexer #(.width(32), .enable("false")) multiplexer_1 (
    .in0(adder_3_out), .in1(adder_1_out), .out(multiplexer_1_out), .sel(Con_flag));
  Shifter #(.width(32)) shifter_1 (.in(Immediate), .\dist (5'b00010), .out(shifter_1_out));
  Hex_Digit_Display hex_digit_display_1 (.value(LedData[31:28]));  // open: dp
  not not_1 (not_1_out, comparator_1_lt);
  Shifter #(.width(32)) shifter_2 (.in(Immediate), .\dist (5'b00010), .out(shifter_2_out));
  not not_2 (not_2_out, Go);
  Multiplexer #(.select(2), .width(32), .enable("false")) multiplexer_2 (
    .in0(multiplexer_1_out), .in1(R1), .in2({PC_add4[31:28], shifter_3_out}), .in3(R1),
    .out(multiplexer_2_out), .sel({JMP, JR}));
  Multiplexer #(.width(32), .enable("false")) multiplexer_3 (
    .in0(multiplexer_2_out), .in1(BGEZ_PC), .out(multiplexer_3_out), .sel(BGEZ_SIGN));
  Adder #(.width(32)) adder_1 (.a(shifter_1_out), .b(PC_add4), .out(adder_1_out));  // open: cin, cout
  Hex_Digit_Display hex_digit_display_2 (.value(LedData[27:24]));  // open: dp
  Hex_Digit_Display hex_digit_display_3 (.value(LedData[23:20]));  // open: dp
  and and_1 (BGEZ_SIGN, not_1_out, BGEZ);
  Adder #(.width(32)) adder_2 (.a(shifter_2_out), .b(PC_add4), .out(BGEZ_PC));  // open: cin, cout
  Shifter #(.width(28)) shifter_3 (.in(IR[27:0]), .\dist (5'b00010), .out(shifter_3_out));
  Hex_Digit_Display hex_digit_display_4 (.value(LedData[15:12]));  // open: dp
  Hex_Digit_Display hex_digit_display_5 (.value(LedData[19:16]));  // open: dp
  Multiplexer #(.enable("false")) multiplexer_4 (.in0(1'b1), .in1(Go), .out(multiplexer_4_out), .sel(Pause));
  Register #(.width(32)) PC (.D(multiplexer_3_out), .en(multiplexer_4_out), .Q(IF_PC), .clk(CLK), .clr(RST));
  Hex_Digit_Display hex_digit_display_6 (.value(LedData[7:4]));  // open: dp
  Hex_Digit_Display hex_digit_display_7 (.value(LedData[11:8]));  // open: dp
  Clock clock_1 (.out(CLK));
  Counter #(.width(16), .max('hffff)) counter_1 (
    .load(1'b0), .count(multiplexer_4_out), .Q(\总周期数 ), .clk(CLK), .clr(RST));  // open: D, carry
  Hex_Digit_Display hex_digit_display_8 (.value(LedData[3:0]));  // open: dp
  Register #(.width(32)) register_1 (.D(R2), .Q(LedData), .clk(Show), .clr(RST));  // open: en
  Adder #(.width(32)) adder_3 (.a(IF_PC), .b(32'h4), .out(adder_3_out));  // open: cin, cout
  // Probe on \总周期数 
  // Mips_Probe mips_probe_1: pin names not known; wires that end beside it: mips_probe_1_p1
  ROM #(.addrWidth(10), .dataWidth(32)) rom_1 (.addr(IF_PC[11:2]), .data(mips_probe_1_p1));  // open: sel
  // Probe on \总周期数 
  // Probe on \无条件分支数 
  // Probe on \条件分支成功数 
  // Probe on \插入气泡数 
  // Probe on \LoadUse次数 
  IF_ID if_id_1 (
    .IR_in(mips_probe_1_p1), .PC_in(adder_3_out), .\气泡_高电平时有效 (J), .clk(CLK), .clear(RST), .enable(Write),
    .IR_out(if_id_1_ir_out), .PC_out(if_id_1_pc_out), .OldPC_in(IF_PC), .OldPC_out(ID_PC));
  // Probe on IF_PC[11:0]
  // Probe on ID_PC[11:0]
  // Probe on EX_PC[11:0]
  \单周期硬布线控制器  \u_单周期硬布线控制器_1  (
    .Func(if_id_1_ir_out[5:0]), .OP(if_id_1_ir_out[31:26]), .ALU_OP(\单周期硬布线控制器_1_alu_op ),
    .MemToReg(\单周期硬布线控制器_1_memtoreg ), .MemWrite(\单周期硬布线控制器_1_memwrite ), .ALU_SRC(\单周期硬布线控制器_1_alu_src ),
    .RegWrite(\单周期硬布线控制器_1_regwrite ), .SysCALL(\单周期硬布线控制器_1_syscall ), .SignedExt(SignExt),
    .RegDst(\单周期硬布线控制器_1_regdst ), .JR(\单周期硬布线控制器_1_jr ), .JMP(\单周期硬布线控制器_1_jmp ), .Beq(\单周期硬布线控制器_1_beq ),
    .JAL(\单周期硬布线控制器_1_jal ), .Bne(\单周期硬布线控制器_1_bne ), .LB(\单周期硬布线控制器_1_lb ), .BGEZ(\单周期硬布线控制器_1_bgez ));
  Multiplexer #(.width(5), .enable("false")) multiplexer_5 (
    .in0(if_id_1_ir_out[25:21]), .in1(5'b00010), .out(multiplexer_5_out), .sel(\单周期硬布线控制器_1_syscall ));
  Multiplexer #(.width(5), .enable("false")) multiplexer_6 (
    .in0(if_id_1_ir_out[20:16]), .in1(5'b00100), .out(multiplexer_6_out), .sel(\单周期硬布线控制器_1_syscall ));
  // Probe on W_num
  assign bit_extender_1_out = {{16{1'b0}}, if_id_1_ir_out[15:0]};  // Bit_Extender bit_extender_1
  assign bit_extender_2_out = {{16{if_id_1_ir_out[15]}}, if_id_1_ir_out[15:0]};  // Bit_Extender bit_extender_2
  // Probe on M_PC[11:0]
  Multiplexer #(.width(32), .enable("false")) multiplexer_7 (
    .in0(bit_extender_1_out), .in1(bit_extender_2_out), .out(multiplexer_7_out), .sel(SignExt));
  // Probe on WB_PC[11:0]
  MIPS_Regifile mips_regifile_1 (
    .Din(RDin), .Clk(CLK), .R1(mips_regifile_1_r1), .R2(mips_regifile_1_r2), .WE(RegWrite), .W_num(W_num),
    .R1_num(multiplexer_5_out), .R2_num(multiplexer_6_out));
  ID_EX id_ex_1 (
    .Beq_in(\单周期硬布线控制器_1_beq ), .Bne_in(\单周期硬布线控制器_1_bne ), .MemToReg_in(\单周期硬布线控制器_1_memtoreg ),
    .MemWrite_in(\单周期硬布线控制器_1_memwrite ), .AluOP_in(\单周期硬布线控制器_1_alu_op ), .AluSrc_in(\单周期硬布线控制器_1_alu_src ),
    .RegWrite_in(\单周期硬布线控制器_1_regwrite ), .JAL_in(\单周期硬布线控制器_1_jal ), .RegDst_in(\单周期硬布线控制器_1_regdst ),
    .Syscall_in(\单周期硬布线控制器_1_syscall ), .JMP_in(\单周期硬布线控制器_1_jmp ), .JR_in(\单周期硬布线控制器_1_jr ),
    .SignedExt_in(SignExt), .LB_in(\单周期硬布线控制器_1_lb ), .BGEZ_in(\单周期硬布线控制器_1_bgez ), .IR_in(if_id_1_ir_out),
    .PC_in(if_id_1_pc_out), .R1_in(mips_regifile_1_r1), .R2_in(mips_regifile_1_r2),
    .Imm_in(multiplexer_7_out), .Beq_out(id_ex_1_beq_out), .Bne_out(id_ex_1_bne_out),
    .MemToReg_out(id_ex_1_memtoreg_out), .MemWrite_out(id_ex_1_memwrite_out), .AluOP_out(id_ex_1_aluop_out),
    .AluSrc_out(AluSrc), .RegWrite_out(id_ex_1_regwrite_out), .JAL_out(id_ex_1_jal_out),
    .RegDst_out(id_ex_1_regdst_out), .Syscall_out(Syscall), .JMP_out(JMP), .JR_out(JR),
    .LB_out(id_ex_1_lb_out), .BGEZ_out(BGEZ), .IR_out(IR), .PC_out(PC_add4), .R1_out(R1), .R2_out(R2),
    .Imm_out(Immediate), .clk(CLK), .clear(RST), .enable(Write), .\气泡_高电平时有效 (J), .OldPC_in(ID_PC),
    .OldPC_out(EX_PC));  // open: SignedExt_out
  Multiplexer #(.width(32), .enable("false")) multiplexer_8 (
    .in0(R2), .in1(Immediate), .out(multiplexer_8_out), .sel(AluSrc));
  and and_2 (and_2_out, Equal, id_ex_1_beq_out);
  not not_3 (not_3_out, Equal);
  and and_3 (and_3_out, not_3_out, id_ex_1_bne_out);
  Multiplexer #(.width(32), .enable("false")) multiplexer_9 (
    .in0(multiplexer_8_out), .in1(32'h22), .out(multiplexer_9_out), .sel(Syscall));
  or or_1 (Con_flag, BGEZ, and_2_out, and_3_out);
  MIPS_ALU mips_alu_1 (
    .X(R1), .Y(multiplexer_9_out), .AluOP(id_ex_1_aluop_out), .Equal(Equal), .Result(mips_alu_1_result),
    .shamt(IR[10:6]));  // open: Result_2
  Counter #(.width(16), .max('hffff)) counter_2 (
    .load(1'b0), .count(Con_flag), .Q(\条件分支成功数 ), .clk(CLK), .clr(RST));  // open: D, carry
  Counter #(.width(16), .max('hffff)) counter_3 (
    .load(1'b0), .count(JMP), .Q(\无条件分支数 ), .clk(CLK), .clr(RST));  // open: D, carry
  or or_2 (J, JMP, JR, Con_flag);
  EX_MEM ex_mem_1 (
    .\气泡_高电平时有效 (1'b0), .clk(CLK), .clear(RST), .enable(Write), .MemToReg_in(id_ex_1_memtoreg_out),
    .MemToReg_out(ex_mem_1_memtoreg_out), .MemWrite_in(id_ex_1_memwrite_out), .MemWrite_out(MemWrite),
    .RegWrite_in(id_ex_1_regwrite_out), .RegWrite_out(ex_mem_1_regwrite_out), .JAL_in(id_ex_1_jal_out),
    .JAL_out(ex_mem_1_jal_out), .LB_in(id_ex_1_lb_out), .LB_out(ex_mem_1_lb_out), .IR_in(IR),
    .IR_out(ex_mem_1_ir_out), .PC_in(PC_add4), .PC_out(ex_mem_1_pc_out), .ALUResult_in(mips_alu_1_result),
    .ALUResult_out(ex_mem_1_aluresult_out), .R2_in(R2), .R2_out(MDin), .RegDst_in(id_ex_1_regdst_out),
    .RegDst_out(ex_mem_1_regdst_out), .Syscall_in(Syscall), .Syscall_out(ex_mem_1_syscall_out),
    .equal_in(Equal), .equal_out(ex_mem_1_equal_out), .OldPC_in(EX_PC), .OldPC_out(M_PC));  // open: pause_in, pause_out
  RAM #(.addrWidth(10), .dataWidth(32), .bus("separate")) ram_1 (
    .addr(ex_mem_1_aluresult_out[11:2]), .din(MDin), .data(ram_1_data), .str(MemWrite), .clk(CLK), .clr(RST));  // open: sel, ld
  MEM_WB mem_wb_1 (
    .\气泡_高电平时有效 (1'b0), .clk(CLK), .clear(RST), .enable(Write), .MemToReg_in(ex_mem_1_memtoreg_out),
    .MemToReg_out(mem_wb_1_memtoreg_out), .MemWrite_in(MemWrite), .RegWrite_in(ex_mem_1_regwrite_out),
    .RegWrite_out(RegWrite), .JAL_in(ex_mem_1_jal_out), .JAL_out(mem_wb_1_jal_out), .LB_in(ex_mem_1_lb_out),
    .IR_in(ex_mem_1_ir_out), .IR_out(mem_wb_1_ir_out), .PC_in(ex_mem_1_pc_out), .PC_out(mem_wb_1_pc_out),
    .ALUResult_in(ex_mem_1_aluresult_out), .ALUResult_out(mem_wb_1_aluresult_out),
    .Memorydata_in(ram_1_data), .Memorydata_out(mem_wb_1_memorydata_out), .RegDst_in(ex_mem_1_regdst_out),
    .RegDst_out(mem_wb_1_regdst_out), .Syscall_in(ex_mem_1_syscall_out), .Syscall_out(mem_wb_1_syscall_out),
    .equal_in(ex_mem_1_equal_out), .equal_out(mem_wb_1_equal_out), .OldPC_in(M_PC), .OldPC_out(WB_PC));  // open: MemWrite_out, LB_out, pause_in, pause_out
  and and_4 (Show, Syscall, mem_wb_1_equal_out);
  not not_4 (not_4_out, mem_wb_1_equal_out);
  and and_5 (Pause, mem_wb_1_syscall_out, not_4_out);
  Multiplexer #(.width(5), .enable("false")) multiplexer_10 (
    .in0(mem_wb_1_ir_out[20:16]), .in1(mem_wb_1_ir_out[15:11]), .out(multiplexer_10_out),
    .sel(mem_wb_1_regdst_out));
  Multiplexer #(.width(5), .enable("false")) multiplexer_11 (
    .in0(multiplexer_10_out), .in1({5{1'b1}}), .out(W_num), .sel(mem_wb_1_jal_out));
  Multiplexer #(.width(32), .enable("false")) multiplexer_12 (
    .in0(mem_wb_1_aluresult_out), .in1(mem_wb_1_memorydata_out), .out(multiplexer_12_out),
    .sel(mem_wb_1_memtoreg_out));
  Multiplexer #(.width(32), .enable("false")) multiplexer_13 (
    .in0(multiplexer_12_out), .in1(mem_wb_1_pc_out), .out(RDin), .sel(mem_wb_1_jal_out));

  // Other names for the same wires on the sheet: MEM_PC[31:0] = M_PC; MemWrite_grade = MemWrite;
  //   RDin_mon[31:0] = RDin

  // Notes on the sheet:
  //   中断源
  //   中断等待指示
  //   数码管输出
  //   contents of rom_1 (hex, n*v repeats v):
  //   20100000 20110000 20120000 20130000 36100000 36310001 36520002 36730003 ae100000 ae110004 ae120008
  //   ae13000c 2002000a 20110000 20120000 20130000 c
  //   OP
  //   Func
  //   OP
  //   Func
  //   流水调试日志用
  //   为方便自动评测，需要输出流水线各段保存的PC值，注意是PC不是PC+4，另外ID段寄存器写入信息，Mem段内存写入信息也要输出
endmodule

// 源寄存器使用情况
module \源寄存器使用情况  (
  input  OP0,
  input  OP1,
  input  OP2,
  input  OP3,
  input  OP4,
  input  OP5,
  input  F0,
  input  F1,
  input  F2,
  input  F3,
  input  F4,
  input  F5,
  output R1_Used,
  output R2_Used
);

  wire and_1_out, and_2_out, and_3_out, and_4_out, and_5_out, and_6_out, and_7_out, and_8_out, and_9_out,
       and_10_out, and_11_out, and_12_out, and_13_out, and_14_out, and_15_out, and_16_out, and_17_out,
       and_18_out, and_19_out, and_20_out, and_21_out, and_22_out, and_23_out, and_24_out, and_25_out,
       and_26_out, and_27_out, and_28_out, and_29_out, and_30_out, and_31_out, and_32_out, and_33_out,
       and_34_out, and_35_out, and_36_out, and_37_out, and_38_out, and_39_out, and_40_out, and_41_out,
       and_42_out, and_43_out, and_44_out, not_1_out, not_2_out, not_3_out, not_4_out, not_5_out, not_6_out,
       not_7_out, not_8_out, not_9_out, not_10_out, not_11_out, not_12_out, not_13_out, not_14_out,
       not_15_out, not_16_out, not_17_out, not_18_out, not_19_out, not_20_out, not_21_out, not_22_out,
       not_23_out, not_24_out, not_25_out, not_26_out, not_27_out, not_28_out, not_29_out, not_30_out,
       not_31_out, not_32_out, not_33_out, not_34_out, not_35_out, not_36_out, not_37_out, not_38_out,
       not_39_out, not_40_out, not_41_out, not_42_out, not_43_out, not_44_out, not_45_out, not_46_out,
       not_47_out, not_48_out, not_49_out, not_50_out, not_51_out, not_52_out, not_53_out, not_54_out,
       not_55_out, not_56_out, not_57_out, not_58_out, not_59_out, not_60_out, not_61_out, not_62_out,
       not_63_out, not_64_out, not_65_out, not_66_out, not_67_out, not_68_out, not_69_out, not_70_out,
       not_71_out, not_72_out, not_73_out, not_74_out, not_75_out, not_76_out, not_77_out, not_78_out,
       not_79_out, not_80_out, not_81_out, not_82_out, not_83_out, not_84_out, not_85_out, not_86_out,
       not_87_out, not_88_out, not_89_out, not_90_out, not_91_out, not_92_out, not_93_out, not_94_out,
       not_95_out, not_96_out, not_97_out, not_98_out, not_99_out, not_100_out, not_101_out, not_102_out,
       not_103_out, not_104_out, not_105_out, not_106_out, not_107_out, not_108_out, not_109_out,
       not_110_out, not_111_out, not_112_out, not_113_out, not_114_out, not_115_out, not_116_out,
       not_117_out, not_118_out, not_119_out, not_120_out, not_121_out, not_122_out, not_123_out,
       not_124_out, not_125_out, not_126_out, not_127_out, not_128_out, not_129_out, not_130_out,
       not_131_out, not_132_out, not_133_out, not_134_out, not_135_out, not_136_out, not_137_out,
       not_138_out, not_139_out, not_140_out, not_141_out, not_142_out, not_143_out, not_144_out,
       not_145_out, not_146_out, not_147_out, not_148_out, not_149_out, not_150_out, not_151_out,
       not_152_out, not_153_out, not_154_out, not_155_out, not_156_out, not_157_out, not_158_out,
       not_159_out, not_160_out, not_161_out, not_162_out, not_163_out, not_164_out, not_165_out,
       not_166_out, not_167_out, not_168_out, not_169_out, not_170_out, not_171_out, not_172_out,
       not_173_out, not_174_out, not_175_out, not_176_out, not_177_out, not_178_out, not_179_out,
       not_180_out, not_181_out, not_182_out, not_183_out, not_184_out, not_185_out, not_186_out,
       not_187_out, not_188_out, not_189_out, not_190_out, not_191_out, not_192_out, not_193_out,
       not_194_out, not_195_out, not_196_out, not_197_out, not_198_out, not_199_out, not_200_out,
       not_201_out, not_202_out, not_203_out, not_204_out, not_205_out, not_206_out, not_207_out,
       not_208_out, not_209_out, not_210_out, not_211_out, not_212_out, not_213_out, not_214_out,
       not_215_out, not_216_out, not_217_out, not_218_out, not_219_out, not_220_out, not_221_out,
       not_222_out, not_223_out, not_224_out, not_225_out, not_226_out, not_227_out, not_228_out,
       not_229_out, not_230_out, not_231_out, not_232_out, not_233_out, not_234_out, not_235_out,
       not_236_out, not_237_out, not_238_out, not_239_out, not_240_out, not_241_out, not_242_out,
       not_243_out, not_244_out, not_245_out, not_246_out, not_247_out, not_248_out, not_249_out,
       not_250_out, not_251_out, not_252_out, not_253_out, not_254_out, not_255_out, not_256_out,
       not_257_out, not_258_out, not_259_out, not_260_out, not_261_out, not_262_out, not_263_out,
       not_264_out, not_265_out, not_266_out, not_267_out, not_268_out, not_269_out, not_270_out,
       not_271_out, not_272_out, not_273_out, not_274_out, not_275_out, not_276_out, not_277_out,
       not_278_out, not_279_out, not_280_out, not_281_out, not_282_out, not_283_out, not_284_out,
       not_285_out, not_286_out, not_287_out, not_288_out, not_289_out, not_290_out, not_291_out,
       not_292_out, not_293_out, not_294_out, not_295_out, not_296_out, not_297_out, not_298_out,
       not_299_out, not_300_out, not_301_out, not_302_out, not_303_out, not_304_out, not_305_out,
       not_306_out, not_307_out, not_308_out, not_309_out, not_310_out, not_311_out, not_312_out,
       not_313_out, not_314_out, not_315_out, not_316_out, not_317_out, not_318_out, not_319_out,
       not_320_out, not_321_out, not_322_out, not_323_out, not_324_out, not_325_out, not_326_out,
       not_327_out, not_328_out, not_329_out, not_330_out, not_331_out;

  not not_1 (not_1_out, OP5);
  not not_2 (not_2_out, OP4);
  not not_3 (not_3_out, OP3);
  not not_4 (not_4_out, OP2);
  not not_5 (not_5_out, OP1);
  not not_6 (not_6_out, OP0);
  not not_7 (not_7_out, F5);
  not not_8 (not_8_out, F4);
  not not_9 (not_9_out, F3);
  not not_10 (not_10_out, F2);
  not not_11 (not_11_out, F1);
  not not_12 (not_12_out, F0);
  not not_13 (not_13_out, OP5);
  not not_14 (not_14_out, OP4);
  not not_15 (not_15_out, OP3);
  not not_16 (not_16_out, OP2);
  not not_17 (not_17_out, OP1);
  not not_18 (not_18_out, OP0);
  not not_19 (not_19_out, F5);
  not not_20 (not_20_out, F4);
  not not_21 (not_21_out, F3);
  not not_22 (not_22_out, F2);
  not not_23 (not_23_out, OP5);
  not not_24 (not_24_out, OP4);
  not not_25 (not_25_out, OP3);
  not not_26 (not_26_out, OP2);
  not not_27 (not_27_out, OP1);
  not not_28 (not_28_out, OP0);
  not not_29 (not_29_out, F5);
  not not_30 (not_30_out, F4);
  not not_31 (not_31_out, F3);
  not not_32 (not_32_out, F2);
  not not_33 (not_33_out, F0);
  not not_34 (not_34_out, OP5);
  not not_35 (not_35_out, OP4);
  not not_36 (not_36_out, OP3);
  not not_37 (not_37_out, OP2);
  not not_38 (not_38_out, OP1);
  not not_39 (not_39_out, OP0);
  not not_40 (not_40_out, F4);
  not not_41 (not_41_out, F3);
  not not_42 (not_42_out, F2);
  not not_43 (not_43_out, F1);
  not not_44 (not_44_out, F0);
  not not_45 (not_45_out, OP5);
  not not_46 (not_46_out, OP4);
  not not_47 (not_47_out, OP3);
  not not_48 (not_48_out, OP2);
  not not_49 (not_49_out, OP1);
  not not_50 (not_50_out, OP0);
  not not_51 (not_51_out, F4);
  not not_52 (not_52_out, F3);
  not not_53 (not_53_out, F2);
  not not_54 (not_54_out, F1);
  not not_55 (not_55_out, OP5);
  not not_56 (not_56_out, OP4);
  not not_57 (not_57_out, OP3);
  not not_58 (not_58_out, OP2);
  not not_59 (not_59_out, OP1);
  not not_60 (not_60_out, OP0);
  not not_61 (not_61_out, F4);
  not not_62 (not_62_out, F3);
  not not_63 (not_63_out, F2);
  not not_64 (not_64_out, F0);
  not not_65 (not_65_out, OP5);
  not not_66 (not_66_out, OP4);
  not not_67 (not_67_out, OP3);
  not not_68 (not_68_out, OP2);
  not not_69 (not_69_out, OP1);
  not not_70 (not_70_out, OP0);
  not not_71 (not_71_out, F4);
  not not_72 (not_72_out, F3);
  not not_73 (not_73_out, F1);
  not not_74 (not_74_out, F0);
  not not_75 (not_75_out, OP5);
  not not_76 (not_76_out, OP4);
  not not_77 (not_77_out, OP3);
  not not_78 (not_78_out, OP2);
  not not_79 (not_79_out, OP1);
  not not_80 (not_80_out, OP0);
  not not_81 (not_81_out, F4);
  not not_82 (not_82_out, F3);
  not not_83 (not_83_out, F1);
  not not_84 (not_84_out, OP5);
  not not_85 (not_85_out, OP4);
  not not_86 (not_86_out, OP3);
  not not_87 (not_87_out, OP2);
  not not_88 (not_88_out, OP1);
  not not_89 (not_89_out, OP0);
  not not_90 (not_90_out, F4);
  not not_91 (not_91_out, F3);
  not not_92 (not_92_out, OP5);
  not not_93 (not_93_out, OP4);
  not not_94 (not_94_out, OP3);
  not not_95 (not_95_out, OP2);
  not not_96 (not_96_out, OP1);
  not not_97 (not_97_out, OP0);
  not not_98 (not_98_out, F4);
  not not_99 (not_99_out, F2);
  not not_100 (not_100_out, F0);
  not not_101 (not_101_out, OP5);
  not not_102 (not_102_out, OP4);
  not not_103 (not_103_out, OP3);
  not not_104 (not_104_out, OP2);
  not not_105 (not_105_out, OP1);
  not not_106 (not_106_out, OP0);
  not not_107 (not_107_out, F4);
  not not_108 (not_108_out, F2);
  not not_109 (not_109_out, OP5);
  not not_110 (not_110_out, OP4);
  not not_111 (not_111_out, OP3);
  not not_112 (not_112_out, OP2);
  not not_113 (not_113_out, OP1);
  not not_114 (not_114_out, OP0);
  not not_115 (not_115_out, F5);
  not not_116 (not_116_out, F4);
  not not_117 (not_117_out, F2);
  not not_118 (not_118_out, F1);
  not not_119 (not_119_out, F0);
  not not_120 (not_120_out, OP5);
  not not_121 (not_121_out, OP4);
  not not_122 (not_122_out, OP3);
  not not_123 (not_123_out, OP2);
  not not_124 (not_124_out, OP1);
  not not_125 (not_125_out, OP0);
  not not_126 (not_126_out, F5);
  not not_127 (not_127_out, F4);
  not not_128 (not_128_out, F1);
  not not_129 (not_129_out, F0);
  not not_130 (not_130_out, OP5);
  not not_131 (not_131_out, OP4);
  not not_132 (not_132_out, OP3);
  not not_133 (not_133_out, OP1);
  not not_134 (not_134_out, OP0);
  not not_135 (not_135_out, OP5);
  not not_136 (not_136_out, OP4);
  not not_137 (not_137_out, OP3);
  not not_138 (not_138_out, OP1);
  not not_139 (not_139_out, OP5);
  not not_140 (not_140_out, OP4);
  not not_141 (not_141_out, OP2);
  not not_142 (not_142_out, OP1);
  not not_143 (not_143_out, OP0);
  not not_144 (not_144_out, OP5);
  not not_145 (not_145_out, OP4);
  not not_146 (not_146_out, OP1);
  not not_147 (not_147_out, OP0);
  not not_148 (not_148_out, OP5);
  not not_149 (not_149_out, OP4);
  not not_150 (not_150_out, OP2);
  not not_151 (not_151_out, OP1);
  not not_152 (not_152_out, OP5);
  not not_153 (not_153_out, OP4);
  not not_154 (not_154_out, OP2);
  not not_155 (not_155_out, OP0);
  not not_156 (not_156_out, OP5);
  not not_157 (not_157_out, OP4);
  not not_158 (not_158_out, OP1);
  not not_159 (not_159_out, OP4);
  not not_160 (not_160_out, OP3);
  not not_161 (not_161_out, OP2);
  not not_162 (not_162_out, OP4);
  not not_163 (not_163_out, OP2);
  not not_164 (not_164_out, OP5);
  not not_165 (not_165_out, OP4);
  not not_166 (not_166_out, OP3);
  not not_167 (not_167_out, OP2);
  not not_168 (not_168_out, OP1);
  not not_169 (not_169_out, OP0);
  not not_170 (not_170_out, F4);
  not not_171 (not_171_out, F3);
  not not_172 (not_172_out, F0);
  not not_173 (not_173_out, OP5);
  not not_174 (not_174_out, OP4);
  not not_175 (not_175_out, OP2);
  not not_176 (not_176_out, OP4);
  not not_177 (not_177_out, OP3);
  not not_178 (not_178_out, OP2);
  not not_179 (not_179_out, OP1);
  not not_180 (not_180_out, OP0);
  not not_181 (not_181_out, OP5);
  not not_182 (not_182_out, OP4);
  not not_183 (not_183_out, OP3);
  not not_184 (not_184_out, OP2);
  not not_185 (not_185_out, OP1);
  not not_186 (not_186_out, OP5);
  not not_187 (not_187_out, OP4);
  not not_188 (not_188_out, OP3);
  not not_189 (not_189_out, OP2);
  not not_190 (not_190_out, OP1);
  not not_191 (not_191_out, OP0);
  not not_192 (not_192_out, F5);
  not not_193 (not_193_out, F4);
  not not_194 (not_194_out, F3);
  not not_195 (not_195_out, F2);
  not not_196 (not_196_out, F1);
  not not_197 (not_197_out, F0);
  not not_198 (not_198_out, OP5);
  not not_199 (not_199_out, OP4);
  not not_200 (not_200_out, OP3);
  not not_201 (not_201_out, OP2);
  not not_202 (not_202_out, OP1);
  not not_203 (not_203_out, OP0);
  not not_204 (not_204_out, F5);
  not not_205 (not_205_out, F4);
  not not_206 (not_206_out, F3);
  not not_207 (not_207_out, F2);
  not not_208 (not_208_out, OP5);
  not not_209 (not_209_out, OP4);
  not not_210 (not_210_out, OP3);
  not not_211 (not_211_out, OP2);
  not not_212 (not_212_out, OP1);
  not not_213 (not_213_out, OP0);
  not not_214 (not_214_out, F5);
  not not_215 (not_215_out, F4);
  not not_216 (not_216_out, F3);
  not not_217 (not_217_out, F2);
  not not_218 (not_218_out, F0);
  not not_219 (not_219_out, OP5);
  not not_220 (not_220_out, OP4);
  not not_221 (not_221_out, OP3);
  not not_222 (not_222_out, OP2);
  not not_223 (not_223_out, OP1);
  not not_224 (not_224_out, OP0);
  not not_225 (not_225_out, F4);
  not not_226 (not_226_out, F3);
  not not_227 (not_227_out, F2);
  not not_228 (not_228_out, F1);
  not not_229 (not_229_out, F0);
  not not_230 (not_230_out, OP5);
  not not_231 (not_231_out, OP4);
  not not_232 (not_232_out, OP3);
  not not_233 (not_233_out, OP2);
  not not_234 (not_234_out, OP1);
  not not_235 (not_235_out, OP0);
  not not_236 (not_236_out, F4);
  not not_237 (not_237_out, F3);
  not not_238 (not_238_out, F2);
  not not_239 (not_239_out, F1);
  not not_240 (not_240_out, OP5);
  not not_241 (not_241_out, OP4);
  not not_242 (not_242_out, OP3);
  not not_243 (not_243_out, OP2);
  not not_244 (not_244_out, OP1);
  not not_245 (not_245_out, OP0);
  not not_246 (not_246_out, F4);
  not not_247 (not_247_out, F3);
  not not_248 (not_248_out, F2);
  not not_249 (not_249_out, F0);
  not not_250 (not_250_out, OP5);
  not not_251 (not_251_out, OP4);
  not not_252 (not_252_out, OP3);
  not not_253 (not_253_out, OP2);
  not not_254 (not_254_out, OP1);
  not not_255 (not_255_out, OP0);
  not not_256 (not_256_out, F4);
  not not_257 (not_257_out, F3);
  not not_258 (not_258_out, F1);
  not not_259 (not_259_out, F0);
  not not_260 (not_260_out, OP5);
  not not_261 (not_261_out, OP4);
  not not_262 (not_262_out, OP3);
  not not_263 (not_263_out, OP2);
  not not_264 (not_264_out, OP1);
  not not_265 (not_265_out, OP0);
  not not_266 (not_266_out, F4);
  not not_267 (not_267_out, F3);
  not not_268 (not_268_out, F1);
  not not_269 (not_269_out, OP5);
  not not_270 (not_270_out, OP4);
  not not_271 (not_271_out, OP3);
  not not_272 (not_272_out, OP2);
  not not_273 (not_273_out, OP1);
  not not_274 (not_274_out, OP0);
  not not_275 (not_275_out, F4);
  not not_276 (not_276_out, F3);
  not not_277 (not_277_out, OP5);
  not not_278 (not_278_out, OP4);
  not not_279 (not_279_out, OP3);
  not not_280 (not_280_out, OP2);
  not not_281 (not_281_out, OP1);
  not not_282 (not_282_out, OP0);
  not not_283 (not_283_out, F4);
  not not_284 (not_284_out, F2);
  not not_285 (not_285_out, F0);
  not not_286 (not_286_out, OP5);
  not not_287 (not_287_out, OP4);
  not not_288 (not_288_out, OP3);
  not not_289 (not_289_out, OP2);
  not not_290 (not_290_out, OP1);
  not not_291 (not_291_out, OP0);
  not not_292 (not_292_out, F4);
  not not_293 (not_293_out, F2);
  not not_294 (not_294_out, OP5);
  not not_295 (not_295_out, OP4);
  not not_296 (not_296_out, OP3);
  not not_297 (not_297_out, OP2);
  not not_298 (not_298_out, OP1);
  not not_299 (not_299_out, OP0);
  not not_300 (not_300_out, F5);
  not not_301 (not_301_out, F4);
  not not_302 (not_302_out, F1);
  not not_303 (not_303_out, F0);
  not not_304 (not_304_out, OP5);
  not not_305 (not_305_out, OP4);
  not not_306 (not_306_out, OP3);
  not not_307 (not_307_out, OP1);
  not not_308 (not_308_out, OP0);
  not not_309 (not_309_out, OP5);
  not not_310 (not_310_out, OP4);
  not not_311 (not_311_out, OP3);
  not not_312 (not_312_out, OP1);
  not not_313 (not_313_out, OP4);
  not not_314 (not_314_out, OP3);
  not not_315 (not_315_out, OP2);
  not not_316 (not_316_out, OP4);
  not not_317 (not_317_out, OP2);
  not not_318 (not_318_out, OP5);
  not not_319 (not_319_out, OP4);
  not not_320 (not_320_out, OP3);
  not not_321 (not_321_out, OP2);
  not not_322 (not_322_out, OP1);
  not not_323 (not_323_out, OP0);
  not not_324 (not_324_out, F4);
  not not_325 (not_325_out, F3);
  not not_326 (not_326_out, F0);
  not not_327 (not_327_out, OP4);
  not not_328 (not_328_out, OP3);
  not not_329 (not_329_out, OP2);
  not not_330 (not_330_out, OP1);
  not not_331 (not_331_out, OP0);
  and and_1 (and_1_out, not_1_out, not_2_out, not_3_out, not_4_out, not_5_out, not_6_out, not_7_out, not_8_out, not_9_out, not_10_out, not_11_out, not_12_out);
  and and_2 (and_2_out, not_13_out, not_14_out, not_15_out, not_16_out, not_17_out, not_18_out, not_19_out, not_20_out, not_21_out, not_22_out, F1, F0);
  and and_3 (and_3_out, not_23_out, not_24_out, not_25_out, not_26_out, not_27_out, not_28_out, not_29_out, not_30_out, not_31_out, not_32_out, F1, not_33_out);
  and and_4 (and_4_out, not_34_out, not_35_out, not_36_out, not_37_out, not_38_out, not_39_out, F5, not_40_out, not_41_out, not_42_out, not_43_out, not_44_out);
  and and_5 (and_5_out, not_45_out, not_46_out, not_47_out, not_48_out, not_49_out, not_50_out, F5, not_51_out, not_52_out, not_53_out, not_54_out, F0);
  and and_6 (and_6_out, not_55_out, not_56_out, not_57_out, not_58_out, not_59_out, not_60_out, F5, not_61_out, not_62_out, not_63_out, F1, not_64_out);
  and and_7 (and_7_out, not_65_out, not_66_out, not_67_out, not_68_out, not_69_out, not_70_out, F5, not_71_out, not_72_out, F2, not_73_out, not_74_out);
  and and_8 (and_8_out, not_75_out, not_76_out, not_77_out, not_78_out, not_79_out, not_80_out, F5, not_81_out, not_82_out, F2, not_83_out, F0);
  and and_9 (and_9_out, not_84_out, not_85_out, not_86_out, not_87_out, not_88_out, not_89_out, F5, not_90_out, not_91_out, F2, F1, F0);
  and and_10 (and_10_out, not_92_out, not_93_out, not_94_out, not_95_out, not_96_out, not_97_out, F5, not_98_out, F3, not_99_out, F1, not_100_out);
  and and_11 (and_11_out, not_101_out, not_102_out, not_103_out, not_104_out, not_105_out, not_106_out, F5, not_107_out, F3, not_108_out, F1, F0);
  and and_12 (and_12_out, not_109_out, not_110_out, not_111_out, not_112_out, not_113_out, not_114_out, not_115_out, not_116_out, F3, not_117_out, not_118_out, not_119_out);
  and and_13 (and_13_out, not_120_out, not_121_out, not_122_out, not_123_out, not_124_out, not_125_out, not_126_out, not_127_out, F3, F2, not_128_out, not_129_out);
  and and_14 (and_14_out, not_130_out, not_131_out, not_132_out, OP2, not_133_out, not_134_out);
  and and_15 (and_15_out, not_135_out, not_136_out, not_137_out, OP2, not_138_out, OP0);
  and and_16 (and_16_out, not_139_out, not_140_out, OP3, not_141_out, not_142_out, not_143_out);
  and and_17 (and_17_out, not_144_out, not_145_out, OP3, OP2, not_146_out, not_147_out);
  and and_18 (and_18_out, not_148_out, not_149_out, OP3, not_150_out, not_151_out, OP0);
  and and_19 (and_19_out, not_152_out, not_153_out, OP3, not_154_out, OP1, not_155_out);
  and and_20 (and_20_out, not_156_out, not_157_out, OP3, OP2, not_158_out, OP0);
  and and_21 (and_21_out, OP5, not_159_out, not_160_out, not_161_out, OP1, OP0);
  and and_22 (and_22_out, OP5, not_162_out, OP3, not_163_out, OP1, OP0);
  and and_23 (and_23_out, not_164_out, not_165_out, not_166_out, not_167_out, not_168_out, not_169_out, F5, not_170_out, not_171_out, F2, F1, not_172_out);
  and and_24 (and_24_out, not_173_out, not_174_out, OP3, not_175_out, OP1, OP0);
  and and_25 (and_25_out, OP5, not_176_out, not_177_out, not_178_out, not_179_out, not_180_out);
  and and_26 (and_26_out, not_181_out, not_182_out, not_183_out, not_184_out, not_185_out, OP0);
  and and_27 (and_27_out, not_186_out, not_187_out, not_188_out, not_189_out, not_190_out, not_191_out, not_192_out, not_193_out, not_194_out, not_195_out, not_196_out, not_197_out);
  and and_28 (and_28_out, not_198_out, not_199_out, not_200_out, not_201_out, not_202_out, not_203_out, not_204_out, not_205_out, not_206_out, not_207_out, F1, F0);
  and and_29 (and_29_out, not_208_out, not_209_out, not_210_out, not_211_out, not_212_out, not_213_out, not_214_out, not_215_out, not_216_out, not_217_out, F1, not_218_out);
  and and_30 (and_30_out, not_219_out, not_220_out, not_221_out, not_222_out, not_223_out, not_224_out, F5, not_225_out, not_226_out, not_227_out, not_228_out, not_229_out);
  and and_31 (and_31_out, not_230_out, not_231_out, not_232_out, not_233_out, not_234_out, not_235_out, F5, not_236_out, not_237_out, not_238_out, not_239_out, F0);
  and and_32 (and_32_out, not_240_out, not_241_out, not_242_out, not_243_out, not_244_out, not_245_out, F5, not_246_out, not_247_out, not_248_out, F1, not_249_out);
  and and_33 (and_33_out, not_250_out, not_251_out, not_252_out, not_253_out, not_254_out, not_255_out, F5, not_256_out, not_257_out, F2, not_258_out, not_259_out);
  and and_34 (and_34_out, not_260_out, not_261_out, not_262_out, not_263_out, not_264_out, not_265_out, F5, not_266_out, not_267_out, F2, not_268_out, F0);
  and and_35 (and_35_out, not_269_out, not_270_out, not_271_out, not_272_out, not_273_out, not_274_out, F5, not_275_out, not_276_out, F2, F1, F0);
  and and_36 (and_36_out, not_277_out, not_278_out, not_279_out, not_280_out, not_281_out, not_282_out, F5, not_283_out, F3, not_284_out, F1, not_285_out);
  and and_37 (and_37_out, not_286_out, not_287_out, not_288_out, not_289_out, not_290_out, not_291_out, F5, not_292_out, F3, not_293_out, F1, F0);
  and and_38 (and_38_out, not_294_out, not_295_out, not_296_out, not_297_out, not_298_out, not_299_out, not_300_out, not_301_out, F3, F2, not_302_out, not_303_out);
  and and_39 (and_39_out, not_304_out, not_305_out, not_306_out, OP2, not_307_out, not_308_out);
  and and_40 (and_40_out, not_309_out, not_310_out, not_311_out, OP2, not_312_out, OP0);
  and and_41 (and_41_out, OP5, not_313_out, not_314_out, not_315_out, OP1, OP0);
  and and_42 (and_42_out, OP5, not_316_out, OP3, not_317_out, OP1, OP0);
  and and_43 (and_43_out, not_318_out, not_319_out, not_320_out, not_321_out, not_322_out, not_323_out, F5, not_324_out, not_325_out, F2, F1, not_326_out);
  and and_44 (and_44_out, OP5, not_327_out, not_328_out, not_329_out, not_330_out, not_331_out);
  or or_1 (R1_Used, and_1_out, and_2_out, and_3_out, and_4_out, and_5_out, and_6_out, and_7_out, and_8_out, and_9_out, and_10_out, and_11_out, and_12_out, and_13_out, and_14_out, and_15_out, and_16_out, and_17_out, and_18_out, and_19_out, and_20_out, and_21_out, and_22_out, and_23_out, and_24_out, and_25_out, and_26_out);
  or or_2 (R2_Used, and_27_out, and_28_out, and_29_out, and_30_out, and_31_out, and_32_out, and_33_out, and_34_out, and_35_out, and_36_out, and_37_out, and_38_out, and_39_out, and_40_out, and_41_out, and_42_out, and_43_out, and_44_out);
endmodule
module \数据相关检测  (
  input  [5:0] OP,
  input  [4:0] EX_WriteReg_num,
  input  EX_RegWrite,
  input  [4:0] MEM_WriteReg_num,
  input  MEM_RegWrite,
  input  [5:0] Func,
  input  [4:0] ID_R1_num,
  input  [4:0] ID_R2_num,
  output \数据相关 
);

  wire and_1_out, and_2_out, and_3_out, and_4_out, and_5_out, and_6_out, and_7_out, and_8_out, and_9_out,
       and_10_out, and_11_out, and_12_out, comparator_1_eq, comparator_2_eq, comparator_3_eq,
       comparator_4_eq, comparator_5_eq, comparator_6_eq, comparator_7_eq, comparator_8_eq, not_1_out,
       not_2_out, not_3_out, not_4_out, or_1_out, or_2_out, R1_USED, R2_USED;

  \源寄存器使用情况  \u_源寄存器使用情况_1  (
    .OP0(OP[0]), .OP1(OP[1]), .OP2(OP[2]), .OP3(OP[3]), .OP4(OP[4]), .OP5(OP[5]), .F0(Func[0]), .F1(Func[1]),
    .F2(Func[2]), .F3(Func[3]), .F4(Func[4]), .F5(Func[5]), .R1_Used(R1_USED), .R2_Used(R2_USED));
  Comparator #(.width(5)) comparator_1 (.a({5{1'b0}}), .b(ID_R1_num), .eq(comparator_1_eq));  // open: gt, lt
  Comparator #(.width(5)) comparator_2 (.a(EX_WriteReg_num), .b(ID_R1_num), .eq(comparator_2_eq));  // open: gt, lt
  Comparator #(.width(5)) comparator_3 (.a({5{1'b0}}), .b(ID_R2_num), .eq(comparator_3_eq));  // open: gt, lt
  Comparator #(.width(5)) comparator_4 (.a(EX_WriteReg_num), .b(ID_R2_num), .eq(comparator_4_eq));  // open: gt, lt
  Comparator #(.width(5)) comparator_5 (.a({5{1'b0}}), .b(ID_R1_num), .eq(comparator_5_eq));  // open: gt, lt
  Comparator #(.width(5)) comparator_6 (.a(MEM_WriteReg_num), .b(ID_R1_num), .eq(comparator_6_eq));  // open: gt, lt
  Comparator #(.width(5)) comparator_7 (.a({5{1'b0}}), .b(ID_R2_num), .eq(comparator_7_eq));  // open: gt, lt
  Comparator #(.width(5)) comparator_8 (.a(MEM_WriteReg_num), .b(ID_R2_num), .eq(comparator_8_eq));  // open: gt, lt
  not not_1 (not_1_out, comparator_1_eq);
  not not_2 (not_2_out, comparator_3_eq);
  not not_3 (not_3_out, comparator_5_eq);
  not not_4 (not_4_out, comparator_7_eq);
  and and_1 (and_1_out, not_1_out, comparator_2_eq);
  and and_2 (and_2_out, not_2_out, comparator_4_eq);
  and and_3 (and_3_out, not_3_out, comparator_6_eq);
  and and_4 (and_4_out, not_4_out, comparator_8_eq);
  and and_5 (and_5_out, and_1_out, R1_USED);
  and and_6 (and_6_out, and_2_out, R2_USED);
  and and_7 (and_7_out, and_3_out, R1_USED);
  and and_8 (and_8_out, and_4_out, R2_USED);
  or or_1 (or_1_out, and_5_out, and_6_out);
  or or_2 (or_2_out, and_7_out, and_8_out);
  and and_9 (and_9_out, 1'b1, EX_RegWrite);
  and and_10 (and_10_out, 1'b1, MEM_RegWrite);
  and and_11 (and_11_out, and_9_out, or_1_out);
  and and_12 (and_12_out, and_10_out, or_2_out);
  or or_3 (\数据相关 , and_11_out, and_12_out);

  // Other names for the same wires on the sheet: OP_CODE[5:0] = OP
endmodule

// IF/ID
module IF_ID (
  input  \气泡_高电平时有效 ,
  input  clk,
  input  clear,
  input  enable,
  input  [31:0] IR_in,
  input  [31:0] PC_in,
  input  [31:0] OldPC_in,
  output [31:0] IR_out,
  output [31:0] PC_out,
  output [31:0] OldPC_out
);

  wire [31:0] multiplexer_1_out, multiplexer_2_out, multiplexer_3_out;

  Multiplexer #(.width(32), .enable("false")) multiplexer_1 (
    .in0(IR_in), .in1({32{1'b0}}), .out(multiplexer_1_out), .sel(\气泡_高电平时有效 ));
  Multiplexer #(.width(32), .enable("false")) multiplexer_2 (
    .in0(PC_in), .in1({32{1'b0}}), .out(multiplexer_2_out), .sel(\气泡_高电平时有效 ));
  Multiplexer #(.width(32), .enable("false")) multiplexer_3 (
    .in0(OldPC_in), .in1({32{1'b0}}), .out(multiplexer_3_out), .sel(\气泡_高电平时有效 ));
  Register #(.width(32)) IR (.D(multiplexer_1_out), .en(enable), .Q(IR_out), .clk(clk), .clr(clear));
  Register #(.width(32)) PC (.D(multiplexer_2_out), .en(enable), .Q(PC_out), .clk(clk), .clr(clear));
  Register #(.width(32)) OldPC (.D(multiplexer_3_out), .en(enable), .Q(OldPC_out), .clk(clk), .clr(clear));
endmodule

// ID/EX
module ID_EX (
  input  \气泡_高电平时有效 ,
  input  clk,
  input  clear,
  input  enable,
  input  Beq_in,
  input  Bne_in,
  input  MemToReg_in,
  input  MemWrite_in,
  input  [3:0] AluOP_in,
  input  AluSrc_in,
  input  RegWrite_in,
  input  JAL_in,
  input  RegDst_in,
  input  Syscall_in,
  input  JMP_in,
  input  JR_in,
  input  SignedExt_in,
  input  LB_in,
  input  BGEZ_in,
  input  [31:0] IR_in,
  input  [31:0] PC_in,
  input  [31:0] R1_in,
  input  [31:0] R2_in,
  input  [31:0] Imm_in,
  input  [31:0] OldPC_in,
  output Beq_out,
  output Bne_out,
  output MemToReg_out,
  output MemWrite_out,
  output [3:0] AluOP_out,
  output AluSrc_out,
  output RegWrite_out,
  output JAL_out,
  output RegDst_out,
  output Syscall_out,
  output JMP_out,
  output JR_out,
  output SignedExt_out,
  output LB_out,
  output BGEZ_out,
  output [31:0] IR_out,
  output [31:0] PC_out,
  output [31:0] R1_out,
  output [31:0] R2_out,
  output [31:0] Imm_out,
  output [31:0] OldPC_out
);

  wire multiplexer_1_out, multiplexer_2_out, multiplexer_3_out, multiplexer_4_out, multiplexer_5_out,
       multiplexer_6_out, multiplexer_7_out, multiplexer_8_out, multiplexer_9_out, multiplexer_10_out,
       multiplexer_11_out, multiplexer_12_out, multiplexer_13_out, multiplexer_14_out;
  wire [3:0] multiplexer_21_out;
  wire [31:0] multiplexer_15_out, multiplexer_16_out, multiplexer_17_out, multiplexer_18_out,
       multiplexer_19_out, multiplexer_20_out;

  Multiplexer #(.enable("false")) multiplexer_1 (.in0(Beq_in), .in1(1'b0), .out(multiplexer_1_out), .sel(\气泡_高电平时有效 ));
  Multiplexer #(.enable("false")) multiplexer_2 (.in0(Bne_in), .in1(1'b0), .out(multiplexer_2_out), .sel(\气泡_高电平时有效 ));
  Multiplexer #(.enable("false")) multiplexer_3 (
    .in0(MemToReg_in), .in1(1'b0), .out(multiplexer_3_out), .sel(\气泡_高电平时有效 ));
  Multiplexer #(.enable("false")) multiplexer_4 (
    .in0(MemWrite_in), .in1(1'b0), .out(multiplexer_4_out), .sel(\气泡_高电平时有效 ));
  Multiplexer #(.enable("false")) multiplexer_5 (
    .in0(AluSrc_in), .in1(1'b0), .out(multiplexer_5_out), .sel(\气泡_高电平时有效 ));
  Multiplexer #(.enable("false")) multiplexer_6 (
    .in0(RegWrite_in), .in1(1'b0), .out(multiplexer_6_out), .sel(\气泡_高电平时有效 ));
  Multiplexer #(.enable("false")) multiplexer_7 (.in0(JAL_in), .in1(1'b0), .out(multiplexer_7_out), .sel(\气泡_高电平时有效 ));
  Multiplexer #(.enable("false")) multiplexer_8 (
    .in0(RegDst_in), .in1(1'b0), .out(multiplexer_8_out), .sel(\气泡_高电平时有效 ));
  Multiplexer #(.enable("false")) multiplexer_9 (
    .in0(Syscall_in), .in1(1'b0), .out(multiplexer_9_out), .sel(\气泡_高电平时有效 ));
  Multiplexer #(.enable("false")) multiplexer_10 (
    .in0(JMP_in), .in1(1'b0), .out(multiplexer_10_out), .sel(\气泡_高电平时有效 ));
  Multiplexer #(.enable("false")) multiplexer_11 (.in0(JR_in), .in1(1'b0), .out(multiplexer_11_out), .sel(\气泡_高电平时有效 ));
  Multiplexer #(.enable("false")) multiplexer_12 (
    .in0(SignedExt_in), .in1(1'b0), .out(multiplexer_12_out), .sel(\气泡_高电平时有效 ));
  Multiplexer #(.enable("false")) multiplexer_13 (.in0(LB_in), .in1(1'b0), .out(multiplexer_13_out), .sel(\气泡_高电平时有效 ));
  Multiplexer #(.enable("false")) multiplexer_14 (
    .in0(BGEZ_in), .in1(1'b0), .out(multiplexer_14_out), .sel(\气泡_高电平时有效 ));
  Multiplexer #(.width(32), .enable("false")) multiplexer_15 (
    .in0(IR_in), .in1({32{1'b0}}), .out(multiplexer_15_out), .sel(\气泡_高电平时有效 ));
  Multiplexer #(.width(32), .enable("false")) multiplexer_16 (
    .in0(PC_in), .in1({32{1'b0}}), .out(multiplexer_16_out), .sel(\气泡_高电平时有效 ));
  Multiplexer #(.width(32), .enable("false")) multiplexer_17 (
    .in0(R1_in), .in1({32{1'b0}}), .out(multiplexer_17_out), .sel(\气泡_高电平时有效 ));
  Multiplexer #(.width(32), .enable("false")) multiplexer_18 (
    .in0(R2_in), .in1({32{1'b0}}), .out(multiplexer_18_out), .sel(\气泡_高电平时有效 ));
  Multiplexer #(.width(32), .enable("false")) multiplexer_19 (
    .in0(Imm_in), .in1({32{1'b0}}), .out(multiplexer_19_out), .sel(\气泡_高电平时有效 ));
  Multiplexer #(.width(32), .enable("false")) multiplexer_20 (
    .in0(OldPC_in), .in1({32{1'b0}}), .out(multiplexer_20_out), .sel(\气泡_高电平时有效 ));
  Multiplexer #(.width(4), .enable("false")) multiplexer_21 (
    .in0(AluOP_in), .in1(4'b0000), .out(multiplexer_21_out), .sel(\气泡_高电平时有效 ));
  Register #(.width(1)) Beq (.D(multiplexer_1_out), .en(enable), .Q(Beq_out), .clk(clk), .clr(clear));
  Register #(.width(1)) Bne (.D(multiplexer_2_out), .en(enable), .Q(Bne_out), .clk(clk), .clr(clear));
  Register #(.width(1)) MemToReg (.D(multiplexer_3_out), .en(enable), .Q(MemToReg_out), .clk(clk), .clr(clear));
  Register #(.width(1)) MemWrite (.D(multiplexer_4_out), .en(enable), .Q(MemWrite_out), .clk(clk), .clr(clear));
  Register #(.width(4)) AluOP (.D(multiplexer_21_out), .en(enable), .Q(AluOP_out), .clk(clk), .clr(clear));
  Register #(.width(1)) AluSrc (.D(multiplexer_5_out), .en(enable), .Q(AluSrc_out), .clk(clk), .clr(clear));
  Register #(.width(1)) RegWrite (.D(multiplexer_6_out), .en(enable), .Q(RegWrite_out), .clk(clk), .clr(clear));
  Register #(.width(1)) JAL (.D(multiplexer_7_out), .en(enable), .Q(JAL_out), .clk(clk), .clr(clear));
  Register #(.width(1)) RegDst (.D(multiplexer_8_out), .en(enable), .Q(RegDst_out), .clk(clk), .clr(clear));
  Register #(.width(1)) Syscall (.D(multiplexer_9_out), .en(enable), .Q(Syscall_out), .clk(clk), .clr(clear));
  Register #(.width(1)) JMP (.D(multiplexer_10_out), .en(enable), .Q(JMP_out), .clk(clk), .clr(clear));
  Register #(.width(1)) JR (.D(multiplexer_11_out), .en(enable), .Q(JR_out), .clk(clk), .clr(clear));
  Register #(.width(1)) SignedExt (.D(multiplexer_12_out), .en(enable), .Q(SignedExt_out), .clk(clk), .clr(clear));
  Register #(.width(1)) LB (.D(multiplexer_13_out), .en(enable), .Q(LB_out), .clk(clk), .clr(clear));
  Register #(.width(1)) BGEZ (.D(multiplexer_14_out), .en(enable), .Q(BGEZ_out), .clk(clk), .clr(clear));
  Register #(.width(32)) IR (.D(multiplexer_15_out), .en(enable), .Q(IR_out), .clk(clk), .clr(clear));
  Register #(.width(32)) PC (.D(multiplexer_16_out), .en(enable), .Q(PC_out), .clk(clk), .clr(clear));
  Register #(.width(32)) R1 (.D(multiplexer_17_out), .en(enable), .Q(R1_out), .clk(clk), .clr(clear));
  Register #(.width(32)) R2 (.D(multiplexer_18_out), .en(enable), .Q(R2_out), .clk(clk), .clr(clear));
  Register #(.width(32)) Imm (.D(multiplexer_19_out), .en(enable), .Q(Imm_out), .clk(clk), .clr(clear));
  Register #(.width(32)) OldPC (.D(multiplexer_20_out), .en(enable), .Q(OldPC_out), .clk(clk), .clr(clear));
endmodule

// EX/MEM
module EX_MEM (
  input  \气泡_高电平时有效 ,
  input  clk,
  input  clear,
  input  enable,
  input  MemToReg_in,
  input  MemWrite_in,
  input  RegWrite_in,
  input  JAL_in,
  input  LB_in,
  input  RegDst_in,
  input  Syscall_in,
  input  equal_in,
  input  pause_in,
  input  [31:0] IR_in,
  input  [31:0] PC_in,
  input  [31:0] ALUResult_in,
  input  [31:0] R2_in,
  input  [31:0] OldPC_in,
  output MemToReg_out,
  output MemWrite_out,
  output RegWrite_out,
  output JAL_out,
  output LB_out,
  output RegDst_out,
  output Syscall_out,
  output equal_out,
  output pause_out,
  output [31:0] IR_out,
  output [31:0] PC_out,
  output [31:0] ALUResult_out,
  output [31:0] R2_out,
  output [31:0] OldPC_out
);

  wire multiplexer_1_out, multiplexer_2_out, multiplexer_3_out, multiplexer_4_out, multiplexer_5_out,
       multiplexer_6_out, multiplexer_7_out, multiplexer_8_out, multiplexer_9_out;
  wire [31:0] multiplexer_10_out, multiplexer_11_out, multiplexer_12_out, multiplexer_13_out,
       multiplexer_14_out;

  Multiplexer #(.enable("false")) multiplexer_1 (
    .in0(MemToReg_in), .in1(1'b0), .out(multiplexer_1_out), .sel(\气泡_高电平时有效 ));
  Multiplexer #(.enable("false")) multiplexer_2 (
    .in0(MemWrite_in), .in1(1'b0), .out(multiplexer_2_out), .sel(\气泡_高电平时有效 ));
  Multiplexer #(.enable("false")) multiplexer_3 (
    .in0(RegWrite_in), .in1(1'b0), .out(multiplexer_3_out), .sel(\气泡_高电平时有效 ));
  Multiplexer #(.enable("false")) multiplexer_4 (.in0(JAL_in), .in1(1'b0), .out(multiplexer_4_out), .sel(\气泡_高电平时有效 ));
  Multiplexer #(.enable("false")) multiplexer_5 (.in0(LB_in), .in1(1'b0), .out(multiplexer_5_out), .sel(\气泡_高电平时有效 ));
  Multiplexer #(.enable("false")) multiplexer_6 (
    .in0(RegDst_in), .in1(1'b0), .out(multiplexer_6_out), .sel(\气泡_高电平时有效 ));
  Multiplexer #(.enable("false")) multiplexer_7 (
    .in0(Syscall_in), .in1(1'b0), .out(multiplexer_7_out), .sel(\气泡_高电平时有效 ));
  Multiplexer #(.enable("false")) multiplexer_8 (
    .in0(equal_in), .in1(1'b0), .out(multiplexer_8_out), .sel(\气泡_高电平时有效 ));
  Multiplexer #(.enable("false")) multiplexer_9 (
    .in0(pause_in), .in1(1'b0), .out(multiplexer_9_out), .sel(\气泡_高电平时有效 ));
  Multiplexer #(.width(32), .enable("false")) multiplexer_10 (
    .in0(IR_in), .in1({32{1'b0}}), .out(multiplexer_10_out), .sel(\气泡_高电平时有效 ));
  Multiplexer #(.width(32), .enable("false")) multiplexer_11 (
    .in0(PC_in), .in1({32{1'b0}}), .out(multiplexer_11_out), .sel(\气泡_高电平时有效 ));
  Multiplexer #(.width(32), .enable("false")) multiplexer_12 (
    .in0(ALUResult_in), .in1({32{1'b0}}), .out(multiplexer_12_out), .sel(\气泡_高电平时有效 ));
  Multiplexer #(.width(32), .enable("false")) multiplexer_13 (
    .in0(R2_in), .in1({32{1'b0}}), .out(multiplexer_13_out), .sel(\气泡_高电平时有效 ));
  Multiplexer #(.width(32), .enable("false")) multiplexer_14 (
    .in0(OldPC_in), .in1({32{1'b0}}), .out(multiplexer_14_out), .sel(\气泡_高电平时有效 ));
  Register #(.width(1)) MemToReg (.D(multiplexer_1_out), .en(enable), .Q(MemToReg_out), .clk(clk), .clr(clear));
  Register #(.width(1)) MemWrite (.D(multiplexer_2_out), .en(enable), .Q(MemWrite_out), .clk(clk), .clr(clear));
  Register #(.width(1)) RegWrite (.D(multiplexer_3_out), .en(enable), .Q(RegWrite_out), .clk(clk), .clr(clear));
  Register #(.width(1)) JAL (.D(multiplexer_4_out), .en(enable), .Q(JAL_out), .clk(clk), .clr(clear));
  Register #(.width(1)) LB (.D(multiplexer_5_out), .en(enable), .Q(LB_out), .clk(clk), .clr(clear));
  Register #(.width(1)) RegDst (.D(multiplexer_6_out), .en(enable), .Q(RegDst_out), .clk(clk), .clr(clear));
  Register #(.width(1)) Syscall (.D(multiplexer_7_out), .en(enable), .Q(Syscall_out), .clk(clk), .clr(clear));
  Register #(.width(1)) equal (.D(multiplexer_8_out), .en(enable), .Q(equal_out), .clk(clk), .clr(clear));
  Register #(.width(1)) pause (.D(multiplexer_9_out), .en(enable), .Q(pause_out), .clk(clk), .clr(clear));
  Register #(.width(32)) IR (.D(multiplexer_10_out), .en(enable), .Q(IR_out), .clk(clk), .clr(clear));
  Register #(.width(32)) PC (.D(multiplexer_11_out), .en(enable), .Q(PC_out), .clk(clk), .clr(clear));
  Register #(.width(32)) ALUResult (.D(multiplexer_12_out), .en(enable), .Q(ALUResult_out), .clk(clk), .clr(clear));
  Register #(.width(32)) R2 (.D(multiplexer_13_out), .en(enable), .Q(R2_out), .clk(clk), .clr(clear));
  Register #(.width(32)) OldPC (.D(multiplexer_14_out), .en(enable), .Q(OldPC_out), .clk(clk), .clr(clear));
endmodule

// MEM/WB
module MEM_WB (
  input  \气泡_高电平时有效 ,
  input  clk,
  input  clear,
  input  enable,
  input  MemToReg_in,
  input  MemWrite_in,
  input  RegWrite_in,
  input  JAL_in,
  input  LB_in,
  input  RegDst_in,
  input  Syscall_in,
  input  equal_in,
  input  pause_in,
  input  [31:0] IR_in,
  input  [31:0] PC_in,
  input  [31:0] ALUResult_in,
  input  [31:0] Memorydata_in,
  input  [31:0] OldPC_in,
  output MemToReg_out,
  output MemWrite_out,
  output RegWrite_out,
  output JAL_out,
  output LB_out,
  output RegDst_out,
  output Syscall_out,
  output equal_out,
  output pause_out,
  output [31:0] IR_out,
  output [31:0] PC_out,
  output [31:0] ALUResult_out,
  output [31:0] Memorydata_out,
  output [31:0] OldPC_out
);

  wire multiplexer_1_out, multiplexer_2_out, multiplexer_3_out, multiplexer_4_out, multiplexer_5_out,
       multiplexer_6_out, multiplexer_7_out, multiplexer_8_out, multiplexer_9_out;
  wire [31:0] multiplexer_10_out, multiplexer_11_out, multiplexer_12_out, multiplexer_13_out,
       multiplexer_14_out;

  Multiplexer #(.enable("false")) multiplexer_1 (
    .in0(MemToReg_in), .in1(1'b0), .out(multiplexer_1_out), .sel(\气泡_高电平时有效 ));
  Multiplexer #(.enable("false")) multiplexer_2 (
    .in0(MemWrite_in), .in1(1'b0), .out(multiplexer_2_out), .sel(\气泡_高电平时有效 ));
  Multiplexer #(.enable("false")) multiplexer_3 (
    .in0(RegWrite_in), .in1(1'b0), .out(multiplexer_3_out), .sel(\气泡_高电平时有效 ));
  Multiplexer #(.enable("false")) multiplexer_4 (.in0(JAL_in), .in1(1'b0), .out(multiplexer_4_out), .sel(\气泡_高电平时有效 ));
  Multiplexer #(.enable("false")) multiplexer_5 (.in0(LB_in), .in1(1'b0), .out(multiplexer_5_out), .sel(\气泡_高电平时有效 ));
  Multiplexer #(.enable("false")) multiplexer_6 (
    .in0(RegDst_in), .in1(1'b0), .out(multiplexer_6_out), .sel(\气泡_高电平时有效 ));
  Multiplexer #(.enable("false")) multiplexer_7 (
    .in0(Syscall_in), .in1(1'b0), .out(multiplexer_7_out), .sel(\气泡_高电平时有效 ));
  Multiplexer #(.enable("false")) multiplexer_8 (
    .in0(equal_in), .in1(1'b0), .out(multiplexer_8_out), .sel(\气泡_高电平时有效 ));
  Multiplexer #(.enable("false")) multiplexer_9 (
    .in0(pause_in), .in1(1'b0), .out(multiplexer_9_out), .sel(\气泡_高电平时有效 ));
  Multiplexer #(.width(32), .enable("false")) multiplexer_10 (
    .in0(IR_in), .in1({32{1'b0}}), .out(multiplexer_10_out), .sel(\气泡_高电平时有效 ));
  Multiplexer #(.width(32), .enable("false")) multiplexer_11 (
    .in0(PC_in), .in1({32{1'b0}}), .out(multiplexer_11_out), .sel(\气泡_高电平时有效 ));
  Multiplexer #(.width(32), .enable("false")) multiplexer_12 (
    .in0(ALUResult_in), .in1({32{1'b0}}), .out(multiplexer_12_out), .sel(\气泡_高电平时有效 ));
  Multiplexer #(.width(32), .enable("false")) multiplexer_13 (
    .in0(Memorydata_in), .in1({32{1'b0}}), .out(multiplexer_13_out), .sel(\气泡_高电平时有效 ));
  Multiplexer #(.width(32), .enable("false")) multiplexer_14 (
    .in0(OldPC_in), .in1({32{1'b0}}), .out(multiplexer_14_out), .sel(\气泡_高电平时有效 ));
  Register #(.width(1)) MemToReg (.D(multiplexer_1_out), .en(enable), .Q(MemToReg_out), .clk(clk), .clr(clear));
  Register #(.width(1)) MemWrite (.D(multiplexer_2_out), .en(enable), .Q(MemWrite_out), .clk(clk), .clr(clear));
  Register #(.width(1)) RegWrite (.D(multiplexer_3_out), .en(enable), .Q(RegWrite_out), .clk(clk), .clr(clear));
  Register #(.width(1)) JAL (.D(multiplexer_4_out), .en(enable), .Q(JAL_out), .clk(clk), .clr(clear));
  Register #(.width(1)) LB (.D(multiplexer_5_out), .en(enable), .Q(LB_out), .clk(clk), .clr(clear));
  Register #(.width(1)) RegDst (.D(multiplexer_6_out), .en(enable), .Q(RegDst_out), .clk(clk), .clr(clear));
  Register #(.width(1)) Syscall (.D(multiplexer_7_out), .en(enable), .Q(Syscall_out), .clk(clk), .clr(clear));
  Register #(.width(1)) equal (.D(multiplexer_8_out), .en(enable), .Q(equal_out), .clk(clk), .clr(clear));
  Register #(.width(1)) pause (.D(multiplexer_9_out), .en(enable), .Q(pause_out), .clk(clk), .clr(clear));
  Register #(.width(32)) IR (.D(multiplexer_10_out), .en(enable), .Q(IR_out), .clk(clk), .clr(clear));
  Register #(.width(32)) PC (.D(multiplexer_11_out), .en(enable), .Q(PC_out), .clk(clk), .clr(clear));
  Register #(.width(32)) ALUResult (.D(multiplexer_12_out), .en(enable), .Q(ALUResult_out), .clk(clk), .clr(clear));
  Register #(.width(32)) Memorydata (.D(multiplexer_13_out), .en(enable), .Q(Memorydata_out), .clk(clk), .clr(clear));
  Register #(.width(32)) OldPC (.D(multiplexer_14_out), .en(enable), .Q(OldPC_out), .clk(clk), .clr(clear));
endmodule

module \分支相关流水线  (
);

  wire AluSrc, and_2_out, and_3_out, BGEZ, BGEZ_SIGN, CLK, comparator_1_lt, Con_flag, Equal,
       ex_mem_1_equal_out, ex_mem_1_jal_out, ex_mem_1_lb_out, ex_mem_1_memtoreg_out, ex_mem_1_memwrite_out,
       ex_mem_1_regdst_out, ex_mem_1_regwrite_out, ex_mem_1_syscall_out, Go, id_ex_1_beq_out,
       id_ex_1_bne_out, id_ex_1_jal_out, id_ex_1_lb_out, id_ex_1_memtoreg_out, id_ex_1_memwrite_out,
       id_ex_1_regdst_out, id_ex_1_regwrite_out, IR1, IR2, IR3, J, JMP, JR, mem_wb_1_equal_out,
       mem_wb_1_jal_out, mem_wb_1_memtoreg_out, mem_wb_1_regdst_out, mem_wb_1_syscall_out, multiplexer_4_out,
       not_1_out, not_2_out, not_3_out, not_4_out, Pause, RegWrite, RST, Show, SignExt, Syscall, W1, W2, W3,
       Write, \单周期硬布线控制器_1_alu_src , \单周期硬布线控制器_1_beq , \单周期硬布线控制器_1_bgez , \单周期硬布线控制器_1_bne ,
       \单周期硬布线控制器_1_jal , \单周期硬布线控制器_1_jmp , \单周期硬布线控制器_1_jr , \单周期硬布线控制器_1_lb , \单周期硬布线控制器_1_memtoreg ,
       \单周期硬布线控制器_1_memwrite , \单周期硬布线控制器_1_regdst , \单周期硬布线控制器_1_regwrite , \单周期硬布线控制器_1_syscall ;
  wire [3:0] id_ex_1_aluop_out, \单周期硬布线控制器_1_alu_op ;
  wire [4:0] multiplexer_5_out, multiplexer_6_out, multiplexer_10_out, W_num;
  wire [9:0] PC_q_2;
  wire [11:0] EX_PC, ID_PC, IF_PC, MEM_PC, WB_PC;
  wire [15:0] \LoadUse次数 , \总周期数 , \插入气泡数 , \无条件分支数 , \条件分支成功数 ;
  wire [27:0] shifter_3_out;
  wire [31:0] adder_1_out, adder_3_out, BGEZ_PC, bit_extender_1_out, bit_extender_2_out, Din,
       ex_mem_1_aluresult_out, ex_mem_1_ir_out, ex_mem_1_oldpc_out, ex_mem_1_pc_out, ex_mem_1_r2_out,
       id_ex_1_oldpc_out, if_id_1_ir_out, if_id_1_oldpc_out, if_id_1_pc_out, Immediate, IR, LedData,
       mem_wb_1_aluresult_out, mem_wb_1_ir_out, mem_wb_1_memorydata_out, mem_wb_1_pc_out, mips_alu_1_result,
       mips_regifile_1_r1, mips_regifile_1_r2, multiplexer_1_out, multiplexer_2_out, multiplexer_3_out,
       multiplexer_7_out, multiplexer_8_out, multiplexer_9_out, multiplexer_12_out, PC_add4, PC_q, R1, R2,
       ram_1_data, rom_1_data, shifter_1_out, shifter_2_out;

  Button \u_总复位  (.out(RST));
  Button _1 (.out(IR1));
  Button _2 (.out(IR2));
  Button _3 (.out(IR3));
  Button \u_继续运行  (.out(Go));
  LED led_1 (.in(W1));
  LED led_2 (.in(W2));
  LED led_3 (.in(W3));
  not not_1 (not_1_out, Go);
  nand nand_1 (Write, not_1_out, Pause);
  Multiplexer #(.width(32), .enable("false")) multiplexer_1 (
    .in0(adder_3_out), .in1(adder_1_out), .out(multiplexer_1_out), .sel(Con_flag));
  Shifter #(.width(32)) shifter_1 (.in(Immediate), .\dist (5'b00010), .out(shifter_1_out));
  Hex_Digit_Display hex_digit_display_1 (.value(LedData[31:28]));  // open: dp
  Comparator #(.width(32)) comparator_1 (.a(R1), .b({32{1'b0}}), .lt(comparator_1_lt));  // open: gt, eq
  Multiplexer #(.select(2), .width(32), .enable("false")) multiplexer_2 (
    .in0(multiplexer_1_out), .in1(R1), .in2({PC_add4[31:28], shifter_3_out}), .in3(R1),
    .out(multiplexer_2_out), .sel({JMP, JR}));
  Multiplexer #(.width(32), .enable("false")) multiplexer_3 (
    .in0(multiplexer_2_out), .in1(BGEZ_PC), .out(multiplexer_3_out), .sel(BGEZ_SIGN));
  Adder #(.width(32)) adder_1 (.a(shifter_1_out), .b(PC_add4), .out(adder_1_out));  // open: cin, cout
  Hex_Digit_Display hex_digit_display_2 (.value(LedData[23:20]));  // open: dp
  Hex_Digit_Display hex_digit_display_3 (.value(LedData[27:24]));  // open: dp
  not not_2 (not_2_out, comparator_1_lt);
  Shifter #(.width(32)) shifter_2 (.in(Immediate), .\dist (5'b00010), .out(shifter_2_out));
  Adder #(.width(32)) adder_2 (.a(shifter_2_out), .b(PC_add4), .out(BGEZ_PC));  // open: cin, cout
  Shifter #(.width(28)) shifter_3 (.in(IR[27:0]), .\dist (5'b00010), .out(shifter_3_out));
  Hex_Digit_Display hex_digit_display_4 (.value(LedData[19:16]));  // open: dp
  Hex_Digit_Display hex_digit_display_5 (.value(LedData[15:12]));  // open: dp
  and and_1 (BGEZ_SIGN, not_2_out, BGEZ);
  Multiplexer #(.enable("false")) multiplexer_4 (.in0(1'b1), .in1(Go), .out(multiplexer_4_out), .sel(Pause));
  Register #(.width(32)) PC (
    .D(multiplexer_3_out), .en(multiplexer_4_out), .Q({PC_q[31:12], PC_q_2, PC_q[1:0]}), .clk(CLK), .clr(RST));
  Hex_Digit_Display hex_digit_display_6 (.value(LedData[11:8]));  // open: dp
  Hex_Digit_Display hex_digit_display_7 (.value(LedData[7:4]));  // open: dp
  Clock clock_1 (.out(CLK));
  Counter #(.width(16), .max('hffff)) counter_1 (
    .load(1'b0), .count(multiplexer_4_out), .Q(\总周期数 ), .clk(CLK), .clr(RST));  // open: D, carry
  Hex_Digit_Display hex_digit_display_8 (.value(LedData[3:0]));  // open: dp
  Adder #(.width(32)) adder_3 (.a({PC_q[31:12], PC_q_2, PC_q[1:0]}), .b(32'h4), .out(adder_3_out));  // open: cin, cout
  ROM #(.addrWidth(10), .dataWidth(32)) rom_1 (.addr(PC_q_2), .data(rom_1_data));  // open: sel
  // Probe on \总周期数 
  // Probe on \无条件分支数 
  // Probe on \条件分支成功数 
  // Probe on \插入气泡数 
  // Probe on \LoadUse次数 
  Register #(.width(32)) register_1 (.D(R2), .Q(LedData), .clk(Show), .clr(RST));  // open: en
  IF_ID if_id_1 (
    .IR_in(rom_1_data), .PC_in(adder_3_out), .\气泡_高电平时有效 (J), .clk(CLK), .clear(RST), .enable(Write),
    .IR_out(if_id_1_ir_out), .PC_out(if_id_1_pc_out), .OldPC_in({PC_q[31:12], PC_q_2, PC_q[1:0]}),
    .OldPC_out(if_id_1_oldpc_out));
  // Probe on IF_PC
  // Probe on ID_PC
  \单周期硬布线控制器  \u_单周期硬布线控制器_1  (
    .Func(if_id_1_ir_out[5:0]), .OP(if_id_1_ir_out[31:26]), .ALU_OP(\单周期硬布线控制器_1_alu_op ),
    .MemToReg(\单周期硬布线控制器_1_memtoreg ), .MemWrite(\单周期硬布线控制器_1_memwrite ), .ALU_SRC(\单周期硬布线控制器_1_alu_src ),
    .RegWrite(\单周期硬布线控制器_1_regwrite ), .SysCALL(\单周期硬布线控制器_1_syscall ), .SignedExt(SignExt),
    .RegDst(\单周期硬布线控制器_1_regdst ), .JR(\单周期硬布线控制器_1_jr ), .JMP(\单周期硬布线控制器_1_jmp ), .Beq(\单周期硬布线控制器_1_beq ),
    .JAL(\单周期硬布线控制器_1_jal ), .Bne(\单周期硬布线控制器_1_bne ), .LB(\单周期硬布线控制器_1_lb ), .BGEZ(\单周期硬布线控制器_1_bgez ));
  Multiplexer #(.width(5), .enable("false")) multiplexer_5 (
    .in0(if_id_1_ir_out[25:21]), .in1(5'b00010), .out(multiplexer_5_out), .sel(\单周期硬布线控制器_1_syscall ));
  Multiplexer #(.width(5), .enable("false")) multiplexer_6 (
    .in0(if_id_1_ir_out[20:16]), .in1(5'b00100), .out(multiplexer_6_out), .sel(\单周期硬布线控制器_1_syscall ));
  // Probe on W_num
  assign bit_extender_1_out = {{16{1'b0}}, if_id_1_ir_out[15:0]};  // Bit_Extender bit_extender_1
  assign bit_extender_2_out = {{16{if_id_1_ir_out[15]}}, if_id_1_ir_out[15:0]};  // Bit_Extender bit_extender_2
  // Probe on EX_PC
  // Probe on MEM_PC
  Multiplexer #(.width(32), .enable("false")) multiplexer_7 (
    .in0(bit_extender_1_out), .in1(bit_extender_2_out), .out(multiplexer_7_out), .sel(SignExt));
  // Probe on WB_PC
  MIPS_Regifile mips_regifile_1 (
    .Din(Din), .Clk(CLK), .R1(mips_regifile_1_r1), .R2(mips_regifile_1_r2), .WE(RegWrite), .W_num(W_num),
    .R1_num(multiplexer_5_out), .R2_num(multiplexer_6_out));
  ID_EX id_ex_1 (
    .Beq_in(\单周期硬布线控制器_1_beq ), .Bne_in(\单周期硬布线控制器_1_bne ), .MemToReg_in(\单周期硬布线控制器_1_memtoreg ),
    .MemWrite_in(\单周期硬布线控制器_1_memwrite ), .AluOP_in(\单周期硬布线控制器_1_alu_op ), .AluSrc_in(\单周期硬布线控制器_1_alu_src ),
    .RegWrite_in(\单周期硬布线控制器_1_regwrite ), .JAL_in(\单周期硬布线控制器_1_jal ), .RegDst_in(\单周期硬布线控制器_1_regdst ),
    .Syscall_in(\单周期硬布线控制器_1_syscall ), .JMP_in(\单周期硬布线控制器_1_jmp ), .JR_in(\单周期硬布线控制器_1_jr ),
    .SignedExt_in(SignExt), .LB_in(\单周期硬布线控制器_1_lb ), .BGEZ_in(\单周期硬布线控制器_1_bgez ), .IR_in(if_id_1_ir_out),
    .PC_in(if_id_1_pc_out), .R1_in(mips_regifile_1_r1), .R2_in(mips_regifile_1_r2),
    .Imm_in(multiplexer_7_out), .Beq_out(id_ex_1_beq_out), .Bne_out(id_ex_1_bne_out),
    .MemToReg_out(id_ex_1_memtoreg_out), .MemWrite_out(id_ex_1_memwrite_out), .AluOP_out(id_ex_1_aluop_out),
    .AluSrc_out(AluSrc), .RegWrite_out(id_ex_1_regwrite_out), .JAL_out(id_ex_1_jal_out),
    .RegDst_out(id_ex_1_regdst_out), .Syscall_out(Syscall), .JMP_out(JMP), .JR_out(JR),
    .LB_out(id_ex_1_lb_out), .BGEZ_out(BGEZ), .IR_out(IR), .PC_out(PC_add4), .R1_out(R1), .R2_out(R2),
    .Imm_out(Immediate), .clk(CLK), .clear(RST), .enable(Write), .\气泡_高电平时有效 (J),
    .OldPC_in(if_id_1_oldpc_out), .OldPC_out(id_ex_1_oldpc_out));  // open: SignedExt_out
  Multiplexer #(.width(32), .enable("false")) multiplexer_8 (
    .in0(R2), .in1(Immediate), .out(multiplexer_8_out), .sel(AluSrc));
  and and_2 (and_2_out, Equal, id_ex_1_beq_out);
  not not_3 (not_3_out, Equal);
  and and_3 (and_3_out, not_3_out, id_ex_1_bne_out);
  Multiplexer #(.width(32), .enable("false")) multiplexer_9 (
    .in0(multiplexer_8_out), .in1(32'h22), .out(multiplexer_9_out), .sel(Syscall));
  or or_1 (Con_flag, BGEZ, and_2_out, and_3_out);
  MIPS_ALU mips_alu_1 (
    .X(R1), .Y(multiplexer_9_out), .AluOP(id_ex_1_aluop_out), .Equal(Equal), .Result(mips_alu_1_result),
    .shamt(IR[10:6]));  // open: Result_2
  Counter #(.width(16), .max('hffff)) counter_2 (
    .load(1'b0), .count(Con_flag), .Q(\条件分支成功数 ), .clk(CLK), .clr(RST));  // open: D, carry
  Counter #(.width(16), .max('hffff)) counter_3 (
    .load(1'b0), .count(JMP), .Q(\无条件分支数 ), .clk(CLK), .clr(RST));  // open: D, carry
  or or_2 (J, JMP, JR, Con_flag);
  EX_MEM ex_mem_1 (
    .\气泡_高电平时有效 (1'b0), .clk(CLK), .clear(RST), .enable(Write), .MemToReg_in(id_ex_1_memtoreg_out),
    .MemToReg_out(ex_mem_1_memtoreg_out), .MemWrite_in(id_ex_1_memwrite_out),
    .MemWrite_out(ex_mem_1_memwrite_out), .RegWrite_in(id_ex_1_regwrite_out),
    .RegWrite_out(ex_mem_1_regwrite_out), .JAL_in(id_ex_1_jal_out), .JAL_out(ex_mem_1_jal_out),
    .LB_in(id_ex_1_lb_out), .LB_out(ex_mem_1_lb_out), .IR_in(IR), .IR_out(ex_mem_1_ir_out), .PC_in(PC_add4),
    .PC_out(ex_mem_1_pc_out), .ALUResult_in(mips_alu_1_result), .ALUResult_out(ex_mem_1_aluresult_out),
    .R2_in(R2), .R2_out(ex_mem_1_r2_out), .RegDst_in(id_ex_1_regdst_out), .RegDst_out(ex_mem_1_regdst_out),
    .Syscall_in(Syscall), .Syscall_out(ex_mem_1_syscall_out), .equal_in(Equal),
    .equal_out(ex_mem_1_equal_out), .OldPC_in(id_ex_1_oldpc_out), .OldPC_out(ex_mem_1_oldpc_out));  // open: pause_in, pause_out
  RAM #(.addrWidth(10), .dataWidth(32), .bus("separate")) ram_1 (
    .addr(ex_mem_1_aluresult_out[11:2]), .din(ex_mem_1_r2_out), .data(ram_1_data),
    .str(ex_mem_1_memwrite_out), .clk(CLK), .clr(RST));  // open: sel, ld
  MEM_WB mem_wb_1 (
    .\气泡_高电平时有效 (1'b0), .clk(CLK), .clear(RST), .enable(Write), .MemToReg_in(ex_mem_1_memtoreg_out),
    .MemToReg_out(mem_wb_1_memtoreg_out), .MemWrite_in(ex_mem_1_memwrite_out),
    .RegWrite_in(ex_mem_1_regwrite_out), .RegWrite_out(RegWrite), .JAL_in(ex_mem_1_jal_out),
    .JAL_out(mem_wb_1_jal_out), .LB_in(ex_mem_1_lb_out), .IR_in(ex_mem_1_ir_out), .IR_out(mem_wb_1_ir_out),
    .PC_in(ex_mem_1_pc_out), .PC_out(mem_wb_1_pc_out), .ALUResult_in(ex_mem_1_aluresult_out),
    .ALUResult_out(mem_wb_1_aluresult_out), .Memorydata_in(ram_1_data),
    .Memorydata_out(mem_wb_1_memorydata_out), .RegDst_in(ex_mem_1_regdst_out),
    .RegDst_out(mem_wb_1_regdst_out), .Syscall_in(ex_mem_1_syscall_out), .Syscall_out(mem_wb_1_syscall_out),
    .equal_in(ex_mem_1_equal_out), .equal_out(mem_wb_1_equal_out), .OldPC_in(ex_mem_1_oldpc_out));  // open: MemWrite_out, LB_out, OldPC_out, pause_in, pause_out
  and and_4 (Show, Syscall, mem_wb_1_equal_out);
  not not_4 (not_4_out, mem_wb_1_equal_out);
  Multiplexer #(.width(5), .enable("false")) multiplexer_10 (
    .in0(mem_wb_1_ir_out[20:16]), .in1(mem_wb_1_ir_out[15:11]), .out(multiplexer_10_out),
    .sel(mem_wb_1_regdst_out));
  and and_5 (Pause, mem_wb_1_syscall_out, not_4_out);
  Multiplexer #(.width(5), .enable("false")) multiplexer_11 (
    .in0(multiplexer_10_out), .in1({5{1'b1}}), .out(W_num), .sel(mem_wb_1_jal_out));
  Multiplexer #(.width(32), .enable("false")) multiplexer_12 (
    .in0(mem_wb_1_aluresult_out), .in1(mem_wb_1_memorydata_out), .out(multiplexer_12_out),
    .sel(mem_wb_1_memtoreg_out));
  Multiplexer #(.width(32), .enable("false")) multiplexer_13 (
    .in0(multiplexer_12_out), .in1(mem_wb_1_pc_out), .out(Din), .sel(mem_wb_1_jal_out));

  // Notes on the sheet:
  //   中断源
  //   中断等待指示
  //   数码管输出
  //   contents of rom_1 (hex, n*v repeats v):
  //   20110020 20020022 8000c06 20110000 20110000 2002000a 10000003 20110000 20110000 2002000a 14110003
  //   20110000 20110000 2002000a c000c14 2002000a 0 0 0 c 2231ffff 0 0 0 112020 0 0 0 c 1620fff6 3e00008
  //   OP
  //   Func
  //   OP
  //   Func
  //   流水调试日志用
endmodule

module \气泡流水线  (
  output RegWrite,
  output MemWrite,
  output [31:0] IF_PC,
  output [31:0] ID_PC,
  output [31:0] EX_PC,
  output [31:0] M_PC,
  output [31:0] WB_PC,
  output [31:0] RDin,
  output [31:0] MDin,
  output [31:0] LedData
);

  wire AluSrc, and_2_out, and_3_out, and_4_out, and_5_out, and_6_out, BGEZ, BGEZ_SIGN, CLK, comparator_1_lt,
       Con_flag, Equal, ex_mem_1_equal_out, ex_mem_1_jal_out, ex_mem_1_lb_out, ex_mem_1_memtoreg_out,
       ex_mem_1_regdst_out, ex_mem_1_syscall_out, ExRegW, Go, id_ex_1_beq_out, id_ex_1_bne_out,
       id_ex_1_jal_out, id_ex_1_lb_out, id_ex_1_memtoreg_out, id_ex_1_memwrite_out, id_ex_1_regdst_out, IR1,
       IR2, IR3, J, JMP, JR, LB, mem_wb_1_equal_out, mem_wb_1_jal_out, mem_wb_1_memtoreg_out,
       mem_wb_1_regdst_out, mem_wb_1_syscall_out, MemRegWrite, multiplexer_4_out, not_1_out, not_2_out,
       not_3_out, not_4_out, not_5_out, not_6_out, or_1_out, Pause, RST, Show, SignExt, Syscall, W1, W2, W3,
       Write, \单周期硬布线控制器_1_alu_src , \单周期硬布线控制器_1_beq , \单周期硬布线控制器_1_bgez , \单周期硬布线控制器_1_bne ,
       \单周期硬布线控制器_1_jal , \单周期硬布线控制器_1_jmp , \单周期硬布线控制器_1_jr , \单周期硬布线控制器_1_lb , \单周期硬布线控制器_1_memtoreg ,
       \单周期硬布线控制器_1_memwrite , \单周期硬布线控制器_1_regdst , \单周期硬布线控制器_1_regwrite , \单周期硬布线控制器_1_syscall , \数据相关 ;
  wire [3:0] id_ex_1_aluop_out, \单周期硬布线控制器_1_alu_op ;
  wire [4:0] ExW_num, MemW_num, multiplexer_9_out, multiplexer_12_out, multiplexer_14_out, R1_num, R2_num,
       W_num;
  wire [5:0] Func, OP;
  wire [7:0] multiplexer_17_out;
  wire [15:0] \LoadUse次数 , \总周期数 , \插入气泡数 , \无条件分支数 , \条件分支成功数 ;
  wire [25:6] if_id_1_ir_out;
  wire [27:0] shifter_3_out;
  wire [31:0] adder_1_out, adder_3_out, BGEZ_PC, bit_extender_1_out, bit_extender_2_out, bit_extender_3_out,
       ex_mem_1_aluresult_out, ex_mem_1_ir_out, ex_mem_1_pc_out, EX_PC_t, ID_PC_t, if_id_1_pc_out, IF_PC_t,
       Immediate, IR, MEM_PC, mem_wb_1_aluresult_out, mem_wb_1_ir_out, mem_wb_1_memorydata_out,
       mem_wb_1_pc_out, mips_alu_1_result, mips_probe_1_p1, multiplexer_1_out, multiplexer_2_out,
       multiplexer_3_out, multiplexer_7_out, multiplexer_8_out, multiplexer_11_out, multiplexer_16_out,
       multiplexer_18_out, PC_add4, R1, R2, ram_1_data, regfile_hacked_bubble_1_r1,
       regfile_hacked_bubble_1_r2, shifter_1_out, shifter_2_out, WB_PC_t;

  Button \u_总复位  (.out(RST));
  Button _1 (.out(IR1));
  Button _2 (.out(IR2));
  Button _3 (.out(IR3));
  Button \u_继续运行  (.out(Go));
  LED led_1 (.in(W1));
  LED led_2 (.in(W2));
  LED led_3 (.in(W3));
  nand nand_1 (Write, not_2_out, Pause);
  Multiplexer #(.width(32), .enable("false")) multiplexer_1 (
    .in0(adder_3_out), .in1(adder_1_out), .out(multiplexer_1_out), .sel(Con_flag));
  Shifter #(.width(32)) shifter_1 (.in(Immediate), .\dist (5'b00010), .out(shifter_1_out));
  Hex_Digit_Display hex_digit_display_1 (.value(LedData[31:28]));  // open: dp
  \数据相关检测  \u_数据相关检测_1  (
    .OP(OP), .EX_WriteReg_num(ExW_num), .EX_RegWrite(ExRegW), .MEM_WriteReg_num(MemW_num),
    .MEM_RegWrite(MemRegWrite), .\数据相关 (\数据相关 ), .Func(Func), .ID_R1_num(R1_num), .ID_R2_num(R2_num));
  Register #(.width(32)) register_1 (.D(R2), .Q(LedData), .clk(Show), .clr(RST));  // open: en
  Comparator #(.width(32)) comparator_1 (.a(R1), .b({32{1'b0}}), .lt(comparator_1_lt));  // open: gt, eq
  not not_1 (not_1_out, comparator_1_lt);
  Shifter #(.width(32)) shifter_2 (.in(Immediate), .\dist (5'b00010), .out(shifter_2_out));
  not not_2 (not_2_out, Go);
  Multiplexer #(.select(2), .width(32), .enable("false")) multiplexer_2 (
    .in0(multiplexer_1_out), .in1(R1), .in2({PC_add4[31:28], shifter_3_out}), .in3(R1),
    .out(multiplexer_2_out), .sel({JMP, JR}));
  Multiplexer #(.width(32), .enable("false")) multiplexer_3 (
    .in0(multiplexer_2_out), .in1(BGEZ_PC), .out(multiplexer_3_out), .sel(BGEZ_SIGN));
  Adder #(.width(32)) adder_1 (.a(shifter_1_out), .b(PC_add4), .out(adder_1_out));  // open: cin, cout
  Hex_Digit_Display hex_digit_display_2 (.value(LedData[23:20]));  // open: dp
  Hex_Digit_Display hex_digit_display_3 (.value(LedData[27:24]));  // open: dp
  and and_1 (BGEZ_SIGN, not_1_out, BGEZ);
  Adder #(.width(32)) adder_2 (.a(shifter_2_out), .b(PC_add4), .out(BGEZ_PC));  // open: cin, cout
  not not_3 (not_3_out, \数据相关 );
  Shifter #(.width(28)) shifter_3 (.in(IR[27:0]), .\dist (5'b00010), .out(shifter_3_out));
  Hex_Digit_Display hex_digit_display_4 (.value(LedData[19:16]));  // open: dp
  Hex_Digit_Display hex_digit_display_5 (.value(LedData[15:12]));  // open: dp
  Multiplexer #(.enable("false")) multiplexer_4 (.in0(1'b1), .in1(Go), .out(multiplexer_4_out), .sel(Pause));
  and and_2 (and_2_out, not_3_out, multiplexer_4_out);
  Register #(.width(32)) PC (.D(multiplexer_3_out), .en(and_2_out), .Q(IF_PC_t), .clk(CLK), .clr(RST));
  Hex_Digit_Display hex_digit_display_6 (.value(LedData[11:8]));  // open: dp
  Hex_Digit_Display hex_digit_display_7 (.value(LedData[7:4]));  // open: dp
  Clock clock_1 (.out(CLK));
  Counter #(.width(16), .max('hffff)) counter_1 (
    .load(1'b0), .count(multiplexer_4_out), .Q(\总周期数 ), .clk(CLK), .clr(RST));  // open: D, carry
  Hex_Digit_Display hex_digit_display_8 (.value(LedData[3:0]));  // open: dp
  // Probe on IF_PC_t[11:2]
  Adder #(.width(32)) adder_3 (.a(IF_PC_t), .b(32'h4), .out(adder_3_out));  // open: cin, cout
  // Probe on \总周期数 
  // Probe on EX_PC_t[11:2]
  // Probe on ID_PC_t[11:2]
  // Mips_Probe mips_probe_1: pin names not known; wires that end beside it: mips_probe_1_p1
  ROM #(.addrWidth(10), .dataWidth(32)) rom_1 (.addr(IF_PC_t[11:2]), .data(mips_probe_1_p1));  // open: sel
  // Probe on \无条件分支数 
  // Probe on \条件分支成功数 
  // Probe on \插入气泡数 
  // Probe on \LoadUse次数 
  // Probe on MEM_PC[11:2]
  not not_4 (not_4_out, \数据相关 );
  and and_3 (and_3_out, not_4_out, Write);
  IF_ID if_id_1 (
    .IR_in(mips_probe_1_p1), .PC_in(adder_3_out), .\气泡_高电平时有效 (J), .clk(CLK), .clear(RST),
    .enable(and_3_out), .IR_out({OP, if_id_1_ir_out, Func}), .PC_out(if_id_1_pc_out), .OldPC_in(IF_PC_t),
    .OldPC_out(ID_PC_t));
  // Probe on \总周期数 
  // Probe on WB_PC_t[11:2]
  \单周期硬布线控制器  \u_单周期硬布线控制器_1  (
    .Func(Func), .OP(OP), .ALU_OP(\单周期硬布线控制器_1_alu_op ), .MemToReg(\单周期硬布线控制器_1_memtoreg ),
    .MemWrite(\单周期硬布线控制器_1_memwrite ), .ALU_SRC(\单周期硬布线控制器_1_alu_src ), .RegWrite(\单周期硬布线控制器_1_regwrite ),
    .SysCALL(\单周期硬布线控制器_1_syscall ), .SignedExt(SignExt), .RegDst(\单周期硬布线控制器_1_regdst ),
    .JR(\单周期硬布线控制器_1_jr ), .JMP(\单周期硬布线控制器_1_jmp ), .Beq(\单周期硬布线控制器_1_beq ), .JAL(\单周期硬布线控制器_1_jal ),
    .Bne(\单周期硬布线控制器_1_bne ), .LB(\单周期硬布线控制器_1_lb ), .BGEZ(\单周期硬布线控制器_1_bgez ));
  Multiplexer #(.width(5), .enable("false")) multiplexer_5 (
    .in0(if_id_1_ir_out[25:21]), .in1(5'b00010), .out(R1_num), .sel(\单周期硬布线控制器_1_syscall ));
  Multiplexer #(.width(5), .enable("false")) multiplexer_6 (
    .in0(if_id_1_ir_out[20:16]), .in1(5'b00100), .out(R2_num), .sel(\单周期硬布线控制器_1_syscall ));
  // Probe on W_num
  assign bit_extender_1_out = {{16{1'b0}}, {if_id_1_ir_out[15:6], Func}};  // Bit_Extender bit_extender_1
  assign bit_extender_2_out = {{16{if_id_1_ir_out[15]}}, {if_id_1_ir_out[15:6], Func}};  // Bit_Extender bit_extender_2
  Multiplexer #(.width(32), .enable("false")) multiplexer_7 (
    .in0(bit_extender_1_out), .in1(bit_extender_2_out), .out(multiplexer_7_out), .sel(SignExt));
  PC_JUDGE pc_judge_1 (.PC_raw32b(IF_PC_t), .PC_judge(IF_PC));
  PC_JUDGE pc_judge_2 (.PC_raw32b(ID_PC_t), .PC_judge(ID_PC));
  PC_JUDGE pc_judge_3 (.PC_raw32b(EX_PC_t), .PC_judge(EX_PC));
  PC_JUDGE pc_judge_4 (.PC_raw32b(MEM_PC), .PC_judge(M_PC));
  PC_JUDGE pc_judge_5 (.PC_raw32b(WB_PC_t), .PC_judge(WB_PC));
  Regfile_Hacked_Bubble regfile_hacked_bubble_1 (
    .R1_num(R1_num), .R2_num(R2_num), .W_num(W_num), .Din(RDin), .R1(regfile_hacked_bubble_1_r1),
    .R2(regfile_hacked_bubble_1_r2), .WE(RegWrite), .Clk(CLK));
  or or_1 (or_1_out, \数据相关 , J);
  ID_EX id_ex_1 (
    .Beq_in(\单周期硬布线控制器_1_beq ), .Bne_in(\单周期硬布线控制器_1_bne ), .MemToReg_in(\单周期硬布线控制器_1_memtoreg ),
    .MemWrite_in(\单周期硬布线控制器_1_memwrite ), .AluOP_in(\单周期硬布线控制器_1_alu_op ), .AluSrc_in(\单周期硬布线控制器_1_alu_src ),
    .RegWrite_in(\单周期硬布线控制器_1_regwrite ), .JAL_in(\单周期硬布线控制器_1_jal ), .RegDst_in(\单周期硬布线控制器_1_regdst ),
    .Syscall_in(\单周期硬布线控制器_1_syscall ), .JMP_in(\单周期硬布线控制器_1_jmp ), .JR_in(\单周期硬布线控制器_1_jr ),
    .SignedExt_in(SignExt), .LB_in(\单周期硬布线控制器_1_lb ), .BGEZ_in(\单周期硬布线控制器_1_bgez ),
    .IR_in({OP, if_id_1_ir_out, Func}), .PC_in(if_id_1_pc_out), .R1_in(regfile_hacked_bubble_1_r1),
    .R2_in(regfile_hacked_bubble_1_r2), .Imm_in(multiplexer_7_out), .Beq_out(id_ex_1_beq_out),
    .Bne_out(id_ex_1_bne_out), .MemToReg_out(id_ex_1_memtoreg_out), .MemWrite_out(id_ex_1_memwrite_out),
    .AluOP_out(id_ex_1_aluop_out), .AluSrc_out(AluSrc), .RegWrite_out(ExRegW), .JAL_out(id_ex_1_jal_out),
    .RegDst_out(id_ex_1_regdst_out), .Syscall_out(Syscall), .JMP_out(JMP), .JR_out(JR),
    .LB_out(id_ex_1_lb_out), .BGEZ_out(BGEZ), .IR_out(IR), .PC_out(PC_add4), .R1_out(R1), .R2_out(R2),
    .Imm_out(Immediate), .clk(CLK), .clear(RST), .enable(Write), .\气泡_高电平时有效 (or_1_out), .OldPC_in(ID_PC_t),
    .OldPC_out(EX_PC_t));  // open: SignedExt_out
  Multiplexer #(.width(32), .enable("false")) multiplexer_8 (
    .in0(R2), .in1(Immediate), .out(multiplexer_8_out), .sel(AluSrc));
  Multiplexer #(.width(5), .enable("false")) multiplexer_9 (
    .in0(IR[20:16]), .in1(IR[15:11]), .out(multiplexer_9_out), .sel(id_ex_1_regdst_out));
  Multiplexer #(.width(5), .enable("false")) multiplexer_10 (
    .in0(multiplexer_9_out), .in1({5{1'b1}}), .out(ExW_num), .sel(id_ex_1_jal_out));
  and and_4 (and_4_out, Equal, id_ex_1_beq_out);
  not not_5 (not_5_out, Equal);
  and and_5 (and_5_out, not_5_out, id_ex_1_bne_out);
  Multiplexer #(.width(32), .enable("false")) multiplexer_11 (
    .in0(multiplexer_8_out), .in1(32'h22), .out(multiplexer_11_out), .sel(Syscall));
  and and_6 (and_6_out, Write, \数据相关 );
  or or_2 (Con_flag, BGEZ_SIGN, and_4_out, and_5_out);
  MIPS_ALU mips_alu_1 (
    .X(R1), .Y(multiplexer_11_out), .AluOP(id_ex_1_aluop_out), .Equal(Equal), .Result(mips_alu_1_result),
    .shamt(IR[10:6]));  // open: Result_2
  Counter #(.width(16), .max('hffff)) counter_2 (
    .D({16{1'b0}}), .count(and_6_out), .Q(\插入气泡数 ), .clk(CLK), .clr(RST));  // open: load, carry
  Counter #(.width(16), .max('hffff)) counter_3 (
    .load(1'b0), .count(Con_flag), .Q(\条件分支成功数 ), .clk(CLK), .clr(RST));  // open: D, carry
  or or_3 (J, JMP, JR, Con_flag);
  Counter #(.width(16), .max('hffff)) counter_4 (
    .load(1'b0), .count(JMP), .Q(\无条件分支数 ), .clk(CLK), .clr(RST));  // open: D, carry
  EX_MEM ex_mem_1 (
    .\气泡_高电平时有效 (1'b0), .clk(CLK), .clear(RST), .enable(Write), .MemToReg_in(id_ex_1_memtoreg_out),
    .MemToReg_out(ex_mem_1_memtoreg_out), .MemWrite_in(id_ex_1_memwrite_out), .MemWrite_out(MemWrite),
    .RegWrite_in(ExRegW), .RegWrite_out(MemRegWrite), .JAL_in(id_ex_1_jal_out), .JAL_out(ex_mem_1_jal_out),
    .LB_in(id_ex_1_lb_out), .LB_out(ex_mem_1_lb_out), .IR_in(IR), .IR_out(ex_mem_1_ir_out), .PC_in(PC_add4),
    .PC_out(ex_mem_1_pc_out), .ALUResult_in(mips_alu_1_result), .ALUResult_out(ex_mem_1_aluresult_out),
    .R2_in(R2), .R2_out(MDin), .RegDst_in(id_ex_1_regdst_out), .RegDst_out(ex_mem_1_regdst_out),
    .Syscall_in(Syscall), .Syscall_out(ex_mem_1_syscall_out), .equal_in(Equal),
    .equal_out(ex_mem_1_equal_out), .OldPC_in(EX_PC_t), .OldPC_out(MEM_PC));  // open: pause_in, pause_out
  Multiplexer #(.width(5), .enable("false")) multiplexer_12 (
    .in0(ex_mem_1_ir_out[20:16]), .in1(ex_mem_1_ir_out[15:11]), .out(multiplexer_12_out),
    .sel(ex_mem_1_regdst_out));
  Multiplexer #(.width(5), .enable("false")) multiplexer_13 (
    .in0(multiplexer_12_out), .in1({5{1'b1}}), .out(MemW_num), .sel(ex_mem_1_jal_out));
  RAM #(.addrWidth(10), .dataWidth(32), .bus("separate")) ram_1 (
    .addr(ex_mem_1_aluresult_out[11:2]), .din(MDin), .data(ram_1_data), .str(MemWrite), .clk(CLK), .clr(RST));  // open: sel, ld
  MEM_WB mem_wb_1 (
    .\气泡_高电平时有效 (1'b0), .clk(CLK), .clear(RST), .enable(Write), .MemToReg_in(ex_mem_1_memtoreg_out),
    .MemToReg_out(mem_wb_1_memtoreg_out), .MemWrite_in(MemWrite), .RegWrite_in(MemRegWrite),
    .RegWrite_out(RegWrite), .JAL_in(ex_mem_1_jal_out), .JAL_out(mem_wb_1_jal_out), .LB_in(ex_mem_1_lb_out),
    .LB_out(LB), .IR_in(ex_mem_1_ir_out), .IR_out(mem_wb_1_ir_out), .PC_in(ex_mem_1_pc_out),
    .PC_out(mem_wb_1_pc_out), .ALUResult_in(ex_mem_1_aluresult_out), .ALUResult_out(mem_wb_1_aluresult_out),
    .Memorydata_in(ram_1_data), .Memorydata_out(mem_wb_1_memorydata_out), .RegDst_in(ex_mem_1_regdst_out),
    .RegDst_out(mem_wb_1_regdst_out), .Syscall_in(ex_mem_1_syscall_out), .Syscall_out(mem_wb_1_syscall_out),
    .equal_in(ex_mem_1_equal_out), .equal_out(mem_wb_1_equal_out), .OldPC_in(MEM_PC), .OldPC_out(WB_PC_t));  // open: MemWrite_out, pause_in, pause_out
  and and_7 (Show, Syscall, mem_wb_1_equal_out);
  not not_6 (not_6_out, mem_wb_1_equal_out);
  and and_8 (Pause, mem_wb_1_syscall_out, not_6_out);
  Multiplexer #(.width(5), .enable("false")) multiplexer_14 (
    .in0(mem_wb_1_ir_out[20:16]), .in1(mem_wb_1_ir_out[15:11]), .out(multiplexer_14_out),
    .sel(mem_wb_1_regdst_out));
  Multiplexer #(.width(5), .enable("false")) multiplexer_15 (
    .in0(multiplexer_14_out), .in1({5{1'b1}}), .out(W_num), .sel(mem_wb_1_jal_out));
  Multiplexer #(.width(32), .enable("false")) multiplexer_16 (
    .in0(mem_wb_1_aluresult_out), .in1(mem_wb_1_memorydata_out), .out(multiplexer_16_out),
    .sel(mem_wb_1_memtoreg_out));
  Multiplexer #(.select(2), .width(8), .enable("false")) multiplexer_17 (
    .in0(multiplexer_16_out[7:0]), .in1(multiplexer_16_out[15:8]), .in2(multiplexer_16_out[23:16]),
    .in3(multiplexer_16_out[31:24]), .out(multiplexer_17_out), .sel(mem_wb_1_aluresult_out[1:0]));
  assign bit_extender_3_out = {{24{multiplexer_17_out[7]}}, multiplexer_17_out};  // Bit_Extender bit_extender_3
  Multiplexer #(.width(32), .enable("false")) multiplexer_18 (
    .in0(multiplexer_16_out), .in1(bit_extender_3_out), .out(multiplexer_18_out), .sel(LB));
  Multiplexer #(.width(32), .enable("false")) multiplexer_19 (
    .in0(multiplexer_18_out), .in1(mem_wb_1_pc_out), .out(RDin), .sel(mem_wb_1_jal_out));

  // Other names for the same wires on the sheet: MemWrite_grade = MemWrite; RDin_mon[31:0] = RDin

  // Notes on the sheet:
  //   中断源
  //   中断等待指示
  //   数码管输出
  //   contents of rom_1 (hex, n*v repeats v):
  //   20110001 8000c05 20110001 20120002 20130003 8000c09 20110001 20120002 20130003 8000c0d 20110001
  //   20120002 20130003 8000c11 20110001 20120002 20130003 c000cb8 20100001 20110001 118fc0 112020
  //   20020022 c 118882 12200001 8000c15 112020 20020022 c 20110001 118880 112020 20020022 c 12200001
  //   8000c1f 20110001 118fc0 112020 20020022 c 1188c3 112020 20020022 c 118903 112020 20020022 c 118903
  //   112020 20020022 c 118903 112020 20020022 c 118903 112020 20020022 c 118903 112020 20020022 c 118903
  //   112020 20020022 c 118903 112020 20020022 c 20100001 109fc0 139fc3 8021 2012000c 24160003 26100001
  //   3210000f 20080008 20090001 139900 2709825 132020 20020022 c 1094022 1500fff9 22100001 2018000f
  //   2188024 108700 20080008 20090001 139902 2709825 132021 20020022 c 1094022 1500fff9 108702 2c9b022
  //   12c00001 8000c50 4020 1084027 84400 3508ffff 82021 20020022 c 2010ffff 20110000 ae300000 22100001
  //   22310004 ae300000 22100001 22310004 ae300000 22100001 22310004 ae300000 22100001 22310004 ae300000
  //   22100001 22310004 ae300000 22100001 22310004 ae300000 22100001 22310004 ae300000 22100001 22310004
  //   ae300000 22100001 22310004 ae300000 22100001 22310004 ae300000 22100001 22310004 ae300000 22100001
  //   22310004 ae300000 22100001 22310004 ae300000 22100001 22310004 ae300000 22100001 22310004 ae300000
  //   22100001 22310004 22100001 8020 2011003c 8e130000 8e340000 274402a 11000002 ae330000 ae140000
  //   2231fffc 1611fff8 102020 20020022 c 22100004 2011003c 1611fff2 20020032 c 20100000 22100001 102020
  //   20020022 c 22100002 102020 20020022 c 22100003 102020 20020022 c 22100004 102020 20020022 c 22100005
  //   102020 20020022 c 22100006 102020 20020022 c 22100007 102020 20020022 c 22100008 102020 20020022
  //   20020022 c 3e00008
  //   OP
  //   Func
  //   OP
  //   Func
  //   流水调试日志用
  //   为方便自动评测，需要输出流水线各段保存的PC值，注意是PC不是PC+4，另外ID段寄存器写入信息，Mem段内存写入信息也要输出
endmodule

module \重定向流水线  (
  output RegWrite,
  output MemWrite,
  output [31:0] IF_PC,
  output [31:0] ID_PC,
  output [31:0] EX_PC,
  output [31:0] M_PC,
  output [31:0] WB_PC,
  output [31:0] RDin,
  output [31:0] MDin,
  output [31:0] LedData
);

  wire AluSrc, and_2_out, and_3_out, and_4_out, and_5_out, and_6_out, BGEZ, BGEZ_SIGN, CLK, comparator_1_lt,
       Con_flag, Equal, ex_mem_1_equal_out, ex_mem_1_jal_out, ex_mem_1_lb_out, ex_mem_1_pause_out,
       ex_mem_1_regdst_out, ex_mem_1_syscall_out, ExRegW, Go, id_ex_1_beq_out, id_ex_1_bne_out,
       id_ex_1_jal_out, id_ex_1_lb_out, id_ex_1_memtoreg_out, id_ex_1_memwrite_out, id_ex_1_regdst_out, IR1,
       IR2, IR3, J, JMP, JR, LB, load_use, mem_wb_1_jal_out, mem_wb_1_memtoreg_out, mem_wb_1_regdst_out,
       MemRegWrite, MemToReg, multiplexer_4_out, not_1_out, not_2_out, not_3_out, not_4_out, not_5_out,
       not_6_out, Old_Pause, or_1_out, or_2_out, Pause, RST, Show, SignExt, Syscall, V0__34, W1, W2, W3,
       Write, \单周期硬布线控制器_1_alu_src , \单周期硬布线控制器_1_beq , \单周期硬布线控制器_1_bgez , \单周期硬布线控制器_1_bne ,
       \单周期硬布线控制器_1_jal , \单周期硬布线控制器_1_jmp , \单周期硬布线控制器_1_jr , \单周期硬布线控制器_1_lb , \单周期硬布线控制器_1_memtoreg ,
       \单周期硬布线控制器_1_memwrite , \单周期硬布线控制器_1_regdst , \单周期硬布线控制器_1_regwrite , \单周期硬布线控制器_1_syscall ;
  wire [1:0] Choose_R1, Choose_R2, \load_use及重定向相关_1_choose_r1 , \load_use及重定向相关_1_choose_r2 ,
       multiplexer_5_out, multiplexer_6_out;
  wire [3:0] id_ex_1_aluop_out, \单周期硬布线控制器_1_alu_op ;
  wire [4:0] ExW_num, MemW_num, multiplexer_10_out, multiplexer_15_out, multiplexer_17_out, R1_num, R2_num,
       W_num;
  wire [5:0] Ex_OP, Func, OP;
  wire [7:0] multiplexer_19_out;
  wire [15:0] \LoadUse次数 , \总周期数 , \插入气泡数 , \无条件分支数 , \条件分支成功数 ;
  wire [25:0] IR;
  wire [25:6] if_id_1_ir_out;
  wire [27:0] shifter_2_out;
  wire [31:0] adder_1_out, adder_3_out, BGEZ_PC, bit_extender_1_out, bit_extender_2_out, bit_extender_3_out,
       ex_mem_1_ir_out, ex_mem_1_pc_out, EX_PC_t, ID_PC_t, if_id_1_pc_out, IF_PC_t, Immediate, Mem_MemData,
       MEM_PC, mem_wb_1_ir_out, mem_wb_1_pc_out, mips_alu_1_result, multiplexer_1_out, multiplexer_2_out,
       multiplexer_3_out, multiplexer_9_out, multiplexer_12_out, multiplexer_14_out, multiplexer_21_out,
       new_R1, new_R2, NewALUResult, Old_MemData, OldALUResult, PC_add4, R1, R2, ram_1_data,
       regfile_hacked_bubble_1_r1, regfile_hacked_bubble_1_r2, rom_1_data, shifter_1_out, shifter_3_out,
       WB_PC_t;

  Button \u_总复位  (.out(RST));
  Button _1 (.out(IR1));
  Button _2 (.out(IR2));
  Button _3 (.out(IR3));
  Button \u_继续运行  (.out(Go));
  LED led_1 (.in(W1));
  LED led_2 (.in(W2));
  LED led_3 (.in(W3));
  nand nand_1 (Write, not_1_out, Pause);
  Multiplexer #(.width(32), .enable("false")) multiplexer_1 (
    .in0(adder_3_out), .in1(adder_1_out), .out(multiplexer_1_out), .sel(Con_flag));
  Shifter #(.width(32)) shifter_1 (.in(Immediate), .\dist (5'b00010), .out(shifter_1_out));
  Hex_Digit_Display hex_digit_display_1 (.value(LedData[31:28]));  // open: dp
  not not_1 (not_1_out, Go);
  Multiplexer #(.select(2), .width(32), .enable("false")) multiplexer_2 (
    .in0(multiplexer_1_out), .in1(new_R1), .in2({PC_add4[31:28], shifter_2_out}), .in3(new_R1),
    .out(multiplexer_2_out), .sel({JMP, JR}));
  Multiplexer #(.width(32), .enable("false")) multiplexer_3 (
    .in0(multiplexer_2_out), .in1(BGEZ_PC), .out(multiplexer_3_out), .sel(BGEZ_SIGN));
  Adder #(.width(32)) adder_1 (.a(shifter_1_out), .b(PC_add4), .out(adder_1_out));  // open: cin, cout
  Hex_Digit_Display hex_digit_display_2 (.value(LedData[23:20]));  // open: dp
  Hex_Digit_Display hex_digit_display_3 (.value(LedData[27:24]));  // open: dp
  Register #(.width(32)) register_1 (.D(new_R2), .Q(LedData), .clk(Show), .clr(RST));  // open: en
  Comparator #(.width(32)) comparator_1 (.a(new_R1), .b({32{1'b0}}), .lt(comparator_1_lt));  // open: gt, eq
  Shifter #(.width(28)) shifter_2 (.in({Ex_OP[1:0], IR}), .\dist (5'b00010), .out(shifter_2_out));
  Hex_Digit_Display hex_digit_display_4 (.value(LedData[15:12]));  // open: dp
  Hex_Digit_Display hex_digit_display_5 (.value(LedData[19:16]));  // open: dp
  not not_2 (not_2_out, comparator_1_lt);
  and and_1 (BGEZ_SIGN, not_2_out, BGEZ);
  Shifter #(.width(32)) shifter_3 (.in(Immediate), .\dist (5'b00010), .out(shifter_3_out));
  Adder #(.width(32)) adder_2 (.a(shifter_3_out), .b(PC_add4), .out(BGEZ_PC));  // open: cin, cout
  Multiplexer #(.enable("false")) multiplexer_4 (.in0(1'b1), .in1(Go), .out(multiplexer_4_out), .sel(Pause));
  not not_3 (not_3_out, load_use);
  and and_2 (and_2_out, not_3_out, multiplexer_4_out);
  Register #(.width(32)) PC (.D(multiplexer_3_out), .en(and_2_out), .Q(IF_PC_t), .clk(CLK), .clr(RST));
  Hex_Digit_Display hex_digit_display_6 (.value(LedData[7:4]));  // open: dp
  Hex_Digit_Display hex_digit_display_7 (.value(LedData[11:8]));  // open: dp
  Clock clock_1 (.out(CLK));
  Counter #(.width(16), .max('hffff)) counter_1 (
    .load(1'b0), .count(multiplexer_4_out), .Q(\总周期数 ), .clk(CLK), .clr(RST));  // open: D, carry
  Hex_Digit_Display hex_digit_display_8 (.value(LedData[3:0]));  // open: dp
  Adder #(.width(32)) adder_3 (.a(IF_PC_t), .b(32'h4), .out(adder_3_out));  // open: cin, cout
  ROM #(.addrWidth(10), .dataWidth(32)) rom_1 (.addr(IF_PC_t[11:2]), .data(rom_1_data));  // open: sel
  // Probe on \总周期数 
  // Probe on \无条件分支数 
  // Probe on \条件分支成功数 
  // Probe on \插入气泡数 
  // Probe on \LoadUse次数 
  \load_use及重定向相关  \load_use及重定向相关_1  (
    .load_use(load_use), .Choose_R1(\load_use及重定向相关_1_choose_r1 ), .Ex_OP(Ex_OP),
    .Choose_R2(\load_use及重定向相关_1_choose_r2 ), .Ex_WriteReg_num(ExW_num), .Mem_WriteReg_num(MemW_num),
    .Ex_RegWrite_num(ExRegW), .OP(OP), .Mem_RegWrite_num(MemRegWrite), .FUNC(Func), .MemToReg(MemToReg),
    .ID_R2_num(R2_num), .ID_R1_num(R1_num));
  not not_4 (not_4_out, load_use);
  and and_3 (and_3_out, not_4_out, Write);
  IF_ID if_id_1 (
    .IR_in(rom_1_data), .PC_in(adder_3_out), .\气泡_高电平时有效 (J), .clk(CLK), .clear(RST), .enable(and_3_out),
    .IR_out({OP, if_id_1_ir_out, Func}), .PC_out(if_id_1_pc_out), .OldPC_in(IF_PC_t), .OldPC_out(ID_PC_t));
  // Probe on IF_PC_t[11:0]
  or or_1 (or_1_out, J, load_use);
  Multiplexer #(.width(2), .enable("false")) multiplexer_5 (
    .in0(\load_use及重定向相关_1_choose_r1 ), .in1(2'b00), .out(multiplexer_5_out), .sel(or_1_out));
  Multiplexer #(.width(2), .enable("false")) multiplexer_6 (
    .in0(\load_use及重定向相关_1_choose_r2 ), .in1(2'b00), .out(multiplexer_6_out), .sel(or_1_out));
  // Probe on ID_PC_t[11:0]
  Register #(.width(2)) register_2 (.D(multiplexer_5_out), .en(Write), .Q(Choose_R1), .clk(CLK), .clr(RST));
  Register #(.width(2)) register_3 (.D(multiplexer_6_out), .en(Write), .Q(Choose_R2), .clk(CLK), .clr(RST));
  \单周期硬布线控制器  \u_单周期硬布线控制器_1  (
    .Func(Func), .OP(OP), .ALU_OP(\单周期硬布线控制器_1_alu_op ), .MemToReg(\单周期硬布线控制器_1_memtoreg ),
    .MemWrite(\单周期硬布线控制器_1_memwrite ), .ALU_SRC(\单周期硬布线控制器_1_alu_src ), .RegWrite(\单周期硬布线控制器_1_regwrite ),
    .SysCALL(\单周期硬布线控制器_1_syscall ), .SignedExt(SignExt), .RegDst(\单周期硬布线控制器_1_regdst ),
    .JR(\单周期硬布线控制器_1_jr ), .JMP(\单周期硬布线控制器_1_jmp ), .Beq(\单周期硬布线控制器_1_beq ), .JAL(\单周期硬布线控制器_1_jal ),
    .Bne(\单周期硬布线控制器_1_bne ), .LB(\单周期硬布线控制器_1_lb ), .BGEZ(\单周期硬布线控制器_1_bgez ));
  Multiplexer #(.width(5), .enable("false")) multiplexer_7 (
    .in0(if_id_1_ir_out[25:21]), .in1(5'b00010), .out(R1_num), .sel(\单周期硬布线控制器_1_syscall ));
  Multiplexer #(.width(5), .enable("false")) multiplexer_8 (
    .in0(if_id_1_ir_out[20:16]), .in1(5'b00100), .out(R2_num), .sel(\单周期硬布线控制器_1_syscall ));
  // Probe on W_num
  assign bit_extender_1_out = {{16{1'b0}}, {if_id_1_ir_out[15:6], Func}};  // Bit_Extender bit_extender_1
  assign bit_extender_2_out = {{16{if_id_1_ir_out[15]}}, {if_id_1_ir_out[15:6], Func}};  // Bit_Extender bit_extender_2
  // Probe on MEM_PC[11:0]
  // Probe on EX_PC_t[11:0]
  Multiplexer #(.width(32), .enable("false")) multiplexer_9 (
    .in0(bit_extender_1_out), .in1(bit_extender_2_out), .out(multiplexer_9_out), .sel(SignExt));
  // Probe on WB_PC_t[11:0]
  PC_JUDGE pc_judge_1 (.PC_raw32b(IF_PC_t), .PC_judge(IF_PC));
  PC_JUDGE pc_judge_2 (.PC_raw32b(ID_PC_t), .PC_judge(ID_PC));
  PC_JUDGE pc_judge_3 (.PC_raw32b(EX_PC_t), .PC_judge(EX_PC));
  PC_JUDGE pc_judge_4 (.PC_raw32b(MEM_PC), .PC_judge(M_PC));
  PC_JUDGE pc_judge_5 (.PC_raw32b(WB_PC_t), .PC_judge(WB_PC));
  Regfile_Hacked_Bubble regfile_hacked_bubble_1 (
    .R1_num(R1_num), .R2_num(R2_num), .W_num(W_num), .Din(RDin), .R1(regfile_hacked_bubble_1_r1),
    .R2(regfile_hacked_bubble_1_r2), .WE(RegWrite), .Clk(CLK));
  or or_2 (or_2_out, load_use, J);
  ID_EX id_ex_1 (
    .Beq_in(\单周期硬布线控制器_1_beq ), .Bne_in(\单周期硬布线控制器_1_bne ), .MemToReg_in(\单周期硬布线控制器_1_memtoreg ),
    .MemWrite_in(\单周期硬布线控制器_1_memwrite ), .AluOP_in(\单周期硬布线控制器_1_alu_op ), .AluSrc_in(\单周期硬布线控制器_1_alu_src ),
    .RegWrite_in(\单周期硬布线控制器_1_regwrite ), .JAL_in(\单周期硬布线控制器_1_jal ), .RegDst_in(\单周期硬布线控制器_1_regdst ),
    .Syscall_in(\单周期硬布线控制器_1_syscall ), .JMP_in(\单周期硬布线控制器_1_jmp ), .JR_in(\单周期硬布线控制器_1_jr ),
    .SignedExt_in(SignExt), .LB_in(\单周期硬布线控制器_1_lb ), .BGEZ_in(\单周期硬布线控制器_1_bgez ),
    .IR_in({OP, if_id_1_ir_out, Func}), .PC_in(if_id_1_pc_out), .R1_in(regfile_hacked_bubble_1_r1),
    .R2_in(regfile_hacked_bubble_1_r2), .Imm_in(multiplexer_9_out), .Beq_out(id_ex_1_beq_out),
    .Bne_out(id_ex_1_bne_out), .MemToReg_out(id_ex_1_memtoreg_out), .MemWrite_out(id_ex_1_memwrite_out),
    .AluOP_out(id_ex_1_aluop_out), .AluSrc_out(AluSrc), .RegWrite_out(ExRegW), .JAL_out(id_ex_1_jal_out),
    .RegDst_out(id_ex_1_regdst_out), .Syscall_out(Syscall), .JMP_out(JMP), .JR_out(JR),
    .LB_out(id_ex_1_lb_out), .BGEZ_out(BGEZ), .IR_out({Ex_OP, IR}), .PC_out(PC_add4), .R1_out(R1),
    .R2_out(R2), .Imm_out(Immediate), .clk(CLK), .clear(RST), .enable(Write), .\气泡_高电平时有效 (or_2_out),
    .OldPC_in(ID_PC_t), .OldPC_out(EX_PC_t));  // open: SignedExt_out
  Multiplexer #(.width(5), .enable("false")) multiplexer_10 (
    .in0(IR[20:16]), .in1(IR[15:11]), .out(multiplexer_10_out), .sel(id_ex_1_regdst_out));
  Multiplexer #(.width(5), .enable("false")) multiplexer_11 (
    .in0(multiplexer_10_out), .in1({5{1'b1}}), .out(ExW_num), .sel(id_ex_1_jal_out));
  Multiplexer #(.select(2), .width(32), .enable("false")) multiplexer_12 (
    .in0(R1), .in1(NewALUResult), .in2(OldALUResult), .in3(Mem_MemData), .out(multiplexer_12_out),
    .sel(Choose_R1));
  and and_4 (and_4_out, Equal, id_ex_1_beq_out);
  not not_5 (not_5_out, Equal);
  and and_5 (and_5_out, not_5_out, id_ex_1_bne_out);
  Multiplexer #(.select(2), .width(32), .enable("false")) multiplexer_13 (
    .in0(R2), .in1(NewALUResult), .in2(OldALUResult), .in3(Mem_MemData), .out(new_R2), .sel(Choose_R2));
  Multiplexer #(.width(32), .enable("false")) multiplexer_14 (
    .in0(new_R2), .in1(Immediate), .out(multiplexer_14_out), .sel(AluSrc));
  and and_6 (and_6_out, Write, load_use);
  or or_3 (Con_flag, BGEZ_SIGN, and_4_out, and_5_out);
  MIPS_ALU mips_alu_1 (
    .X(multiplexer_12_out), .Y(multiplexer_14_out), .AluOP(id_ex_1_aluop_out), .Equal(Equal),
    .Result(mips_alu_1_result), .shamt(IR[10:6]));  // open: Result_2
  Counter #(.width(16), .max('hffff)) counter_2 (
    .D({16{1'b0}}), .count(and_6_out), .Q(\LoadUse次数 ), .clk(CLK), .clr(RST));  // open: load, carry
  Counter #(.width(16), .max('hffff)) counter_3 (
    .load(1'b0), .count(Con_flag), .Q(\条件分支成功数 ), .clk(CLK), .clr(RST));  // open: D, carry
  Counter #(.width(16), .max('hffff)) counter_4 (
    .load(1'b0), .count(JMP), .Q(\无条件分支数 ), .clk(CLK), .clr(RST));  // open: D, carry
  or or_4 (J, JMP, JR, Con_flag);
  EX_MEM ex_mem_1 (
    .\气泡_高电平时有效 (1'b0), .clk(CLK), .clear(RST), .enable(Write), .MemToReg_in(id_ex_1_memtoreg_out),
    .MemToReg_out(MemToReg), .MemWrite_in(id_ex_1_memwrite_out), .MemWrite_out(MemWrite),
    .RegWrite_in(ExRegW), .RegWrite_out(MemRegWrite), .JAL_in(id_ex_1_jal_out), .JAL_out(ex_mem_1_jal_out),
    .LB_in(id_ex_1_lb_out), .LB_out(ex_mem_1_lb_out), .IR_in({Ex_OP, IR}), .IR_out(ex_mem_1_ir_out),
    .PC_in(PC_add4), .PC_out(ex_mem_1_pc_out), .ALUResult_in(mips_alu_1_result),
    .ALUResult_out(NewALUResult), .R2_in(new_R2), .R2_out(MDin), .RegDst_in(id_ex_1_regdst_out),
    .RegDst_out(ex_mem_1_regdst_out), .Syscall_in(Syscall), .Syscall_out(ex_mem_1_syscall_out),
    .equal_in(Equal), .equal_out(ex_mem_1_equal_out), .OldPC_in(EX_PC_t), .OldPC_out(MEM_PC),
    .pause_in(Old_Pause), .pause_out(ex_mem_1_pause_out));
  Multiplexer #(.width(5), .enable("false")) multiplexer_15 (
    .in0(ex_mem_1_ir_out[20:16]), .in1(ex_mem_1_ir_out[15:11]), .out(multiplexer_15_out),
    .sel(ex_mem_1_regdst_out));
  Multiplexer #(.width(5), .enable("false")) multiplexer_16 (
    .in0(multiplexer_15_out), .in1({5{1'b1}}), .out(MemW_num), .sel(ex_mem_1_jal_out));
  RAM #(.addrWidth(10), .dataWidth(32), .bus("separate")) ram_1 (
    .addr(NewALUResult[11:2]), .din(MDin), .data(ram_1_data), .str(MemWrite), .clk(CLK), .clr(RST));  // open: sel, ld
  MEM_WB mem_wb_1 (
    .\气泡_高电平时有效 (1'b0), .clk(CLK), .clear(RST), .enable(Write), .MemToReg_in(MemToReg),
    .MemToReg_out(mem_wb_1_memtoreg_out), .MemWrite_in(MemWrite), .RegWrite_in(MemRegWrite),
    .RegWrite_out(RegWrite), .JAL_in(ex_mem_1_jal_out), .JAL_out(mem_wb_1_jal_out), .LB_in(ex_mem_1_lb_out),
    .LB_out(LB), .IR_in(ex_mem_1_ir_out), .IR_out(mem_wb_1_ir_out), .PC_in(ex_mem_1_pc_out),
    .PC_out(mem_wb_1_pc_out), .ALUResult_in(NewALUResult), .ALUResult_out(OldALUResult),
    .Memorydata_in(ram_1_data), .Memorydata_out(Old_MemData), .RegDst_in(ex_mem_1_regdst_out),
    .RegDst_out(mem_wb_1_regdst_out), .Syscall_in(ex_mem_1_syscall_out), .equal_in(ex_mem_1_equal_out),
    .OldPC_in(MEM_PC), .OldPC_out(WB_PC_t), .pause_in(ex_mem_1_pause_out), .pause_out(Pause));  // open: MemWrite_out, Syscall_out, equal_out
  not not_6 (not_6_out, V0__34);
  and and_7 (Old_Pause, not_6_out, Syscall);
  Multiplexer #(.width(5), .enable("false")) multiplexer_17 (
    .in0(mem_wb_1_ir_out[20:16]), .in1(mem_wb_1_ir_out[15:11]), .out(multiplexer_17_out),
    .sel(mem_wb_1_regdst_out));
  Multiplexer #(.select(2), .width(32), .enable("false")) multiplexer_18 (
    .in0(R1), .in1(NewALUResult), .in2(OldALUResult), .in3(Mem_MemData), .out(new_R1), .sel(Choose_R1));
  Multiplexer #(.select(2), .width(8), .enable("false")) multiplexer_19 (
    .in0(Old_MemData[7:0]), .in1(Old_MemData[15:8]), .in2(Old_MemData[23:16]), .in3(Old_MemData[31:24]),
    .out(multiplexer_19_out), .sel(OldALUResult[1:0]));
  and and_8 (Show, Syscall, V0__34);
  Multiplexer #(.width(5), .enable("false")) multiplexer_20 (
    .in0(multiplexer_17_out), .in1({5{1'b1}}), .out(W_num), .sel(mem_wb_1_jal_out));
  assign bit_extender_3_out = {{24{multiplexer_19_out[7]}}, multiplexer_19_out};  // Bit_Extender bit_extender_3
  Multiplexer #(.width(32), .enable("false")) multiplexer_21 (
    .in0(OldALUResult), .in1(Mem_MemData), .out(multiplexer_21_out), .sel(mem_wb_1_memtoreg_out));
  Comparator #(.width(32)) comparator_2 (.a(new_R1), .b(32'h22), .eq(V0__34));  // open: gt, lt
  Multiplexer #(.width(32), .enable("false")) multiplexer_22 (
    .in0(Old_MemData), .in1(bit_extender_3_out), .out(Mem_MemData), .sel(LB));
  Multiplexer #(.width(32), .enable("false")) multiplexer_23 (
    .in0(multiplexer_21_out), .in1(mem_wb_1_pc_out), .out(RDin), .sel(mem_wb_1_jal_out));

  // Other names for the same wires on the sheet: IR[31:26] = Ex_OP; MemWrite_grade = MemWrite; RDin_mon[31:0] = RDin

  // Notes on the sheet:
  //   中断源
  //   中断等待指示
  //   数码管输出
  //   contents of rom_1 (hex, n*v repeats v):
  //   20110001 8000c05 20110001 20120002 20130003 8000c09 20110001 20120002 20130003 8000c0d 20110001
  //   20120002 20130003 8000c11 20110001 20120002 20130003 c000cb8 20100001 20110001 118fc0 112020
  //   20020022 c 118882 12200001 8000c15 112020 20020022 c 20110001 118880 112020 20020022 c 12200001
  //   8000c1f 20110001 118fc0 112020 20020022 c 1188c3 112020 20020022 c 118903 112020 20020022 c 118903
  //   112020 20020022 c 118903 112020 20020022 c 118903 112020 20020022 c 118903 112020 20020022 c 118903
  //   112020 20020022 c 118903 112020 20020022 c 20100001 109fc0 139fc3 8021 2012000c 24160003 26100001
  //   3210000f 20080008 20090001 139900 2709825 132020 20020022 c 1094022 1500fff9 22100001 2018000f
  //   2188024 108700 20080008 20090001 139902 2709825 132021 20020022 c 1094022 1500fff9 108702 2c9b022
  //   12c00001 8000c50 4020 1084027 84400 3508ffff 82021 20020022 c 2010ffff 20110000 ae300000 22100001
  //   22310004 ae300000 22100001 22310004 ae300000 22100001 22310004 ae300000 22100001 22310004 ae300000
  //   22100001 22310004 ae300000 22100001 22310004 ae300000 22100001 22310004 ae300000 22100001 22310004
  //   ae300000 22100001 22310004 ae300000 22100001 22310004 ae300000 22100001 22310004 ae300000 22100001
  //   22310004 ae300000 22100001 22310004 ae300000 22100001 22310004 ae300000 22100001 22310004 ae300000
  //   22100001 22310004 22100001 8020 2011003c 8e130000 8e340000 274402a 11000002 ae330000 ae140000
  //   2231fffc 1611fff8 102020 20020022 c 22100004 2011003c 1611fff2 20020032 c 20100000 22100001 102020
  //   20020022 c 22100002 102020 20020022 c 22100003 102020 20020022 c 22100004 102020 20020022 c 22100005
  //   102020 20020022 c 22100006 102020 20020022 c 22100007 102020 20020022 c 22100008 102020 20020022
  //   20020022 c 3e00008
  //   OP
  //   Func
  //   OP
  //   Func
  //   流水调试日志用
  //   为方便自动评测，需要输出流水线各段保存的PC值，注意是PC不是PC+4，另外ID段寄存器写入信息，Mem段内存写入信息也要输出
endmodule

module new_4 (
  input  OP0,
  input  OP1,
  input  OP2,
  input  OP3,
  input  OP4,
  input  OP5,
  input  F0,
  input  F1,
  input  F2,
  input  F3,
  input  F4,
  input  F5,
  output LB,
  output BEGZ
);

  wire not_1_out, not_2_out, not_3_out, not_4_out, not_5_out, not_6_out, not_7_out, not_8_out, not_9_out,
       not_10_out;

  not not_1 (not_1_out, OP4);
  not not_2 (not_2_out, OP3);
  not not_3 (not_3_out, OP2);
  not not_4 (not_4_out, OP1);
  not not_5 (not_5_out, OP0);
  not not_6 (not_6_out, OP5);
  not not_7 (not_7_out, OP4);
  not not_8 (not_8_out, OP3);
  not not_9 (not_9_out, OP2);
  not not_10 (not_10_out, OP1);
  and and_1 (LB, OP5, not_1_out, not_2_out, not_3_out, not_4_out, not_5_out);
  and and_2 (BEGZ, not_6_out, not_7_out, not_8_out, not_9_out, not_10_out, OP0);
endmodule

// load_use
module \load_use及重定向相关  (
  input  [5:0] Ex_OP,
  input  [4:0] Ex_WriteReg_num,
  input  [4:0] Mem_WriteReg_num,
  input  Ex_RegWrite_num,
  input  [5:0] OP,
  input  Mem_RegWrite_num,
  input  [5:0] FUNC,
  input  MemToReg,
  input  [4:0] ID_R2_num,
  input  [4:0] ID_R1_num,
  output load_use,
  output [1:0] Choose_R1,
  output [1:0] Choose_R2
);

  wire and_1_out, and_2_out, and_3_out, and_4_out, and_5_out, and_6_out, and_7_out, and_8_out, and_9_out,
       and_12_out, comparator_1_eq, comparator_2_eq, comparator_3_eq, comparator_4_eq, comparator_5_eq,
       comparator_6_eq, comparator_7_eq, comparator_8_eq, comparator_9_eq, comparator_10_eq, load_use1,
       load_use2, not_1_out, not_2_out, not_3_out, not_4_out, or_1_out, or_2_out, R1_USED, R2_USED;
  wire [1:0] and_15_out, and_16_out;

  Comparator #(.width(5)) comparator_1 (.a(Ex_WriteReg_num), .b(ID_R1_num), .eq(comparator_1_eq));  // open: gt, lt
  Comparator #(.width(5)) comparator_2 (.a(Mem_WriteReg_num), .b(ID_R1_num), .eq(comparator_2_eq));  // open: gt, lt
  Comparator #(.width(5)) comparator_3 (.a(ID_R1_num), .b({5{1'b0}}), .eq(comparator_3_eq));  // open: gt, lt
  Comparator #(.width(5)) comparator_4 (.a(Ex_WriteReg_num), .b(ID_R2_num), .eq(comparator_4_eq));  // open: gt, lt
  Comparator #(.width(5)) comparator_5 (.a(Mem_WriteReg_num), .b(ID_R2_num), .eq(comparator_5_eq));  // open: gt, lt
  Comparator #(.width(5)) comparator_6 (.a(ID_R2_num), .b({5{1'b0}}), .eq(comparator_6_eq));  // open: gt, lt
  not not_1 (not_1_out, comparator_6_eq);
  not not_2 (not_2_out, comparator_3_eq);
  and and_1 (and_1_out, comparator_4_eq, not_1_out);
  and and_2 (and_2_out, comparator_5_eq, not_1_out);
  and and_3 (and_3_out, comparator_1_eq, not_2_out);
  and and_4 (and_4_out, comparator_2_eq, not_2_out);
  \源寄存器使用情况  \u_源寄存器使用情况_1  (
    .OP0(OP[0]), .OP1(OP[1]), .OP2(OP[2]), .OP3(OP[3]), .OP4(OP[4]), .OP5(OP[5]), .F0(FUNC[0]), .F1(FUNC[1]),
    .F2(FUNC[2]), .F3(FUNC[3]), .F4(FUNC[4]), .F5(FUNC[5]), .R1_Used(R1_USED), .R2_Used(R2_USED));
  and and_5 (and_5_out, R2_USED, and_1_out);
  and and_6 (and_6_out, and_2_out, R2_USED);
  Comparator #(.width(6)) comparator_7 (.a(Ex_OP), .b(6'b100000), .eq(comparator_7_eq));  // open: gt, lt
  Comparator #(.width(6)) comparator_8 (.a(Ex_OP), .b(6'b100011), .eq(comparator_8_eq));  // open: gt, lt
  and and_7 (and_7_out, R1_USED, and_3_out);
  and and_8 (and_8_out, and_4_out, R1_USED);
  Comparator #(.width(6)) comparator_9 (.a(Ex_OP), .b(6'b100000), .eq(comparator_9_eq));  // open: gt, lt
  Comparator #(.width(6)) comparator_10 (.a(Ex_OP), .b(6'b100011), .eq(comparator_10_eq));  // open: gt, lt
  or or_1 (or_1_out, comparator_7_eq, comparator_8_eq);
  and and_9 (and_9_out, and_7_out, Ex_RegWrite_num);
  and and_10 (and_15_out[1], Mem_RegWrite_num, and_8_out);
  and and_11 (load_use2, or_2_out, and_12_out);
  or or_2 (or_2_out, comparator_9_eq, comparator_10_eq);
  and and_12 (and_12_out, and_5_out, Ex_RegWrite_num);
  and and_13 (and_16_out[1], Mem_RegWrite_num, and_6_out);
  and and_14 (load_use1, or_1_out, and_9_out);
  not not_3 (not_3_out, or_1_out);
  not not_4 (not_4_out, or_2_out);
  and and_15 (and_15_out[0], not_3_out, and_9_out);
  and and_16 (and_16_out[0], not_4_out, and_12_out);
  Multiplexer #(.select(3), .width(2), .enable("false")) multiplexer_1 (
    .in0(2'b00), .in1(2'b01), .in2(2'b10), .in3(2'b01), .in4(2'b00), .in5(2'b01), .in6(2'b11), .in7(2'b01),
    .out(Choose_R2), .sel({MemToReg, and_16_out}));
  Multiplexer #(.select(3), .width(2), .enable("false")) multiplexer_2 (
    .in0(2'b00), .in1(2'b01), .in2(2'b10), .in3(2'b01), .in4(2'b00), .in5(2'b01), .in6(2'b11), .in7(2'b01),
    .out(Choose_R1), .sel({MemToReg, and_15_out}));
  or or_3 (load_use, load_use1, load_use2);
endmodule

// REG FALLING EDGE
module Regfile_FallingEdge (
  input  [4:0] R1_num,
  input  [4:0] R2_num,
  input  [4:0] W_num,
  input  [31:0] Din,
  input  WE,
  input  Clk,
  output [31:0] R1,
  output [31:0] R2
);

  // RegisterFile registerfile_1: pin names not known; wires that end beside it: Din, Clk, WE, W_num, R1_num, R2_num, R1, R2
endmodule

module Regfile_Hacked_Bubble (
  input  [4:0] R1_num,
  input  [4:0] R2_num,
  input  [4:0] W_num,
  input  [31:0] Din,
  input  WE,
  input  Clk,
  output [31:0] R1,
  output [31:0] R2
);

  wire and_1_out, and_2_out, comparator_1_eq, comparator_2_eq;
  wire [31:0] registerfile_1_p7, registerfile_1_p8;

  // RegisterFile registerfile_1: pin names not known; wires that end beside it: Din, Clk, WE, W_num, R1_num, R2_num, registerfile_1_p7, registerfile_1_p8
  Comparator #(.width(5)) comparator_1 (.a(W_num), .b(R1_num), .eq(comparator_1_eq));  // open: gt, lt
  Comparator #(.width(5)) comparator_2 (.a(R2_num), .b(W_num), .eq(comparator_2_eq));  // open: gt, lt
  and and_1 (and_1_out, WE, comparator_1_eq);
  and and_2 (and_2_out, WE, comparator_2_eq);
  Multiplexer #(.width(32), .enable("false")) multiplexer_1 (
    .in0(registerfile_1_p7), .in1(Din), .out(R1), .sel(and_1_out));
  Multiplexer #(.width(32), .enable("false")) multiplexer_2 (
    .in0(registerfile_1_p8), .in1(Din), .out(R2), .sel(and_2_out));
endmodule

module PC_JUDGE (
  input  [31:0] PC_raw32b,
  output [31:0] PC_judge
);

  assign PC_judge = PC_raw32b & 32'hffff;  // AND_Gate and_1, 32 bits wide
endmodule
