// Logisim project 2-comp-sum.circ as structural Verilog: 1 circuit, main circuit main
module main (
  input  A,
  input  B,
  input  C,
  output Carry,
  output Sum
);

  wire and_1_out, and_2_out, xor_1_out;

  xor xor_1 (xor_1_out, A, B);
  and and_1 (and_1_out, A, B);
  xor xor_2 (Sum, C, xor_1_out);
  and and_2 (and_2_out, C, xor_1_out);
  xor xor_3 (Carry, and_1_out, and_2_out);

  // Notes on the sheet:
  //   semi-add-1
  //   semi-add-2
  //   semi-add-3
endmodule
