// Logisim project 3-4b-sum.circ as structural Verilog: 1 circuit, main circuit main
module main (
  input  A0,
  input  A1,
  input  A2,
  input  A3,
  input  B0,
  input  B1,
  input  B2,
  input  B3,
  input  C0,
  output S1,
  output S0,
  output S2,
  output S3,
  output C4
);

  wire main_1_carry, main_2_carry, main_3_carry;

  _2_comp_sum_main main_1 (.A(A0), .B(B0), .C(C0), .Carry(main_1_carry), .Sum(S0));
  _2_comp_sum_main main_2 (.A(A1), .B(B1), .C(main_1_carry), .Carry(main_2_carry), .Sum(S1));
  _2_comp_sum_main main_3 (.A(A2), .B(B2), .C(main_2_carry), .Carry(main_3_carry), .Sum(S2));
  _2_comp_sum_main main_4 (.A(A3), .B(B3), .C(main_3_carry), .Carry(C4), .Sum(S3));
endmodule
