// Logisim project 4-low-latency-4b-sum.circ as structural Verilog: 2 circuits, main circuit main
module main (
  input  A0,
  input  A1,
  input  A2,
  input  A3,
  input  B0,
  input  B1,
  input  B2,
  input  B3,
  input  C0,
  output S0,
  output S1,
  output S2,
  output S3,
  output C4
);

  wire and_1_out, and_2_out, and_3_out, and_4_out, and_5_out, and_6_out, and_7_out, and_8_out, and_9_out,
       and_10_out, and_11_out, and_12_out, and_13_out, and_14_out, or_1_out, or_2_out, or_3_out, xor_3_out,
       xor_6_out, xor_7_out, xor_8_out;

  and and_1 (and_1_out, xor_3_out, C0);
  and and_2 (and_2_out, xor_6_out, and_10_out);
  or or_1 (or_1_out, and_1_out, and_10_out);
  and and_3 (and_3_out, xor_6_out, xor_3_out, C0);
  or or_2 (or_2_out, and_13_out, and_2_out, and_3_out);
  and and_4 (and_4_out, xor_7_out, and_13_out);
  and and_5 (and_5_out, xor_3_out, xor_6_out, xor_7_out, C0);
  and and_6 (and_6_out, xor_6_out, xor_7_out, and_10_out);
  or or_3 (or_3_out, and_12_out, and_4_out, and_6_out, and_5_out);
  and and_7 (and_7_out, xor_8_out, and_12_out);
  and and_8 (and_8_out, xor_8_out, xor_7_out, and_13_out);
  or or_4 (C4, and_14_out, and_7_out, and_8_out, and_9_out, and_11_out);
  and and_9 (and_9_out, xor_8_out, xor_7_out, xor_6_out, and_10_out);
  and and_10 (and_10_out, B0, A0);
  and and_11 (and_11_out, xor_3_out, xor_6_out, xor_7_out, xor_8_out, C0);
  and and_12 (and_12_out, B2, A2);
  and and_13 (and_13_out, B1, A1);
  xor xor_1 (S0, xor_3_out, C0);
  xor xor_2 (S1, xor_6_out, or_1_out);
  and and_14 (and_14_out, B3, A3);
  xor xor_3 (xor_3_out, B0, A0);
  xor xor_4 (S3, xor_8_out, or_3_out);
  xor xor_5 (S2, xor_7_out, or_2_out);
  xor xor_6 (xor_6_out, B1, A1);
  xor xor_7 (xor_7_out, B2, A2);
  xor xor_8 (xor_8_out, B3, A3);
endmodule

module \module  (
  input  A0,
  input  A1,
  input  A2,
  input  A3,
  input  B0,
  input  B1,
  input  B2,
  input  B3,
  input  C0,
  output S0,
  output S1,
  output S2,
  output S3,
  output C4
);

  wire and_1_out, and_2_out, and_3_out, and_4_out, and_5_out, and_6_out, and_7_out, and_8_out, and_9_out,
       and_10_out, and_11_out, and_12_out, and_13_out, and_14_out, or_1_out, or_2_out, or_3_out, xor_4_out,
       xor_5_out, xor_7_out, xor_8_out;

  and and_1 (and_1_out, xor_4_out, C0);
  or or_1 (or_1_out, and_1_out, and_11_out);
  and and_2 (and_2_out, xor_5_out, and_11_out);
  or or_2 (or_2_out, and_12_out, and_2_out, and_3_out);
  and and_3 (and_3_out, xor_5_out, xor_4_out, C0);
  and and_4 (and_4_out, xor_5_out, xor_8_out, and_11_out);
  and and_5 (and_5_out, xor_8_out, and_12_out);
  or or_3 (or_3_out, and_14_out, and_5_out, and_4_out, and_6_out);
  and and_6 (and_6_out, xor_4_out, xor_5_out, xor_8_out, C0);
  and and_7 (and_7_out, xor_7_out, and_14_out);
  and and_8 (and_8_out, xor_7_out, xor_8_out, xor_5_out, and_11_out);
  and and_9 (and_9_out, xor_7_out, xor_8_out, and_12_out);
  or or_4 (C4, and_13_out, and_7_out, and_9_out, and_8_out, and_10_out);
  and and_10 (and_10_out, xor_4_out, xor_5_out, xor_8_out, xor_7_out, C0);
  and and_11 (and_11_out, B0, A0);
  and and_12 (and_12_out, B1, A1);
  xor xor_1 (S0, xor_4_out, C0);
  and and_13 (and_13_out, B3, A3);
  and and_14 (and_14_out, B2, A2);
  xor xor_2 (S1, xor_5_out, or_1_out);
  xor xor_3 (S2, xor_8_out, or_2_out);
  xor xor_4 (xor_4_out, B0, A0);
  xor xor_5 (xor_5_out, B1, A1);
  xor xor_6 (S3, xor_7_out, or_3_out);
  xor xor_7 (xor_7_out, B3, A3);
  xor xor_8 (xor_8_out, B2, A2);
endmodule
