// Logisim project 1-counter.circ as structural Verilog: 2 circuits, main circuit 74193
module _74193 (
  input  cpu,
  input  cpd,
  input  reset,
  output Q0,
  output Q1,
  output Q2,
  output Q3
);

  wire and_1_out, and_2_out, and_3_out, and_4_out, and_5_out, and_6_out, buffer_1_out, buffer_2_out,
       buffer_7_out, buffer_8_out, nand_1_out, nand_2_out, nand_3_out, nand_4_out, nand_5_out, nand_6_out,
       nand_7_out, nand_8_out, nand_9_out, nand_10_out, nor_1_out, nor_2_out, nor_3_out, nor_4_out,
       not_1_out, not_2_out, not_3_out, not_4_out, not_5_out, or_1_out, or_2_out, or_3_out, or_4_out,
       t_ff_1_q, t_ff_1_qn, t_ff_2_q, t_ff_2_qn, t_ff_3_q, t_ff_3_qn, t_ff_4_q, t_ff_4_qn;

  buf buffer_1 (buffer_1_out, cpu);
  buf buffer_2 (buffer_2_out, cpd);
  not not_1 (not_1_out, reset);
  nand nand_1 (nand_1_out, 1'b0, 1'b1);
  not not_2 (not_2_out, nand_1_out);
  nor nor_1 (nor_1_out, buffer_1_out, buffer_2_out);
  or or_1 (or_1_out, ~not_1_out, ~nand_2_out);  // OR_Gate
  nand nand_2 (nand_2_out, nand_1_out, 1'b0);
  T_Flip_Flop t_ff_1 (
    .clk(nor_1_out), .T(nor_1_out), .Q(t_ff_1_q), .Qn(t_ff_1_qn), .preset(not_2_out), .reset(or_1_out));  // open: en
  buf buffer_3 (Q0, t_ff_1_q);
  and and_1 (and_1_out, cpu, t_ff_1_q);
  nor nor_2 (nor_2_out, and_1_out, and_2_out);
  and and_2 (and_2_out, t_ff_1_qn, cpd);
  nand nand_3 (nand_3_out, 1'b0, 1'b0);
  nand nand_4 (nand_4_out, nand_3_out, 1'b0);
  not not_3 (not_3_out, nand_3_out);
  T_Flip_Flop t_ff_2 (
    .clk(nor_2_out), .T(nor_2_out), .Q(t_ff_2_q), .Qn(t_ff_2_qn), .preset(not_3_out), .reset(or_2_out));  // open: en
  or or_2 (or_2_out, ~not_1_out, ~nand_4_out);  // OR_Gate
  buf buffer_4 (Q1, t_ff_2_q);
  and and_3 (and_3_out, cpu, t_ff_1_q, t_ff_2_q);
  and and_4 (and_4_out, t_ff_2_qn, t_ff_1_qn, cpd);
  nor nor_3 (nor_3_out, and_3_out, and_4_out);
  nand nand_5 (nand_5_out, nand_6_out, 1'b0);
  nand nand_6 (nand_6_out, 1'b0, 1'b0);
  not not_4 (not_4_out, nand_6_out);
  T_Flip_Flop t_ff_3 (
    .clk(nor_3_out), .T(nor_3_out), .Q(t_ff_3_q), .Qn(t_ff_3_qn), .preset(not_4_out), .reset(or_3_out));  // open: en
  or or_3 (or_3_out, ~not_1_out, ~nand_5_out);  // OR_Gate
  buf buffer_5 (Q2, t_ff_3_q);
  and and_5 (and_5_out, t_ff_2_q, cpu, t_ff_1_q, t_ff_3_q);
  nor nor_4 (nor_4_out, and_5_out, and_6_out);
  and and_6 (and_6_out, t_ff_3_qn, t_ff_2_qn, t_ff_1_qn, cpd);
  nand nand_7 (nand_7_out, 1'b0, 1'b0);
  nand nand_8 (nand_8_out, nand_7_out, 1'b0);
  not not_5 (not_5_out, nand_7_out);
  T_Flip_Flop t_ff_4 (
    .clk(nor_4_out), .T(nor_4_out), .Q(t_ff_4_q), .Qn(t_ff_4_qn), .preset(not_5_out), .reset(or_4_out));  // open: en
  or or_4 (or_4_out, ~not_1_out, ~nand_8_out);  // OR_Gate
  buf buffer_6 (Q3, t_ff_4_q);
  nand nand_9 (nand_9_out, t_ff_3_q, cpu, t_ff_4_q, t_ff_2_q, t_ff_1_q);
  nand nand_10 (nand_10_out, t_ff_1_qn, t_ff_4_qn, t_ff_3_qn, t_ff_2_qn, cpd);
  buf buffer_7 (buffer_7_out, nand_9_out);
  buf buffer_8 (buffer_8_out, nand_10_out);
endmodule

module test (
  input  in_1,
  input  in_2,
  input  in_3
);

  _74193 u_74193_1 (.cpu(in_1), .cpd(in_2), .reset(in_3));  // open: Q0, Q1, Q2, Q3
endmodule
