// Logisim project 2-bin2bcd.circ as structural Verilog: 2 circuits, main circuit main
module main (
  input  in_1,
  input  in_2,
  input  in_3,
  input  in_4,
  output out_5,
  output out_6,
  output out_7,
  output out_8,
  output out_9,
  output out_10,
  output out_11,
  output out_12
);

  wire module_1_s0, module_1_s1, module_1_s2, module_1_s3;

  \module  module_1 (
    .A0(in_4), .A1(in_3), .A2(in_2), .A3(in_1), .B0(1'b0), .B1(1'b1), .B2(1'b1), .B3(1'b0), .C0(1'b0),
    .S0(module_1_s0), .S1(module_1_s1), .S2(module_1_s2), .S3(module_1_s3), .C4(out_8));
  selector selector_1 (.in_1(module_1_s3), .in_2(out_8), .in_3(in_1), .out_4(out_9));
  selector selector_2 (.in_1(module_1_s2), .in_2(out_8), .in_3(in_2), .out_4(out_10));
  selector selector_3 (.in_1(module_1_s1), .in_2(out_8), .in_3(in_3), .out_4(out_11));
  selector selector_4 (.in_1(module_1_s0), .in_2(out_8), .in_3(in_4), .out_4(out_12));

  assign out_5 = 1'b0;
  assign out_6 = 1'b0;
  assign out_7 = 1'b0;
endmodule

module selector (
  input  in_1,
  input  in_2,
  input  in_3,
  output out_4
);

  wire and_1_out, and_2_out, not_1_out;

  not not_1 (not_1_out, in_2);
  and and_1 (and_1_out, in_1, in_2);
  and and_2 (and_2_out, not_1_out, in_3);
  or or_1 (out_4, and_1_out, and_2_out);
endmodule
