// Logisim project 3-bcd2gui.circ as structural Verilog: 2 circuits, main circuit main
module main (
  input  in_1,
  input  in_2,
  input  in_3,
  input  in_4,
  output out_5,
  output out_6,
  output out_7,
  output out_8,
  output out_9,
  output out_10,
  output out_11
);

  wire and_1_out, and_2_out, and_3_out, and_5_out, and_6_out, and_7_out, nor_1_out, nor_2_out, nor_4_out,
       nor_5_out, not_1_out, not_2_out, not_3_out, not_4_out, not_5_out, not_6_out, or_5_out, or_6_out,
       xnor_1_out, xnor_2_out, xor_1_out;

  xnor xnor_1 (xnor_1_out, in_4, in_2);
  or or_1 (out_5, in_3, in_1, xnor_1_out);
  xnor xnor_2 (xnor_2_out, in_4, in_3);
  not not_1 (not_1_out, in_2);
  or or_2 (out_6, xnor_2_out, not_1_out, in_1);
  not not_2 (not_2_out, in_3);
  or or_3 (out_7, in_4, not_2_out, in_2);
  xor xor_1 (xor_1_out, in_4, in_2);
  not not_3 (not_3_out, in_3);
  and and_1 (and_1_out, in_4, in_3, in_2);
  and and_2 (and_2_out, xor_1_out, not_3_out);
  nor nor_1 (nor_1_out, and_2_out, and_1_out);
  or or_4 (out_8, nor_1_out, in_1);
  not not_4 (not_4_out, in_4);
  not not_5 (not_5_out, in_1);
  and and_3 (and_3_out, in_3, in_2, not_5_out);
  or or_5 (or_5_out, and_3_out, not_6_out);
  and and_4 (out_9, not_4_out, or_5_out);
  and and_5 (and_5_out, in_3, in_1);
  or or_6 (or_6_out, and_5_out, in_2);
  nor nor_2 (nor_2_out, in_2, in_1, nor_4_out);
  not not_6 (not_6_out, or_6_out);
  nor nor_3 (out_10, nor_2_out, and_6_out);
  nor nor_4 (nor_4_out, in_4, in_3);
  and and_6 (and_6_out, in_4, in_3, in_2);
  and and_7 (and_7_out, in_4, in_3, in_2);
  nor nor_5 (nor_5_out, in_3, in_2, in_1);
  nor nor_6 (out_11, nor_5_out, and_7_out);
endmodule

module test (
  input  in_1,
  input  in_2,
  input  in_3,
  input  in_4
);

  wire and_1_out, and_2_out, and_3_out, and_4_out, and_5_out, and_6_out, and_7_out, nor_1_out, nor_2_out,
       nor_3_out, nor_4_out, nor_5_out, nor_6_out, not_1_out, not_2_out, not_3_out, not_4_out, not_5_out,
       not_6_out, or_1_out, or_2_out, or_3_out, or_4_out, or_5_out, or_6_out, xnor_1_out, xnor_2_out,
       xor_1_out;

  xnor xnor_1 (xnor_1_out, in_4, in_2);
  or or_1 (or_1_out, in_3, in_1, xnor_1_out);
  xnor xnor_2 (xnor_2_out, in_4, in_3);
  not not_1 (not_1_out, in_2);
  or or_2 (or_2_out, xnor_2_out, not_1_out, in_1);
  not not_2 (not_2_out, in_3);
  or or_3 (or_3_out, in_4, not_2_out, in_2);
  xor xor_1 (xor_1_out, in_4, in_2);
  not not_3 (not_3_out, in_3);
  and and_1 (and_1_out, xor_1_out, not_3_out);
  and and_2 (and_2_out, in_4, in_3, in_2);
  nor nor_1 (nor_1_out, and_1_out, and_2_out);
  or or_4 (or_4_out, nor_1_out, in_1);
  not not_4 (not_4_out, in_4);
  not not_5 (not_5_out, in_1);
  and and_3 (and_3_out, in_3, in_2, not_5_out);
  or or_5 (or_5_out, and_3_out, not_6_out);
  and and_4 (and_4_out, not_4_out, or_5_out);
  and and_5 (and_5_out, in_3, in_1);
  or or_6 (or_6_out, and_5_out, in_2);
  nor nor_2 (nor_2_out, in_2, in_1, nor_4_out);
  not not_6 (not_6_out, or_6_out);
  nor nor_3 (nor_3_out, nor_2_out, and_6_out);
  nor nor_4 (nor_4_out, in_4, in_3);
  and and_6 (and_6_out, in_4, in_3, in_2);
  and and_7 (and_7_out, in_4, in_3, in_2);
  nor nor_5 (nor_5_out, in_3, in_2, in_1);
  nor nor_6 (nor_6_out, nor_5_out, and_7_out);
endmodule
