// Logisim project 4-main.circ as structural Verilog: 2 circuits, main circuit main
module main (
  input  in_1,
  input  in_2,
  input  in_3,
  output out_4,
  output out_5,
  output out_6,
  output out_7,
  output out_8,
  output out_9,
  output out_10,
  output out_11,
  output out_12,
  output out_13,
  output out_14,
  output out_15,
  output out_16,
  output out_17,
  output out_18
);

  wire main_1_out_5, main_1_out_6, main_1_out_7, main_1_out_8, main_1_out_9, main_1_out_10, main_1_out_11,
       main_1_out_12, n74193_1_q0, n74193_1_q1, n74193_1_q2, n74193_1_q3, nor_1_out, selector_1_out_4,
       selector_2_out_4;

  selector selector_1 (.in_1(1'b0), .in_2(out_4), .in_3(in_1), .out_4(selector_1_out_4));
  selector selector_2 (.in_1(1'b0), .in_2(nor_1_out), .in_3(in_2), .out_4(selector_2_out_4));
  _74193 u_74193_1 (
    .cpu(selector_1_out_4), .cpd(selector_2_out_4), .reset(in_3), .Q0(n74193_1_q0), .Q1(n74193_1_q1),
    .Q2(n74193_1_q2), .Q3(n74193_1_q3));
  and and_1 (out_4, n74193_1_q0, n74193_1_q1, n74193_1_q2, n74193_1_q3);
  nor nor_1 (nor_1_out, n74193_1_q0, n74193_1_q1, n74193_1_q2, n74193_1_q3);
  _2_bin2bcd_main main_1 (
    .in_1(n74193_1_q3), .in_2(n74193_1_q2), .in_3(n74193_1_q1), .in_4(n74193_1_q0), .out_5(main_1_out_5),
    .out_6(main_1_out_6), .out_7(main_1_out_7), .out_8(main_1_out_8), .out_9(main_1_out_9),
    .out_10(main_1_out_10), .out_11(main_1_out_11), .out_12(main_1_out_12));
  _3_bcd2gui_main main_2 (
    .in_1(main_1_out_5), .in_2(main_1_out_6), .in_3(main_1_out_7), .in_4(main_1_out_8), .out_5(out_8),
    .out_6(out_5), .out_7(out_9), .out_8(out_6), .out_9(out_10), .out_10(out_7), .out_11(out_11));
  _3_bcd2gui_main main_3 (
    .in_1(main_1_out_9), .in_2(main_1_out_10), .in_3(main_1_out_11), .in_4(main_1_out_12), .out_5(out_15),
    .out_6(out_12), .out_7(out_16), .out_8(out_13), .out_9(out_17), .out_10(out_14), .out_11(out_18));
endmodule

module test (
  input  in_1,
  input  in_2,
  input  in_3
);

  wire main_1_out_4, main_1_out_5, main_1_out_6, main_1_out_7, main_1_out_8, main_1_out_9, main_1_out_10,
       main_1_out_11, main_1_out_12, main_1_out_13, main_1_out_14, main_1_out_15, main_1_out_16,
       main_1_out_17, main_1_out_18;

  main main_1 (
    .in_1(in_1), .in_2(in_3), .in_3(in_2), .out_4(main_1_out_4), .out_8(main_1_out_8), .out_5(main_1_out_5),
    .out_9(main_1_out_9), .out_6(main_1_out_6), .out_10(main_1_out_10), .out_7(main_1_out_7),
    .out_11(main_1_out_11), .out_15(main_1_out_15), .out_12(main_1_out_12), .out_16(main_1_out_16),
    .out_13(main_1_out_13), .out_17(main_1_out_17), .out_14(main_1_out_14), .out_18(main_1_out_18));
  _7_Segment_Display u_7_segment_display_1 (
    .g(main_1_out_11), .f(main_1_out_7), .a(main_1_out_8), .b(main_1_out_5), .e(main_1_out_10),
    .d(main_1_out_6), .c(main_1_out_9));  // open: dp
  _7_Segment_Display u_7_segment_display_2 (
    .g(main_1_out_18), .f(main_1_out_14), .a(main_1_out_15), .b(main_1_out_12), .e(main_1_out_17),
    .d(main_1_out_13), .c(main_1_out_16));  // open: dp
  LED led_1 (.in(main_1_out_4));
endmodule
