// Logisim project clk.circ as structural Verilog: 4 circuits, main circuit main
module main (
);

  wire ChangeClockFreq_out, Clear_out, clk_gen_1_out_1, clk_gen_1_out_2, clk_gen_1_out_3, clk_gen_1_out_4,
       multiplexer_1_out, Start_out, Stop_out;
  wire [1:0] counter_1_q;
  wire [3:0] clk2seq_1_t1_prime, ctl_1_t1;

  Button ChangeClockFreq (.out(ChangeClockFreq_out));
  clk_gen clk_gen_1 (
    .out_1(clk_gen_1_out_1), .out_2(clk_gen_1_out_2), .out_3(clk_gen_1_out_3), .out_4(clk_gen_1_out_4));
  Counter #(.width(2), .max('h3)) counter_1 (
    .Q(counter_1_q), .clk(ChangeClockFreq_out));  // open: load, D, count, carry, clr
  Multiplexer #(.select(2)) multiplexer_1 (
    .in0(clk_gen_1_out_1), .in1(clk_gen_1_out_2), .in2(clk_gen_1_out_3), .in3(clk_gen_1_out_4),
    .out(multiplexer_1_out), .sel(counter_1_q));  // open: en
  clk2seq clk2seq_1 (
    .CP(multiplexer_1_out), .T1_prime(clk2seq_1_t1_prime[0]), .T2_prime(clk2seq_1_t1_prime[1]),
    .T3_prime(clk2seq_1_t1_prime[2]), .T4_prime(clk2seq_1_t1_prime[3]), .CLR(Clear_out));
  Button Start (.out(Start_out));
  Button Stop (.out(Stop_out));
  Button Clear (.out(Clear_out));
  ctl ctl_1 (
    .T1_prime(clk2seq_1_t1_prime[0]), .in_2(clk2seq_1_t1_prime[1]), .in_3(clk2seq_1_t1_prime[2]),
    .in_4(clk2seq_1_t1_prime[3]), .T1(ctl_1_t1[0]), .out_10(ctl_1_t1[1]), .out_11(ctl_1_t1[2]),
    .out_12(ctl_1_t1[3]), .START(Start_out), .STOP(Stop_out), .CLK(multiplexer_1_out), .CLR(Clear_out));
  DotMatrix #(.matrixcols(1), .matrixrows(4)) dotmatrix_1 (.col0(ctl_1_t1));
endmodule

module clk_gen (
  output out_1,
  output out_2,
  output out_3,
  output out_4
);

  wire clock_1_out;

  Clock clock_1 (.out(clock_1_out));
  // IC_74161 ic_74161_1: pin names not known; wires that end beside it: clock_1_out, 1'b1, 1'b1, 1'b1, out_1, out_2, out_3, out_4
endmodule

module clk2seq (
  input  CP,
  input  CLR,
  output T1_prime,
  output T2_prime,
  output T3_prime,
  output T4_prime
);

  wire d_flip_flop_1_p4, d_flip_flop_1_p5, ic_74175_1_p1, ic_74175_1_p2, ic_74175_1_p5, ic_74175_1_p9,
       ic_74175_1_p10, nand_1_out, not_1_out;

  not not_1 (not_1_out, CP);
  nand nand_1 (nand_1_out, not_1_out, d_flip_flop_1_p5);
  // IC_74175 ic_74175_1: pin names not known; wires that end beside it: ic_74175_1_p1, ic_74175_1_p2, 1'b1, nand_1_out, ic_74175_1_p5, T3_prime, ic_74175_1_p1, ic_74175_1_p2, ic_74175_1_p9, ic_74175_1_p10, T4_prime
  nand nand_2 (ic_74175_1_p5, d_flip_flop_1_p4, CP);
  // D_Flip_Flop d_flip_flop_1: pin names not known; wires that end beside it: T3_prime, not_1_out, CLR, d_flip_flop_1_p4, d_flip_flop_1_p5
  and and_1 (T1_prime, ic_74175_1_p10, ic_74175_1_p2);
  and and_2 (T2_prime, ic_74175_1_p9, ic_74175_1_p1);
endmodule

module ctl (
  input  T1_prime,
  input  in_2,
  input  in_3,
  input  in_4,
  input  START,
  input  STOP,
  input  CLK,
  input  CLR,
  output T1,
  output out_10,
  output out_11,
  output out_12
);

  wire d_flip_flop_1_p4, nand_1_out, nand_2_out, not_1_out, not_2_out, not_3_out;

  nand nand_1 (nand_1_out, not_1_out, nand_2_out);
  not not_1 (not_1_out, START);
  nand nand_2 (nand_2_out, nand_1_out, not_3_out, not_2_out);
  not not_2 (not_2_out, STOP);
  and and_1 (T1, T1_prime, d_flip_flop_1_p4);
  and and_2 (out_10, in_2, d_flip_flop_1_p4);
  and and_3 (out_11, in_3, d_flip_flop_1_p4);
  and and_4 (out_12, in_4, d_flip_flop_1_p4);
  // D_Flip_Flop d_flip_flop_1: pin names not known; wires that end beside it: nand_1_out, CLK, CLR, d_flip_flop_1_p4
  not not_3 (not_3_out, CLR);
endmodule
